// Logisim project 2-exp2021-MEM.circ as structural Verilog: 3 circuits, main circuit 2-1  存储器扩展
module \_2_1__存储器扩展  (
  input  CLK,
  input  WE,
  input  [13:0] Addr,
  input  [31:0] Din,
  output [31:0] Dout
);

  RAM #(.addrWidth(12), .bus("separate"), .Select("low")) ram_1 ();  // open: addr, din, data, str, sel, clk, ld, clr
  Hex_Digit_Display hex_digit_display_1 (.value(Dout[15:12]));  // open: dp
  Hex_Digit_Display hex_digit_display_2 (.value(Dout[31:28]));  // open: dp
  Hex_Digit_Display hex_digit_display_3 (.value(Dout[7:4]));  // open: dp
  Hex_Digit_Display hex_digit_display_4 (.value(Dout[11:8]));  // open: dp
  Hex_Digit_Display hex_digit_display_5 (.value(Dout[27:24]));  // open: dp
  Hex_Digit_Display hex_digit_display_6 (.value(Dout[23:20]));  // open: dp
  Hex_Digit_Display hex_digit_display_7 (.value(Dout[3:0]));  // open: dp
  Hex_Digit_Display hex_digit_display_8 (.value(Dout[19:16]));  // open: dp

  // Notes on the sheet:
  //   注：不能增加任何输入输出端口信号
  //   输入引脚区
  //   RAM 4K×8
  //   输出引脚区
  //   请用4K×8的存储芯片实现16K×32的存储器，并搭建外围电路，自动实现对存储器的读写操作
  //   输出数据测试区
endmodule

module \_2_2__MIPS_RF模块  (
  input  CLK,
  input  WE,
  input  [4:0] RA1,
  input  [4:0] RA2,
  input  [31:0] Din,
  input  [4:0] WA,
  output [31:0] RD2,
  output [31:0] RD1
);

  wire button_1_out;
  wire [31:0] multiplexer_1_out;

  Register #(.width(32), .Select("low")) register_1 ();  // open: D, en, Q, clk, clr
  Multiplexer #(.width(32), .enable("false")) multiplexer_1 (
    .in0(RD1), .in1(RD2), .out(multiplexer_1_out), .sel(button_1_out));
  Button button_1 (.out(button_1_out));
  Hex_Digit_Display hex_digit_display_1 (.value(multiplexer_1_out[15:12]));  // open: dp
  Hex_Digit_Display hex_digit_display_2 (.value(multiplexer_1_out[31:28]));  // open: dp
  Hex_Digit_Display hex_digit_display_3 (.value(multiplexer_1_out[7:4]));  // open: dp
  Hex_Digit_Display hex_digit_display_4 (.value(multiplexer_1_out[11:8]));  // open: dp
  Hex_Digit_Display hex_digit_display_5 (.value(multiplexer_1_out[23:20]));  // open: dp
  Hex_Digit_Display hex_digit_display_6 (.value(multiplexer_1_out[27:24]));  // open: dp
  Hex_Digit_Display hex_digit_display_7 (.value(multiplexer_1_out[3:0]));  // open: dp
  Hex_Digit_Display hex_digit_display_8 (.value(multiplexer_1_out[19:16]));  // open: dp

  // Notes on the sheet:
  //   输入引脚区
  //   注：不能增加任何输入输出端口信号
  //   输出引脚区
  //   实现MIPS寄存器组，32个寄存器可以采用模块化方法实现，模块规模不限，注意0号寄存器恒为0
  //   输出数据测试区
endmodule

module \_2_3__数据互传  (
  input  CLK,
  input  WE,
  input  [2:0] AluOp,
  input  [1:0] RWsel,
  input  LA1,
  input  LA2,
  input  [31:0] Din,
  input  LWA,
  input  [1:0] Dispsel,
  output [31:0] Disp
);

  Hex_Digit_Display hex_digit_display_1 (.value(Disp[11:8]));  // open: dp
  Hex_Digit_Display hex_digit_display_2 (.value(Disp[15:12]));  // open: dp
  Hex_Digit_Display hex_digit_display_3 (.value(Disp[31:28]));  // open: dp
  Hex_Digit_Display hex_digit_display_4 (.value(Disp[27:24]));  // open: dp
  Hex_Digit_Display hex_digit_display_5 (.value(Disp[7:4]));  // open: dp
  Hex_Digit_Display hex_digit_display_6 (.value(Disp[3:0]));  // open: dp
  Hex_Digit_Display hex_digit_display_7 (.value(Disp[23:20]));  // open: dp
  Hex_Digit_Display hex_digit_display_8 (.value(Disp[19:16]));  // open: dp

  // Notes on the sheet:
  //   输入引脚区
  //   注：请完善数据通路可以增加必要的输入控制端口信号
  //   输出引脚区
  //   注：数据通路图中RF使用2-2MIPS RF模块，MEMU是2-1存储器扩展模块
  //   输出数据测试区
endmodule
