// Logisim project 八位加法器，32位加减可控运算器，32位ALU，补码一位乘法器(1).circ as structural Verilog: 5 circuits, main circuit 1-1  8位加法器
module \_1_2_32位可控加减器  (
  input  Sub,
  input  [31:0] X,
  input  [31:0] Y,
  output CF,
  output OF,
  output ZF,
  output SF,
  output [31:0] S
);

  wire \n1_1_8位加法器_2_cout , \n1_1_8位加法器_3_cout , \n1_1_8位加法器_4_cout ;
  wire [2:0] multiplexer_1_out, multiplexer_1_out_2, multiplexer_1_out_3;
  wire [7:0] bit_extender_1_out, xor_1_out, xor_2_out, xor_3_out, xor_4_out;

  \_1_1__8位加法器  \u_1_1_8位加法器_1  (
    .X(X[31:24]), .Y(xor_1_out), .Cin(\n1_1_8位加法器_2_cout ), .S(S[31:24]), .Cout(CF), .OF(OF));
  assign xor_1_out = Y[31:24] ^ bit_extender_1_out;  // XOR_Gate xor_1, 8 bits wide
  \_1_1__8位加法器  \u_1_1_8位加法器_2  (
    .X(X[23:16]), .Y(xor_2_out), .Cin(\n1_1_8位加法器_3_cout ), .S(S[23:16]), .Cout(\n1_1_8位加法器_2_cout ));  // open: OF
  assign xor_2_out = Y[23:16] ^ bit_extender_1_out;  // XOR_Gate xor_2, 8 bits wide
  // Probe on X
  // Probe on Y
  // Probe on S
  Comparator #(.width(32)) comparator_1 (.a(S), .b({32{1'b0}}), .eq(ZF));  // open: gt, lt
  \_1_1__8位加法器  \u_1_1_8位加法器_3  (
    .X(X[15:8]), .Y(xor_3_out), .Cin(\n1_1_8位加法器_4_cout ), .S(S[15:8]), .Cout(\n1_1_8位加法器_3_cout ));  // open: OF
  assign xor_3_out = Y[15:8] ^ bit_extender_1_out;  // XOR_Gate xor_3, 8 bits wide
  \_1_1__8位加法器  \u_1_1_8位加法器_4  (
    .X(X[7:0]), .Y(xor_4_out), .Cin(Sub), .S(S[7:0]), .Cout(\n1_1_8位加法器_4_cout ));  // open: OF
  // Probe on X
  // Probe on Y
  // Probe on S
  assign xor_4_out = Y[7:0] ^ bit_extender_1_out;  // XOR_Gate xor_4, 8 bits wide
  assign bit_extender_1_out = {{7{Sub}}, Sub};  // Bit_Extender bit_extender_1
  DotMatrix #(.matrixcols(3), .matrixrows(3)) dotmatrix_1 (
    .col0(multiplexer_1_out_3), .col1(multiplexer_1_out_2), .col2(multiplexer_1_out));
  Multiplexer #(.width(9), .enable("false")) multiplexer_1 (
    .in0(9'hba), .in1(9'h92), .out({multiplexer_1_out_3, multiplexer_1_out_2, multiplexer_1_out}), .sel(Sub));

  assign SF = S[31];

  // Notes on the sheet:
  //   输入引脚区
  //   注：不能增加任何输入输出端口信号
  //   用封装后的8位加法器构成32位加减可控运算器，并产生正确的标志位
  //   输出引脚区
  //   =
  //   有符号数
  //   =
  //   结果测试区
  //   无符号数
endmodule

module \_1_1__8位加法器  (
  input  [7:0] X,
  input  [7:0] Y,
  input  Cin,
  output [7:0] S,
  output Cout,
  output OF
);

  wire \n1位全加器_2_cout , \n1位全加器_3_cout , \n1位全加器_4_cout , \n1位全加器_5_cout , \n1位全加器_6_cout , \n1位全加器_7_cout ,
       \n1位全加器_8_cout , Of_t;

  \_1位全加器  \u_1位全加器_1  (.Cout(Cout), .Si(S[7]), .Cin(\n1位全加器_2_cout ), .Xi(Y[7]), .Yi(X[7]));
  \_1位全加器  \u_1位全加器_2  (.Cout(\n1位全加器_2_cout ), .Si(S[6]), .Cin(\n1位全加器_3_cout ), .Xi(Y[6]), .Yi(X[6]));
  xor xor_1 (Of_t, \n1位全加器_2_cout , Cout);
  \_1位全加器  \u_1位全加器_3  (.Cout(\n1位全加器_3_cout ), .Si(S[5]), .Cin(\n1位全加器_4_cout ), .Xi(Y[5]), .Yi(X[5]));
  \_1位全加器  \u_1位全加器_4  (.Cout(\n1位全加器_4_cout ), .Si(S[4]), .Cin(\n1位全加器_5_cout ), .Xi(Y[4]), .Yi(X[4]));
  \_1位全加器  \u_1位全加器_5  (.Cout(\n1位全加器_5_cout ), .Si(S[3]), .Cin(\n1位全加器_6_cout ), .Xi(Y[3]), .Yi(X[3]));
  \_1位全加器  \u_1位全加器_6  (.Cout(\n1位全加器_6_cout ), .Si(S[2]), .Cin(\n1位全加器_7_cout ), .Xi(Y[2]), .Yi(X[2]));
  // Probe on X
  // Probe on Y
  // Probe on S
  \_1位全加器  \u_1位全加器_7  (.Cout(\n1位全加器_7_cout ), .Si(S[1]), .Cin(\n1位全加器_8_cout ), .Xi(Y[1]), .Yi(X[1]));
  \_1位全加器  \u_1位全加器_8  (.Cout(\n1位全加器_8_cout ), .Si(S[0]), .Cin(Cin), .Xi(Y[0]), .Yi(X[0]));
  // Probe on X
  // Probe on Y
  // Probe on S

  // Notes on the sheet:
  //   输入引脚区
  //   注：不能增加任何输入输出端口信号
  //   （1）使用1位全加器FA实现8位加法器，给出溢出标志OF
  //   输出引脚区
  //   =
  //   有符号数
  //   （2）封装电路供后续实验使用
  //   =
  //   结果测试区
  //   无符号数
endmodule

module \_1_3_32位ALU  (
  input  [2:0] AluOp,
  input  [31:0] X,
  input  [31:0] Y,
  output OF,
  output UOF,
  output ZF,
  output [31:0] S
);

  wire comparator_1_lt, \n1_2_32位可控加减器_3_of , \n1_2_32位可控加减器_3_sf , \n1_2_32位可控加减器_4_of ,
       \n1_2_32位可控加减器_4_sf , \n1_2_32位可控加减器_5_of , \n1_2_32位可控加减器_6_of , xor_1_out, xor_2_out;
  wire [31:0] and_1_out, bit_extender_1_out, buffer_1_out, multiplier_1_out, \n1_2_32位可控加减器_1_s ,
       \n1_2_32位可控加减器_2_s , not_1_out, or_1_out;

  assign buffer_1_out = Y;  // Buffer buffer_1, 32 bits wide
  assign not_1_out = ~Y;  // NOT_Gate not_1, 32 bits wide
  \_1_2_32位可控加减器  \u_1_2_32位可控加减器_1  (.X(X), .Y(Y), .Sub(AluOp[0]), .S(\n1_2_32位可控加减器_1_s ));  // open: CF, OF, ZF, SF
  \_1_2_32位可控加减器  \u_1_2_32位可控加减器_2  (.X(X), .Y(Y), .Sub(AluOp[0]), .S(\n1_2_32位可控加减器_2_s ));  // open: CF, OF, ZF, SF
  assign and_1_out = Y & X;  // AND_Gate and_1, 32 bits wide
  assign or_1_out = Y | X;  // OR_Gate or_1, 32 bits wide
  Multiplier #(.width(32)) multiplier_1 (.a(Y), .b(X), .out(multiplier_1_out));  // open: cin, cout
  Comparator #(.width(32)) comparator_1 (.a(X), .b(Y), .lt(comparator_1_lt));  // open: gt, eq
  assign bit_extender_1_out = {{31{1'b0}}, comparator_1_lt};  // Bit_Extender bit_extender_1
  // Probe on X
  // Probe on Y
  // Probe on S
  // Probe on X
  // Probe on Y
  // Probe on S
  Multiplexer #(.select(3), .width(32), .enable("false")) multiplexer_1 (
    .in0(\n1_2_32位可控加减器_1_s ), .in1(\n1_2_32位可控加减器_2_s ), .in2(and_1_out), .in3(or_1_out),
    .in4(multiplier_1_out), .in5(buffer_1_out), .in6(not_1_out), .in7(bit_extender_1_out), .out(S),
    .sel(AluOp));
  Comparator #(.width(32)) comparator_2 (.a(S), .b({32{1'b0}}), .eq(ZF));  // open: gt, lt
  \_1_2_32位可控加减器  \u_1_2_32位可控加减器_3  (
    .X(Y), .Y(X), .Sub(AluOp[0]), .OF(\n1_2_32位可控加减器_3_of ), .SF(\n1_2_32位可控加减器_3_sf ));  // open: S, CF, ZF
  \_1_2_32位可控加减器  \u_1_2_32位可控加减器_4  (
    .X(Y), .Y(X), .Sub(AluOp[0]), .OF(\n1_2_32位可控加减器_4_of ), .SF(\n1_2_32位可控加减器_4_sf ));  // open: S, CF, ZF
  \_1_2_32位可控加减器  \u_1_2_32位可控加减器_5  (.X(Y), .Y(X), .Sub(AluOp[0]), .OF(\n1_2_32位可控加减器_5_of ));  // open: S, CF, ZF, SF
  \_1_2_32位可控加减器  \u_1_2_32位可控加减器_6  (.X(Y), .Y(X), .Sub(AluOp[0]), .OF(\n1_2_32位可控加减器_6_of ));  // open: S, CF, ZF, SF
  xor xor_1 (xor_1_out, \n1_2_32位可控加减器_3_of , \n1_2_32位可控加减器_3_sf );
  xor xor_2 (xor_2_out, \n1_2_32位可控加减器_4_of , \n1_2_32位可控加减器_4_sf );
  Multiplexer #(.select(3), .enable("false")) multiplexer_2 (
    .in0(xor_1_out), .in1(xor_2_out), .in2(1'b0), .in3(1'b0), .in4(1'b0), .in5(1'b0), .in6(1'b0), .in7(1'b0),
    .out(OF), .sel(AluOp));
  Multiplexer #(.select(3), .enable("false")) multiplexer_3 (
    .in0(\n1_2_32位可控加减器_6_of ), .in1(\n1_2_32位可控加减器_5_of ), .in2(1'b0), .in3(1'b0), .in4(1'b0), .in5(1'b0),
    .in6(1'b0), .in7(1'b0), .out(UOF), .sel(AluOp));

  // Notes on the sheet:
  //   输入引脚区
  //   000 ：S=X+Y
  //   注：不能增加任何输入输出端口信号
  //   001：S=X-Y
  //   010 ：S=X&Y
  //   实现一个32位的ALU，可以由AluOP控制实现8种运算操作，并产生正确的标志位。AluOp与运算关系如下：
  //   011：S=X|Y
  //   输出引脚区
  //   100 ：S=X^Y
  //   =
  //   有符号数
  //   101 ：S=Y
  //   110 ：S=~Y
  //   =
  //   结果测试区
  //   无符号数
  //   111 ：S=X<Y?1:0
endmodule

module \_1_4_补码一位乘法器  (
  input  [7:0] X,
  input  [7:0] Y,
  output [15:0] S
);

  wire and_1_out, clock_1_out, comparator_2_eq, not_2_out, not_3_out, Reset, tunnel;
  wire [0:0] \n1_1_8位加法器_1_s_2 , Yn_1_q;
  wire [7:0] counter_1_q, multiplexer_1_out, multiplexer_2_out, \n1_1_8位加法器_1_s , not_1_out;

  Clock clock_1 (.out(clock_1_out));
  Button \u_复位  (.out(Reset));
  // Probe on S[15:8]
  Register \u_Σ_2  (
    .D({{2{\n1_1_8位加法器_1_s [7]}}, \n1_1_8位加法器_1_s [5:0]}), .en(not_2_out), .Q(S[15:8]), .clk(clock_1_out),
    .clr(Reset));
  Register u_Y (.D(multiplexer_1_out), .en(not_2_out), .Q(S[7:0]), .clk(clock_1_out), .clr(Reset));
  Multiplexer #(.width(8), .enable("false")) multiplexer_1 (
    .in0({\n1_1_8位加法器_1_s_2 [0], S[7:1]}), .in1(Y), .out(multiplexer_1_out), .sel(tunnel));
  \_1_1__8位加法器  \u_1_1_8位加法器_1  (
    .X(S[15:8]), .Y(multiplexer_2_out), .Cin(and_1_out),
    .S({\n1_1_8位加法器_1_s [7], \n1_1_8位加法器_1_s [5:0], \n1_1_8位加法器_1_s_2 [0]}));  // open: Cout, OF
  // Probe on S[7:0]
  Register #(.width(1)) Yn_1 (.D(S[0]), .en(not_2_out), .Q(Yn_1_q[0]), .clk(clock_1_out), .clr(Reset));
  Multiplexer #(.select(2), .width(8), .enable("false")) multiplexer_2 (
    .in0({8{1'b0}}), .in1(X), .in2(not_1_out), .in3({8{1'b0}}), .out(multiplexer_2_out),
    .sel({S[0], Yn_1_q[0]}));
  assign not_1_out = ~X;  // NOT_Gate not_1, 8 bits wide
  // Probe on Yn_1_q[0]
  not not_2 (not_2_out, comparator_2_eq);
  and and_1 (and_1_out, S[0], not_3_out);
  not not_3 (not_3_out, Yn_1_q[0]);
  // Probe on X
  // Probe on Y
  // Probe on S
  Counter counter_1 (.Q(counter_1_q), .clk(clock_1_out), .clr(Reset));  // open: load, D, count, carry
  Comparator comparator_1 (.a(counter_1_q), .b({8{1'b0}}), .eq(tunnel));  // open: gt, lt
  Comparator comparator_2 (.a(counter_1_q), .b(8'h9), .eq(comparator_2_eq));  // open: gt, lt

  // Other names for the same wires on the sheet: 乘积[15:0] = S

  // Notes on the sheet:
  //   注：不能增加任何输入输出端口信号
  //   输入引脚区
  //   算术右移1位
  //   功能说明：补码一位乘法器，S=X×Y，要求采用Booth乘法实现，最终结果输出到乘积引脚上。
  //   输出引脚区
  //   =
  //   有符号数
  //   核心算法：｛∑，Y｝=｛∑，( Yn+1-Yn ) [X]    ,    Y }  / 2
  //   结果测试区
  //   补
endmodule

module \_1位全加器  (
  input  Cin,
  input  Xi,
  input  Yi,
  output Cout,
  output Si
);

  wire and_1_out, and_2_out, xor_2_out;

  and and_1 (and_1_out, Xi, Yi);
  or or_1 (Cout, and_1_out, and_2_out);
  and and_2 (and_2_out, Cin, xor_2_out);
  xor xor_1 (Si, Cin, xor_2_out);
  xor xor_2 (xor_2_out, Xi, Yi);
endmodule
