// Logisim project 实验2.circ as structural Verilog: 5 circuits, main circuit main
module main (
  input  [11:0] A,
  input  We,
  input  clk,
  input  [31:0] Di,
  output [31:0] Do
);

  RAM #(.addrWidth(12), .bus("separate"), .Select("high"), .simpleMode("false")) ram_1 (
    .addr(A), .din(Di[31:24]), .data(Do[31:24]), .str(We), .clk(clk));  // open: sel, ld, clr
  RAM #(.addrWidth(12), .bus("separate"), .Select("high"), .simpleMode("false")) ram_2 (
    .addr(A), .din(Di[23:16]), .data(Do[23:16]), .str(We), .clk(clk));  // open: sel, ld, clr
  RAM #(.addrWidth(12), .bus("separate"), .Select("high"), .simpleMode("false")) ram_3 (
    .addr(A), .din(Di[15:8]), .data(Do[15:8]), .str(We), .clk(clk));  // open: sel, ld, clr
  RAM #(.addrWidth(12), .bus("separate"), .Select("high"), .simpleMode("false")) ram_4 (
    .addr(A), .din(Di[7:0]), .data(Do[7:0]), .str(We), .clk(clk));  // open: sel, ld, clr
endmodule

module \存储器  (
  input  CLK,
  input  [15:0] A,
  input  We,
  input  [31:0] Di,
  output [31:0] Do
);

  wire [31:0] demultiplexer_1_out0, demultiplexer_1_out1, demultiplexer_1_out2, demultiplexer_1_out3;

  Demultiplexer #(.select(2), .width(32), .enable("false")) demultiplexer_1 (
    .out0(demultiplexer_1_out0), .out1(demultiplexer_1_out1), .out2(demultiplexer_1_out2),
    .out3(demultiplexer_1_out3), .in(Di), .sel(A[15:14]));
  main main_1 (.A(A[13:2]), .We(We), .clk(CLK), .Di(demultiplexer_1_out0), .Do(Do));
  main main_2 (.A(A[13:2]), .We(We), .clk(CLK), .Di(demultiplexer_1_out1), .Do(Do));
  main main_3 (.A(A[13:2]), .We(We), .clk(CLK), .Di(demultiplexer_1_out2), .Do(Do));
  main main_4 (.A(A[13:2]), .We(We), .clk(CLK), .Di(demultiplexer_1_out3), .Do(Do));
endmodule

module RegFile (
  input  [1:0] ra,
  input  [1:0] rw,
  input  [1:0] rb,
  input  [31:0] din,
  input  we,
  input  clk,
  output [31:0] douta,
  output [31:0] doutb
);

  wire and_1_out, and_2_out, and_3_out, and_4_out, decoder_1_out0, decoder_1_out1, decoder_1_out2,
       decoder_1_out3;
  wire [31:0] register_1_q, register_2_q, register_3_q, register_4_q;

  Decoder #(.select(2), .enable("false")) decoder_1 (
    .out0(decoder_1_out0), .out1(decoder_1_out1), .out2(decoder_1_out2), .out3(decoder_1_out3), .sel(rw));
  and and_1 (and_1_out, we, decoder_1_out0, clk);
  and and_2 (and_2_out, we, decoder_1_out1, clk);
  and and_3 (and_3_out, we, decoder_1_out2, clk);
  and and_4 (and_4_out, we, decoder_1_out3, clk);
  Register #(.width(32), .Select("high")) register_1 (
    .D(din), .en(and_1_out), .Q(register_1_q), .clk(and_1_out));  // open: clr
  Register #(.width(32), .Select("high")) register_2 (
    .D(din), .en(and_2_out), .Q(register_2_q), .clk(and_2_out));  // open: clr
  Register #(.width(32), .Select("high")) register_3 (
    .D(din), .en(and_3_out), .Q(register_3_q), .clk(and_3_out));  // open: clr
  Register #(.width(32), .Select("high")) register_4 (
    .D(din), .en(and_4_out), .Q(register_4_q), .clk(and_4_out));  // open: clr
  Multiplexer #(.select(2), .width(32), .enable("false")) multiplexer_1 (
    .in0(register_1_q), .in1(register_2_q), .in2(register_3_q), .in3(register_4_q), .out(douta), .sel(ra));
  Multiplexer #(.select(2), .width(32), .enable("false")) multiplexer_2 (
    .in0(register_1_q), .in1(register_2_q), .in2(register_3_q), .in3(register_4_q), .out(doutb), .sel(rb));
endmodule

module REGFILE (
  input  [4:0] RA1,
  input  [4:0] RA2,
  input  [4:0] WA,
  input  [31:0] Din,
  input  in_5,
  input  WE,
  output [31:0] RD1,
  output [31:0] RD2
);

  wire and_1_out, and_2_out, demultiplexer_1_out0, demultiplexer_1_out1, demultiplexer_1_out2,
       demultiplexer_1_out3, demultiplexer_1_out4, demultiplexer_1_out5, demultiplexer_1_out6,
       demultiplexer_1_out7;
  wire [31:0] regfile_1_douta, regfile_1_doutb, regfile_2_douta, regfile_2_doutb, regfile_3_douta,
       regfile_3_doutb, regfile_4_douta, regfile_4_doutb, regfile_5_douta, regfile_5_doutb, regfile_6_douta,
       regfile_6_doutb, regfile_7_douta, regfile_7_doutb, regfile_8_douta, regfile_8_doutb;

  Demultiplexer #(.select(3), .enable("false")) demultiplexer_1 (
    .out0(demultiplexer_1_out0), .out1(demultiplexer_1_out1), .out2(demultiplexer_1_out2),
    .out3(demultiplexer_1_out3), .out4(demultiplexer_1_out4), .out5(demultiplexer_1_out5),
    .out6(demultiplexer_1_out6), .out7(demultiplexer_1_out7), .in(WE), .sel(WA[4:2]));
  and and_1 (and_1_out, WA[0], WA[1]);
  and and_2 (and_2_out, and_1_out, demultiplexer_1_out0);
  RegFile regfile_1 (
    .ra(RA1[1:0]), .rw(WA[1:0]), .rb(RA2[1:0]), .din(Din), .we(and_2_out), .clk(in_5),
    .douta(regfile_1_douta), .doutb(regfile_1_doutb));
  RegFile regfile_2 (
    .ra(RA1[1:0]), .rw(WA[1:0]), .rb(RA2[1:0]), .din(Din), .we(demultiplexer_1_out1), .clk(in_5),
    .douta(regfile_2_douta), .doutb(regfile_2_doutb));
  RegFile regfile_3 (
    .ra(RA1[1:0]), .rw(WA[1:0]), .rb(RA2[1:0]), .din(Din), .we(demultiplexer_1_out2), .clk(in_5),
    .douta(regfile_3_douta), .doutb(regfile_3_doutb));
  RegFile regfile_4 (
    .ra(RA1[1:0]), .rw(WA[1:0]), .rb(RA2[1:0]), .din(Din), .we(demultiplexer_1_out3), .clk(in_5),
    .douta(regfile_4_douta), .doutb(regfile_4_doutb));
  RegFile regfile_5 (
    .ra(RA1[1:0]), .rw(WA[1:0]), .rb(RA2[1:0]), .din(Din), .we(demultiplexer_1_out4), .clk(in_5),
    .douta(regfile_5_douta), .doutb(regfile_5_doutb));
  RegFile regfile_6 (
    .ra(RA1[1:0]), .rw(WA[1:0]), .rb(RA2[1:0]), .din(Din), .we(demultiplexer_1_out5), .clk(in_5),
    .douta(regfile_6_douta), .doutb(regfile_6_doutb));
  RegFile regfile_7 (
    .ra(RA1[1:0]), .rw(WA[1:0]), .rb(RA2[1:0]), .din(Din), .we(demultiplexer_1_out6), .clk(in_5),
    .douta(regfile_7_douta), .doutb(regfile_7_doutb));
  RegFile regfile_8 (
    .ra(RA1[1:0]), .rw(WA[1:0]), .rb(RA2[1:0]), .din(Din), .we(demultiplexer_1_out7), .clk(in_5),
    .douta(regfile_8_douta), .doutb(regfile_8_doutb));
  Multiplexer #(.select(3), .width(32), .enable("false")) multiplexer_1 (
    .in0(regfile_1_douta), .in1(regfile_2_douta), .in2(regfile_3_douta), .in3(regfile_4_douta),
    .in4(regfile_5_douta), .in5(regfile_6_douta), .in6(regfile_7_douta), .in7(regfile_8_douta), .out(RD1),
    .sel(RA1[4:2]));
  Multiplexer #(.select(3), .width(32), .enable("false")) multiplexer_2 (
    .in0(regfile_1_doutb), .in1(regfile_2_doutb), .in2(regfile_3_doutb), .in3(regfile_4_doutb),
    .in4(regfile_5_doutb), .in5(regfile_6_doutb), .in6(regfile_7_doutb), .in7(regfile_8_doutb), .out(RD2),
    .sel(RA2[4:2]));
endmodule

module over (
  input  in_1,
  input  [1:0] in_2,
  input  [4:0] in_3,
  input  in_4,
  input  [2:0] in_5,
  input  [4:0] in_6,
  input  [31:0] in_7,
  input  [1:0] in_8,
  input  in_9,
  input  [4:0] in_10,
  input  in_11,
  output [31:0] out_12
);

  wire [31:0] alu_1_p4, multiplexer_1_out, multiplexer_2_out, regfile_1_rd1, regfile_1_rd2, \存储器_1_do ;

  REGFILE regfile_1 (
    .RA1(in_3), .RA2(in_6), .WA(in_10), .Din(multiplexer_2_out), .WE(in_4), .in_5(in_9), .RD1(regfile_1_rd1),
    .RD2(regfile_1_rd2));
  Multiplexer #(.width(32), .enable("false")) multiplexer_1 (
    .in0(regfile_1_rd2), .in1(in_7), .out(multiplexer_1_out), .sel(in_1));
  Multiplexer #(.select(2), .width(32), .enable("false")) multiplexer_2 (
    .in0(in_7), .in1(alu_1_p4), .in2(\存储器_1_do ), .in3({32{1'b0}}), .out(multiplexer_2_out), .sel(in_8));
  // ALU alu_1: pin names not known; wires that end beside it: regfile_1_rd1, multiplexer_1_out, in_5, alu_1_p4
  \存储器  \u_存储器_1  (.CLK(in_9), .A(alu_1_p4[15:0]), .We(in_11), .Di(regfile_1_rd2), .Do(\存储器_1_do ));
  Multiplexer #(.select(2), .width(32), .enable("false")) multiplexer_3 (
    .in0(alu_1_p4), .in1(regfile_1_rd2), .in2(\存储器_1_do ), .in3(multiplexer_2_out), .out(out_12), .sel(in_2));

  // Other names for the same wires on the sheet: AluOp[2:0] = in_5; AluYSel = in_1; CLK = in_9; Din[31:0] = in_7;
  //   Display[31:0] = out_12; DisSel[1:0] = in_2; DMWr = in_11; RA1[4:0] = in_3; RA2[4:0] = in_6; RFWr = in_4;
  //   RWSel[1:0] = in_8; WA[4:0] = in_10
endmodule
