// Logisim project Exp2_MEM.circ as structural Verilog: 4 circuits, main circuit 2-1  存储器扩展
module \_2_1__存储器扩展  (
  input  CLK,
  input  WE,
  input  [13:0] Addr,
  input  [31:0] Din,
  output [31:0] Dout
);

  wire decoder_1_out0, decoder_1_out1, decoder_1_out2, decoder_1_out3, not_1_out, not_2_out, not_3_out,
       not_4_out;

  Decoder #(.select(2), .tristate("false"), .disabled("Z"), .enable("false")) decoder_1 (
    .out0(decoder_1_out0), .out1(decoder_1_out1), .out2(decoder_1_out2), .out3(decoder_1_out3),
    .sel(Addr[13:12]));
  not not_1 (not_1_out, decoder_1_out0);
  not not_2 (not_2_out, decoder_1_out2);
  not not_3 (not_3_out, decoder_1_out1);
  RAM #(.addrWidth(12), .dataWidth(8), .bus("separate"), .Select("low")) ram_1 (
    .addr(Addr[11:0]), .din(Din[7:0]), .data(Dout[7:0]), .str(WE), .sel(not_1_out), .clk(CLK), .ld(1'b1));  // open: clr
  RAM #(.addrWidth(12), .dataWidth(8), .bus("separate"), .Select("low")) ram_2 (
    .addr(Addr[11:0]), .din(Din[15:8]), .data(Dout[15:8]), .str(WE), .sel(not_1_out), .clk(CLK), .ld(1'b1));  // open: clr
  RAM #(.addrWidth(12), .dataWidth(8), .bus("separate"), .Select("low")) ram_3 (
    .addr(Addr[11:0]), .din(Din[23:16]), .data(Dout[23:16]), .str(WE), .sel(not_1_out), .clk(CLK), .ld(1'b1));  // open: clr
  RAM #(.addrWidth(12), .dataWidth(8), .bus("separate"), .Select("low")) ram_4 (
    .addr(Addr[11:0]), .din(Din[31:24]), .data(Dout[31:24]), .str(WE), .sel(not_1_out), .clk(CLK), .ld(1'b1));  // open: clr
  not not_4 (not_4_out, decoder_1_out3);
  Hex_Digit_Display hex_digit_display_1 (.value(Dout[15:12]));  // open: dp
  Hex_Digit_Display hex_digit_display_2 (.value(Dout[31:28]));  // open: dp
  Hex_Digit_Display hex_digit_display_3 (.value(Dout[11:8]));  // open: dp
  Hex_Digit_Display hex_digit_display_4 (.value(Dout[7:4]));  // open: dp
  Hex_Digit_Display hex_digit_display_5 (.value(Dout[23:20]));  // open: dp
  Hex_Digit_Display hex_digit_display_6 (.value(Dout[27:24]));  // open: dp
  RAM #(.addrWidth(12), .dataWidth(8), .bus("separate"), .Select("low")) ram_5 (
    .addr(Addr[11:0]), .din(Din[7:0]), .data(Dout[7:0]), .str(WE), .sel(not_3_out), .clk(CLK), .ld(1'b1));  // open: clr
  RAM #(.addrWidth(12), .dataWidth(8), .bus("separate"), .Select("low")) ram_6 (
    .addr(Addr[11:0]), .din(Din[15:8]), .data(Dout[15:8]), .str(WE), .sel(not_3_out), .clk(CLK), .ld(1'b1));  // open: clr
  RAM #(.addrWidth(12), .dataWidth(8), .bus("separate"), .Select("low")) ram_7 (
    .addr(Addr[11:0]), .din(Din[23:16]), .data(Dout[23:16]), .str(WE), .sel(not_3_out), .clk(CLK), .ld(1'b1));  // open: clr
  RAM #(.addrWidth(12), .dataWidth(8), .bus("separate"), .Select("low")) ram_8 (
    .addr(Addr[11:0]), .din(Din[31:24]), .data(Dout[31:24]), .str(WE), .sel(not_3_out), .clk(CLK), .ld(1'b1));  // open: clr
  Hex_Digit_Display hex_digit_display_7 (.value(Dout[3:0]));  // open: dp
  Hex_Digit_Display hex_digit_display_8 (.value(Dout[19:16]));  // open: dp
  RAM #(.addrWidth(12), .dataWidth(8), .bus("separate"), .Select("low")) ram_9 (
    .addr(Addr[11:0]), .din(Din[7:0]), .data(Dout[7:0]), .str(WE), .sel(not_2_out), .clk(CLK), .ld(1'b1));  // open: clr
  RAM #(.addrWidth(12), .dataWidth(8), .bus("separate"), .Select("low")) ram_10 (
    .addr(Addr[11:0]), .din(Din[15:8]), .data(Dout[15:8]), .str(WE), .sel(not_2_out), .clk(CLK), .ld(1'b1));  // open: clr
  RAM #(.addrWidth(12), .dataWidth(8), .bus("separate"), .Select("low")) ram_11 (
    .addr(Addr[11:0]), .din(Din[23:16]), .data(Dout[23:16]), .str(WE), .sel(not_2_out), .clk(CLK), .ld(1'b1));  // open: clr
  RAM #(.addrWidth(12), .dataWidth(8), .bus("separate"), .Select("low")) ram_12 (
    .addr(Addr[11:0]), .din(Din[31:24]), .data(Dout[31:24]), .str(WE), .sel(not_2_out), .clk(CLK), .ld(1'b1));  // open: clr
  RAM #(.addrWidth(12), .dataWidth(8), .bus("separate"), .Select("low")) ram_13 (
    .addr(Addr[11:0]), .din(Din[7:0]), .data(Dout[7:0]), .str(WE), .sel(not_4_out), .clk(CLK), .ld(1'b1));  // open: clr
  RAM #(.addrWidth(12), .dataWidth(8), .bus("separate"), .Select("low")) ram_14 (
    .addr(Addr[11:0]), .din(Din[15:8]), .data(Dout[15:8]), .str(WE), .sel(not_4_out), .clk(CLK), .ld(1'b1));  // open: clr
  RAM #(.addrWidth(12), .dataWidth(8), .bus("separate"), .Select("low")) ram_15 (
    .addr(Addr[11:0]), .din(Din[23:16]), .data(Dout[23:16]), .str(WE), .sel(not_4_out), .clk(CLK), .ld(1'b1));  // open: clr
  RAM #(.addrWidth(12), .dataWidth(8), .bus("separate"), .Select("low")) ram_16 (
    .addr(Addr[11:0]), .din(Din[31:24]), .data(Dout[31:24]), .str(WE), .sel(not_4_out), .clk(CLK), .ld(1'b1));  // open: clr

  // Notes on the sheet:
  //   注：不能增加任何输入输出端口信号
  //   输入引脚区
  //   输出引脚区
  //   请用4K×8的存储芯片实现16K×32的存储器，并搭建外围电路，自动实现对存储器的读写操作
  //   输出数据测试区
endmodule

module \_2_2__MIPS_RF模块  (
  input  CLK,
  input  WE,
  input  [4:0] RA1,
  input  [4:0] RA2,
  input  [31:0] Din,
  input  [4:0] WA,
  output [31:0] RD2,
  output [31:0] RD1
);

  wire _0, _1, _2, _3, _4, _5, _6, _7, _8, _9, _10, _11, _12, _13, _14, _15, _16, _17, _18, _19, _20, _21,
       _22, _23, _24, _25, _26, _27, _28, _29, _30, _31, button_1_out, not_1_out, not_2_out, not_3_out,
       not_4_out, not_5_out, not_6_out, not_7_out, not_8_out, not_9_out, not_10_out, not_11_out, not_12_out,
       not_13_out, not_14_out, not_15_out, not_16_out, not_17_out, not_18_out, not_19_out, not_20_out,
       not_21_out, not_22_out, not_23_out, not_24_out, not_25_out, not_26_out, not_27_out, not_28_out,
       not_29_out, not_30_out, not_31_out, not_32_out, R1_0, R1_1, R1_2, R1_3, R1_4, R1_5, R1_6, R1_7, R1_8,
       R1_9, R1_10, R1_11, R1_12, R1_13, R1_14, R1_15, R1_16, R1_17, R1_18, R1_19, R1_20, R1_21, R1_22,
       R1_23, R1_24, R1_25, R1_26, R1_27, R1_28, R1_29, R1_30, R1_31, R2_0, R2_1, R2_2, R2_3, R2_4, R2_5,
       R2_6, R2_7, R2_8, R2_9, R2_10, R2_11, R2_12, R2_13, R2_14, R2_15, R2_16, R2_17, R2_18, R2_19, R2_20,
       R2_21, R2_22, R2_23, R2_24, R2_25, R2_26, R2_27, R2_28, R2_29, R2_30, R2_31, W0, W1, W2, W3, W4, W5,
       W6, W7, W8, W9, W10, W11, W12, W13, W14, W15, W16, W17, W18, W19, W20, W21, W22, W23, W24, W25, W26,
       W27, W28, W29, W30, W31;
  wire [31:0] multiplexer_1_out, O_0, O_1, O_2, O_3, O_4, O_5, O_6, O_7, O_8, O_9, O_10, O_11, O_12, O_13,
       O_14, O_15, O_16, O_17, O_18, O_19, O_20, O_21, O_22, O_23, O_24, O_25, O_26, O_27, O_29, O_30, O_31,
       undriven;

  or or_1 (_0, W0, R1_0, R2_0);
  or or_2 (_8, W8, R1_8, R2_8);
  or or_3 (_16, W16, R1_16, R2_16);
  or or_4 (_24, W24, R1_24, R2_24);
  not not_1 (not_1_out, _0);
  not not_2 (not_2_out, _1);
  not not_3 (not_3_out, _2);
  not not_4 (not_4_out, _3);
  not not_5 (not_5_out, _4);
  not not_6 (not_6_out, _5);
  not not_7 (not_7_out, _6);
  not not_8 (not_8_out, _7);
  or or_5 (_1, W1, R1_1, R2_1);
  or or_6 (_9, W9, R1_9, R2_9);
  or or_7 (_17, W17, R1_17, R2_1);
  or or_8 (_25, W25, R1_25, R2_25);
  Register #(.width(32), .trigger("rising"), .Select("low")) register_1 (
    .D({32{1'b0}}), .en(WE), .Q(O_0), .clk(CLK), .cs(not_1_out));  // open: clr, preset
  Register #(.width(32), .trigger("rising"), .Select("low")) register_2 (
    .D(Din), .en(WE), .Q(O_1), .clk(CLK), .cs(not_2_out));  // open: clr, preset
  Register #(.width(32), .trigger("rising"), .Select("low")) register_3 (
    .D(Din), .en(WE), .Q(O_2), .clk(CLK), .cs(not_3_out));  // open: clr, preset
  Register #(.width(32), .trigger("rising"), .Select("low")) register_4 (
    .D(Din), .en(WE), .Q(O_3), .clk(CLK), .cs(not_4_out));  // open: clr, preset
  Register #(.width(32), .trigger("rising"), .Select("low")) register_5 (
    .D(Din), .en(WE), .Q(O_4), .clk(CLK), .cs(not_5_out));  // open: clr, preset
  Register #(.width(32), .trigger("rising"), .Select("low")) register_6 (
    .D(Din), .en(WE), .Q(O_5), .clk(CLK), .cs(not_6_out));  // open: clr, preset
  Register #(.width(32), .trigger("rising"), .Select("low")) register_7 (
    .D(Din), .en(WE), .Q(O_6), .clk(CLK), .cs(not_7_out));  // open: clr, preset
  Register #(.width(32), .trigger("rising"), .Select("low")) register_8 (
    .D(Din), .en(WE), .Q(O_7), .clk(CLK), .cs(not_8_out));  // open: clr, preset
  not not_9 (not_9_out, _8);
  Register #(.width(32), .trigger("rising"), .Select("low")) register_9 (
    .D(Din), .en(WE), .Q(O_8), .clk(CLK), .cs(not_9_out));  // open: clr, preset
  not not_10 (not_10_out, _9);
  Register #(.width(32), .trigger("rising"), .Select("low")) register_10 (
    .D(Din), .en(WE), .Q(O_9), .clk(CLK), .cs(not_10_out));  // open: clr, preset
  not not_11 (not_11_out, _10);
  Register #(.width(32), .trigger("rising"), .Select("low")) register_11 (
    .D(Din), .en(WE), .Q(O_10), .clk(CLK), .cs(not_11_out));  // open: clr, preset
  not not_12 (not_12_out, _11);
  Register #(.width(32), .trigger("rising"), .Select("low")) register_12 (
    .D(Din), .en(WE), .Q(O_11), .clk(CLK), .cs(not_12_out));  // open: clr, preset
  not not_13 (not_13_out, _12);
  Register #(.width(32), .trigger("rising"), .Select("low")) register_13 (
    .D(Din), .en(WE), .Q(O_12), .clk(CLK), .cs(not_13_out));  // open: clr, preset
  not not_14 (not_14_out, _13);
  Register #(.width(32), .trigger("rising"), .Select("low")) register_14 (
    .D(Din), .en(WE), .Q(O_13), .clk(CLK), .cs(not_14_out));  // open: clr, preset
  not not_15 (not_15_out, _14);
  Register #(.width(32), .trigger("rising"), .Select("low")) register_15 (
    .D(Din), .en(WE), .Q(O_14), .clk(CLK), .cs(not_15_out));  // open: clr, preset
  not not_16 (not_16_out, _15);
  Register #(.width(32), .trigger("rising"), .Select("low")) register_16 (
    .D(Din), .en(WE), .Q(O_15), .clk(CLK), .cs(not_16_out));  // open: clr, preset
  Decoder #(.select(5), .tristate("false"), .disabled("Z"), .enable("false")) decoder_1 (
    .out0(W0), .out1(W1), .out2(W2), .out3(W3), .out4(W4), .out5(W5), .out6(W6), .out7(W7), .out8(W8),
    .out9(W9), .out10(W10), .out11(W11), .out12(W12), .out13(W13), .out14(W14), .out15(W15), .out16(W16),
    .out17(W17), .out18(W18), .out19(W19), .out20(W20), .out21(W21), .out22(W22), .out23(W23), .out24(W24),
    .out25(W25), .out26(W26), .out27(W27), .out28(W28), .out29(W29), .out30(W30), .out31(W31), .sel(WA));
  or or_9 (_2, W2, R1_2, R2_2);
  or or_10 (_10, W10, R1_10, R2_10);
  or or_11 (_18, W18, R1_18, R2_18);
  or or_12 (_26, W26, R1_26, R2_26);
  not not_17 (not_17_out, _16);
  Register #(.width(32), .trigger("rising"), .Select("low")) register_17 (
    .D(Din), .en(WE), .Q(O_16), .clk(CLK), .cs(not_17_out));  // open: clr, preset
  not not_18 (not_18_out, _17);
  Register #(.width(32), .trigger("rising"), .Select("low")) register_18 (
    .D(Din), .en(WE), .Q(O_17), .clk(CLK), .cs(not_18_out));  // open: clr, preset
  not not_19 (not_19_out, _18);
  Register #(.width(32), .trigger("rising"), .Select("low")) register_19 (
    .D(Din), .en(WE), .Q(O_18), .clk(CLK), .cs(not_19_out));  // open: clr, preset
  not not_20 (not_20_out, _19);
  Register #(.width(32), .trigger("rising"), .Select("low")) register_20 (
    .D(Din), .en(WE), .Q(O_19), .clk(CLK), .cs(not_20_out));  // open: clr, preset
  not not_21 (not_21_out, _20);
  Register #(.width(32), .trigger("rising"), .Select("low")) register_21 (
    .D(Din), .en(WE), .Q(O_20), .clk(CLK), .cs(not_21_out));  // open: clr, preset
  not not_22 (not_22_out, _21);
  Register #(.width(32), .trigger("rising"), .Select("low")) register_22 (
    .D(Din), .en(WE), .Q(O_21), .clk(CLK), .cs(not_22_out));  // open: clr, preset
  not not_23 (not_23_out, _22);
  Register #(.width(32), .trigger("rising"), .Select("low")) register_23 (
    .D(Din), .en(WE), .Q(O_22), .clk(CLK), .cs(not_23_out));  // open: clr, preset
  not not_24 (not_24_out, _23);
  Register #(.width(32), .trigger("rising"), .Select("low")) register_24 (
    .D(Din), .en(WE), .Q(O_23), .clk(CLK), .cs(not_24_out));  // open: clr, preset
  Multiplexer #(.select(1), .width(32), .disabled("Z"), .enable("false")) multiplexer_1 (
    .in0(RD1), .in1(RD2), .out(multiplexer_1_out), .sel(button_1_out));
  Button button_1 (.out(button_1_out));
  not not_25 (not_25_out, _24);
  Register #(.width(32), .trigger("rising"), .Select("low")) register_25 (
    .D(Din), .en(WE), .Q(O_24), .clk(CLK), .cs(not_25_out));  // open: clr, preset
  not not_26 (not_26_out, _25);
  Register #(.width(32), .trigger("rising"), .Select("low")) register_26 (
    .D(Din), .en(WE), .Q(O_25), .clk(CLK), .cs(not_26_out));  // open: clr, preset
  not not_27 (not_27_out, _26);
  Register #(.width(32), .trigger("rising"), .Select("low")) register_27 (
    .D(Din), .en(WE), .Q(O_26), .clk(CLK), .cs(not_27_out));  // open: clr, preset
  not not_28 (not_28_out, _27);
  Register #(.width(32), .trigger("rising"), .Select("low")) register_28 (
    .D(Din), .en(WE), .Q(O_27), .clk(CLK), .cs(not_28_out));  // open: clr, preset
  not not_29 (not_29_out, _28);
  Register #(.width(32), .trigger("rising"), .Select("low")) register_29 (
    .D(Din), .en(WE), .Q(O_27), .clk(CLK), .cs(not_29_out));  // open: clr, preset
  not not_30 (not_30_out, _29);
  Register #(.width(32), .trigger("rising"), .Select("low")) register_30 (
    .D(Din), .en(WE), .Q(O_29), .clk(CLK), .cs(not_30_out));  // open: clr, preset
  not not_31 (not_31_out, _30);
  Register #(.width(32), .trigger("rising"), .Select("low")) register_31 (
    .D(Din), .en(WE), .Q(O_30), .clk(CLK), .cs(not_31_out));  // open: clr, preset
  not not_32 (not_32_out, _31);
  Register #(.width(32), .trigger("rising"), .Select("low")) register_32 (
    .D(Din), .en(WE), .Q(O_31), .clk(CLK), .cs(not_32_out));  // open: clr, preset
  or or_13 (_3, W3, R1_3, R2_3);
  or or_14 (_11, W11, R1_11, R2_1);
  or or_15 (_19, W19, R1_19, R2_19);
  or or_16 (_27, W27, R1_27, R2_27);
  Hex_Digit_Display hex_digit_display_1 (.value(multiplexer_1_out[15:12]));  // open: dp
  Hex_Digit_Display hex_digit_display_2 (.value(multiplexer_1_out[31:28]));  // open: dp
  Decoder #(.select(5), .tristate("false"), .disabled("Z"), .enable("false")) decoder_2 (
    .out0(R1_0), .out1(R1_1), .out2(R1_2), .out3(R1_3), .out4(R1_4), .out5(R1_5), .out6(R1_6), .out7(R1_7),
    .out8(R1_8), .out9(R1_9), .out10(R1_10), .out11(R1_11), .out12(R1_12), .out13(R1_13), .out14(R1_14),
    .out15(R1_15), .out16(R1_16), .out17(R1_17), .out18(R1_18), .out19(R1_19), .out20(R1_20), .out21(R1_21),
    .out22(R1_22), .out23(R1_23), .out24(R1_24), .out25(R1_25), .out26(R1_26), .out27(R1_27), .out28(R1_28),
    .out29(R1_29), .out30(R1_30), .out31(R1_31), .sel(RA1));
  or or_17 (_4, W4, R1_4, R2_4);
  or or_18 (_12, W12, R1_12, R2_12);
  or or_19 (_20, W20, R1_20, R2_20);
  or or_20 (_28, W28, R1_28, R2_28);
  Hex_Digit_Display hex_digit_display_3 (.value(multiplexer_1_out[7:4]));  // open: dp
  Hex_Digit_Display hex_digit_display_4 (.value(multiplexer_1_out[11:8]));  // open: dp
  Hex_Digit_Display hex_digit_display_5 (.value(multiplexer_1_out[27:24]));  // open: dp
  Hex_Digit_Display hex_digit_display_6 (.value(multiplexer_1_out[23:20]));  // open: dp
  Hex_Digit_Display hex_digit_display_7 (.value(multiplexer_1_out[3:0]));  // open: dp
  Hex_Digit_Display hex_digit_display_8 (.value(multiplexer_1_out[19:16]));  // open: dp
  or or_21 (_5, W5, R1_5, R2_5);
  or or_22 (_13, W13, R1_13, R2_13);
  or or_23 (_21, W21, R1_21, R2_21);
  or or_24 (_29, W29, R1_29, R2_29);
  Multiplexer #(.select(5), .width(32), .disabled("Z"), .enable("false")) multiplexer_2 (
    .in0(O_0), .in1(O_1), .in2(O_2), .in3(O_3), .in4(O_4), .in5(O_5), .in6(O_6), .in7(O_7), .in8(O_8),
    .in9(O_9), .in10(O_10), .in11(O_11), .in12(O_12), .in13(O_13), .in14(O_14), .in15(O_15), .in16(O_16),
    .in17(O_17), .in18(O_18), .in19(O_19), .in20(O_20), .in21(O_21), .in22(O_22), .in23(O_23), .in24(O_24),
    .in25(O_25), .in26(O_26), .in27(O_27), .in28(O_27), .in29(O_29), .in30(O_30), .in31(O_31), .out(RD1),
    .sel(RA1));
  or or_25 (_6, W6, R1_6, R2_6);
  or or_26 (_14, W14, R1_14, R2_14);
  or or_27 (_22, W22, R1_22, R2_22);
  Decoder #(.select(5), .tristate("false"), .disabled("Z"), .enable("false")) decoder_3 (
    .out0(R2_0), .out1(R2_1), .out2(R2_2), .out3(R2_3), .out4(R2_4), .out5(R2_5), .out6(R2_6), .out7(R2_7),
    .out8(R2_8), .out9(R2_9), .out10(R2_10), .out11(R2_11), .out12(R2_12), .out13(R2_13), .out14(R2_14),
    .out15(R2_15), .out16(R2_16), .out17(R2_17), .out18(R2_18), .out19(R2_19), .out20(R2_20), .out21(R2_21),
    .out22(R2_22), .out23(R2_23), .out24(R2_24), .out25(R2_25), .out26(R2_26), .out27(R2_27), .out28(R2_28),
    .out29(R2_29), .out30(R2_30), .out31(R2_31), .sel(RA2));
  or or_28 (_30, W30, R1_30, R2_30);
  Multiplexer #(.select(5), .width(32), .disabled("Z"), .enable("false")) multiplexer_3 (
    .in0(O_0), .in1(O_1), .in2(O_2), .in3(O_3), .in4(O_4), .in5(O_5), .in6(O_6), .in7(O_7), .in8(O_8),
    .in9(O_9), .in10(O_10), .in11(O_11), .in12(O_12), .in13(O_13), .in14(undriven), .in15(O_15), .in16(O_16),
    .in17(O_17), .in18(O_18), .in19(O_19), .in20(O_20), .in21(O_21), .in22(O_22), .in23(O_23), .in24(O_24),
    .in25(O_25), .in26(O_26), .in27(O_27), .in28(O_27), .in29(O_29), .in30(O_30), .in31(O_31), .out(RD2),
    .sel(RA2));
  or or_29 (_7, W7, R1_7, R2_7);
  or or_30 (_15, W15, R1_15, R2_15);
  or or_31 (_23, W23, R1_23, R2_23);
  or or_32 (_31, W31, R1_31, R2_31);

  // Other names for the same wires on the sheet: O_28[31:0] = O_27

  // Notes on the sheet:
  //   输入引脚区
  //   注：不能增加任何输入输出端口信号
  //   7
  //   输出引脚区
  //   实现MIPS寄存器组，32个寄存器可以采用模块化方法实现，模块规模不限，注意0号寄存器恒为0
  //   1
  //   输出数据测试区
endmodule

module \_2_3__数据互传  (
  input  CLK,
  input  WE,
  input  [2:0] AluOp,
  input  [1:0] RWsel,
  input  LA1,
  input  LA2,
  input  [31:0] Din,
  input  LWA,
  input  [1:0] Dispsel,
  input  in_10,
  input  in_11,
  output [31:0] Disp
);

  wire [4:0] register_1_q, register_2_q, register_3_q;
  wire [31:0] multiplexer_1_out, multiplexer_2_out, \n1_3_32位alu_1_p4 , \n2_1_存储器扩展_1_dout ,
       \n2_2_mips_rf模块_1_rd1 , \n2_2_mips_rf模块_1_rd2 ;

  // Probe on Din[31:27]
  // Probe on register_1_q
  Register #(.width(5), .trigger("rising"), .Select("low")) register_1 (
    .D(Din[31:27]), .en(LA1), .Q(register_1_q), .clk(CLK));  // open: clr
  // Probe on register_2_q
  Register #(.width(5), .trigger("rising"), .Select("low")) register_2 (
    .D(Din[31:27]), .en(LA2), .Q(register_2_q), .clk(CLK));  // open: clr
  // Probe on register_3_q
  Register #(.width(5), .trigger("rising"), .Select("low")) register_3 (
    .D(Din[31:27]), .en(LWA), .Q(register_3_q), .clk(CLK));  // open: clr
  // Probe on multiplexer_1_out
  \_2_2__MIPS_RF模块  \u_2_2_mips_rf模块_1  (
    .RA1(register_1_q), .RA2(register_2_q), .WA(register_3_q), .Din(multiplexer_1_out), .CLK(CLK),
    .WE(in_11), .RD1(\n2_2_mips_rf模块_1_rd1 ), .RD2(\n2_2_mips_rf模块_1_rd2 ));
  Multiplexer #(.select(2), .width(32), .disabled("Z"), .enable("false")) multiplexer_1 (
    .in0(Din), .in1(\n1_3_32位alu_1_p4 ), .in2(\n2_1_存储器扩展_1_dout ), .in3({32{1'b0}}),
    .out(multiplexer_1_out), .sel(RWsel));
  Multiplexer #(.select(1), .width(32), .disabled("Z"), .enable("false")) multiplexer_2 (
    .in0(\n2_2_mips_rf模块_1_rd2 ), .in1(Din), .out(multiplexer_2_out), .sel(in_10));
  // Probe on \n2_2_mips_rf模块_1_rd1 
  // Probe on multiplexer_2_out
  Hex_Digit_Display hex_digit_display_1 (.value(Disp[11:8]));  // open: dp
  Hex_Digit_Display hex_digit_display_2 (.value(Disp[15:12]));  // open: dp
  Hex_Digit_Display hex_digit_display_3 (.value(Disp[31:28]));  // open: dp
  Hex_Digit_Display hex_digit_display_4 (.value(Disp[27:24]));  // open: dp
  // _1_3_32位ALU 1_3_32位alu_1: pin names not known; wires that end beside it: \n2_2_mips_rf模块_1_rd1 , multiplexer_2_out, AluOp, \n1_3_32位alu_1_p4 
  // Probe on \n1_3_32位alu_1_p4 
  Hex_Digit_Display hex_digit_display_5 (.value(Disp[3:0]));  // open: dp
  Hex_Digit_Display hex_digit_display_6 (.value(Disp[7:4]));  // open: dp
  Hex_Digit_Display hex_digit_display_7 (.value(Disp[19:16]));  // open: dp
  Hex_Digit_Display hex_digit_display_8 (.value(Disp[23:20]));  // open: dp
  // Probe on \n1_3_32位alu_1_p4 [13:0]
  // Probe on \n2_2_mips_rf模块_1_rd1 
  \_2_1__存储器扩展  \u_2_1_存储器扩展_1  (
    .Addr(\n1_3_32位alu_1_p4 [13:0]), .Din(\n2_2_mips_rf模块_1_rd1 ), .CLK(CLK), .WE(WE),
    .Dout(\n2_1_存储器扩展_1_dout ));
  Multiplexer #(.select(2), .width(32), .disabled("Z"), .enable("false")) multiplexer_3 (
    .in0(\n2_2_mips_rf模块_1_rd1 ), .in1(\n2_2_mips_rf模块_1_rd2 ), .in2(\n1_3_32位alu_1_p4 ),
    .in3(\n2_1_存储器扩展_1_dout ), .out(Disp), .sel(Dispsel));

  // Other names for the same wires on the sheet: MUX1 = in_10; WE_RF = in_11

  // Notes on the sheet:
  //   输入引脚区
  //   注：请完善数据通路可以增加必要的输入控制端口信号
  //   输出引脚区
  //   注：数据通路图中RF使用2-2MIPS RF模块，MEMU是2-1存储器扩展模块
  //   输出数据测试区
endmodule

module \测试电路  (
  input  in_1,
  input  [13:0] in_2,
  input  in_3,
  input  [31:0] in_4,
  input  in_5
);

  wire clock_1_out;
  wire [13:0] counter_1_q;
  wire [31:0] counter_2_q, \n2_1_存储器扩展_1_dout ;

  Clock #(.highDuration(1), .lowDuration(1)) clock_1 (.out(clock_1_out));
  Counter #(.width(14), .max('h3fff), .ongoal("wrap"), .trigger("rising"), .behavior("new")) counter_1 (
    .load(in_1), .D(in_2), .Q(counter_1_q), .clk(clock_1_out), .clr(in_5));  // open: count, carry, preset, down
  Counter #(.width(32), .max('hffffffff), .ongoal("wrap"), .trigger("rising"), .behavior("new")) counter_2 (
    .load(in_1), .D(in_4), .Q(counter_2_q), .clk(clock_1_out), .clr(in_5));  // open: count, carry, preset, down
  // Probe on counter_1_q
  // Probe on counter_2_q
  \_2_1__存储器扩展  \u_2_1_存储器扩展_1  (
    .Addr(counter_1_q), .Din(counter_2_q), .CLK(clock_1_out), .WE(in_3), .Dout(\n2_1_存储器扩展_1_dout ));
  // Probe on \n2_1_存储器扩展_1_dout 

  // Notes on the sheet:
  //   起始地址
  //   起始数据
endmodule
