// Logisim project 软件工程2201黄少政17.circ as structural Verilog: 8 circuits, main circuit ◇单周期MIPS
module \单周期MIPS  (
  output [31:0] PC,
  output [31:0] IR,
  output [31:0] RDin,
  output [31:0] MDin,
  output [31:0] LedData
);

  wire ALUB_src, beq, CLK, DMWr, Go, Jump, REGA3_src, RFWr, Rst, Sign_ext, zero, \单周期硬布线控制器_1_npcop ;
  wire [1:0] REGD_src;
  wire [2:0] ALUOp;
  wire [4:0] multiplexer_2_out;
  wire [15:0] bit_extender_2_out, \总周期数 ;
  wire [25:0] bit_extender_1_out;
  wire [31:0] bit_extender_3_out, bit_extender_4_out, mips_alu_1_s, mips_regifile_1_r1, multiplexer_1_out,
       multiplexer_3_out, multiplexer_4_out, rom_1_data, undriven, undriven_2;

  Clock #(.highDuration(1), .lowDuration(1)) clock_1 (.out(CLK));
  Button button_1 (.out(Rst));
  // DipSwitch #(.NSwitches(1)) dipswitch_1: pin names not known; wires that end beside it: Go
  NPC npc_1 (.Zero(zero), .Jump(Jump), .Imm(multiplexer_1_out), .Clk(CLK), .Branch(beq), .RST(Rst), .PC(PC));
  Multiplexer #(.select(1), .width(32), .disabled("Z"), .enable("false")) multiplexer_1 (
    .in0(undriven), .in1(undriven_2), .out(multiplexer_1_out), .sel(\单周期硬布线控制器_1_npcop ));
  Hex_Digit_Display hex_digit_display_1 (.value(LedData[31:28]));  // open: dp
  Hex_Digit_Display hex_digit_display_2 (.value(LedData[23:20]));  // open: dp
  Hex_Digit_Display hex_digit_display_3 (.value(LedData[27:24]));  // open: dp
  Bit_Extender #(.in_width(32), .out_width(26), .\type ("zero")) bit_extender_1 (
    .in(undriven), .out(bit_extender_1_out));
  Bit_Extender #(.in_width(32), .out_width(16), .\type ("zero")) bit_extender_2 (
    .in(undriven_2), .out(bit_extender_2_out));
  Hex_Digit_Display hex_digit_display_4 (.value(LedData[15:12]));  // open: dp
  Hex_Digit_Display hex_digit_display_5 (.value(LedData[19:16]));  // open: dp
  ROM #(.addrWidth(10), .dataWidth(32), .Select("high")) rom_1 (.addr(PC[11:2]), .data(rom_1_data));
  Hex_Digit_Display hex_digit_display_6 (.value(LedData[11:8]));  // open: dp
  Hex_Digit_Display hex_digit_display_7 (.value(LedData[7:4]));  // open: dp
  // Probe on \总周期数 
  ID id_1 (
    .Instruction(rom_1_data), .OP(IR[31:26]), .Funct(IR[5:0]), .Shamt(IR[10:6]), .rs(IR[25:21]),
    .rt(IR[20:16]), .rd(IR[15:11]), .Imm16(bit_extender_2_out), .Imm20(bit_extender_1_out));
  \单周期硬布线控制器  \u_单周期硬布线控制器_1  (
    .Func(IR[5:0]), .OP(IR[31:26]), .ALU_OP(ALUOp), .ALUB_src(ALUB_src), .RegA3(Jump), .RegD_src(REGD_src),
    .Jump(REGA3_src), .Beq(beq), .Sign_Ext(Sign_ext), .RFwr(RFWr), .DMwr(DMWr), .NPCop(\单周期硬布线控制器_1_npcop ),
    .Zero(zero));
  Hex_Digit_Display hex_digit_display_8 (.value(LedData[3:0]));  // open: dp
  Multiplexer #(.select(1), .width(5), .disabled("Z"), .enable("false")) multiplexer_2 (
    .in0(IR[20:16]), .in1(IR[15:11]), .out(multiplexer_2_out), .sel(REGA3_src));
  assign bit_extender_3_out = {{16{1'b0}}, bit_extender_2_out};  // Bit_Extender bit_extender_3
  assign bit_extender_4_out = {{16{bit_extender_2_out[15]}}, bit_extender_2_out};  // Bit_Extender bit_extender_4
  MIPS_Regifile mips_regifile_1 (
    .Din(RDin), .Clk(CLK), .R1(mips_regifile_1_r1), .R2(MDin), .WE(RFWr), .W_num(multiplexer_2_out),
    .R1_num(IR[25:21]), .R2_num(IR[20:16]));
  Multiplexer #(.select(1), .width(32), .disabled("Z"), .enable("false")) multiplexer_3 (
    .in0(bit_extender_3_out), .in1(bit_extender_4_out), .out(multiplexer_3_out), .sel(Sign_ext));
  Counter #(.width(16), .max('hffff), .ongoal("wrap"), .trigger("rising"), .behavior("new")) counter_1 (
    .count(Go), .Q(\总周期数 ), .clk(CLK), .clr(Rst));  // open: load, D, carry, preset, down
  Multiplexer #(.select(1), .width(32), .disabled("Z"), .enable("false")) multiplexer_4 (
    .in0(MDin), .in1(multiplexer_3_out), .out(multiplexer_4_out), .sel(ALUB_src));
  MIPS_ALU mips_alu_1 (
    .X(mips_regifile_1_r1), .Y(multiplexer_4_out), .AluOP(ALUOp), .S(mips_alu_1_s), .ZF(zero));  // open: OF, UOF
  Multiplexer #(.select(2), .width(32), .disabled("Z"), .enable("false")) multiplexer_5 (
    .in0(mips_alu_1_s), .in1(LedData), .out(RDin), .sel(REGD_src));  // open: in2, in3
  RAM #(.addrWidth(10), .dataWidth(32), .bus("separate"), .Select("high")) ram_1 (
    .addr(mips_alu_1_s[11:2]), .din(MDin), .data(LedData), .str(DMWr), .clk(CLK), .ld(1'b1), .clr(Rst));  // open: sel

  // Other names for the same wires on the sheet: Funct[5:0] = IR[5:0]; Shamt[4:0] = IR[10:6]; rd[4:0] = IR[15:11];
  //   rt[4:0] = IR[20:16]; rs[4:0] = IR[25:21]; OP[5:0] = IR[31:26]

  // Notes on the sheet:
  //   总复位信号应将除ROM以外所有存储组件全部清零
  //   指令存储器
  //   数码管输出
  //   contents of rom_1 (hex, n*v repeats v):
  //   8c030000 34050001 34020001 20630001 2020 852020 a22820 a3082a 10200001 c000c05 ac040004 c000c0b
  //   数码管输出应该用寄存器锁存，否则显示数据只能一闪而过
  //   此连线不得改动
  //   此连线不得改动
  //   此连线不得改动
  //   为方便自动评测，需要输出PC，IR，寄存器文件写入端口RDin，内存写入端口MDin等信号
  //   数据存储器
endmodule

// 单周期硬布线控制器
module \单周期硬布线控制器  (
  input  [5:0] OP,
  input  [5:0] Func,
  input  Zero,
  output [2:0] ALU_OP,
  output ALUB_src,
  output RegA3,
  output [1:0] RegD_src,
  output Jump,
  output Beq,
  output Sign_Ext,
  output RFwr,
  output DMwr,
  output NPCop
);

  \运算控制信号自动生成器  \u_运算控制信号自动生成器_1  (
    .OP0(OP[0]), .OP1(OP[1]), .OP2(OP[2]), .OP3(OP[3]), .OP4(OP[4]), .OP5(OP[5]), .F0(Func[0]), .F1(Func[1]),
    .F2(Func[2]), .F3(Func[3]), .F4(Func[4]), .F5(Func[5]), .S0(ALU_OP[0]), .S1(ALU_OP[1]), .S2(ALU_OP[2]));
  \控制信号发生器  \u_控制信号发生器_1  (
    .OP0(OP[0]), .OP1(OP[1]), .OP2(OP[2]), .OP3(OP[3]), .OP4(OP[4]), .OP5(OP[5]), .F0(Func[0]), .F1(Func[1]),
    .F2(Func[2]), .F3(Func[3]), .F4(Func[4]), .F5(Func[5]), .in_13(Zero), .ALUB_src(ALUB_src),
    .RegA3_src(RegA3), .RegD_src(RegD_src), .Jump(Jump), .Beq(Beq), .SigneExt(Sign_Ext), .RFWrite(RFwr),
    .DMWr(DMwr), .NPcop_src(NPCop));

  // Other names for the same wires on the sheet: OP_CODE[5:0] = OP

  // Notes on the sheet:
  //   运算器控制器，根据指令生成运算器功能选择信号
endmodule

// 运算控制信号发射器
module \运算控制信号自动生成器  (
  input  OP0,
  input  OP1,
  input  OP2,
  input  OP3,
  input  OP4,
  input  OP5,
  input  F0,
  input  F1,
  input  F2,
  input  F3,
  input  F4,
  input  F5,
  output S0,
  output S1,
  output S2
);

  wire ADD, BEQ, comparator_7_eq, comparator_8_eq, comparator_9_eq, JAL, LW, RT, SLT, SUB, SW;

  Comparator #(.width(6), .mode("twosComplement")) comparator_1 (
    .a({OP5, OP4, OP3, OP2, {2{OP0}}}), .b(6'b100000), .eq(LW));  // open: gt, lt
  Comparator #(.width(6), .mode("twosComplement")) comparator_2 (
    .a({OP5, OP4, OP3, OP2, {2{OP0}}}), .b(6'b101011), .eq(SW));  // open: gt, lt
  Comparator #(.width(6), .mode("twosComplement")) comparator_3 (
    .a({OP5, OP4, OP3, OP2, {2{OP0}}}), .b(6'b001101), .eq(S1));  // open: gt, lt
  Comparator #(.width(6), .mode("twosComplement")) comparator_4 (
    .a({OP5, OP4, OP3, OP2, {2{OP0}}}), .b(6'b000100), .eq(BEQ));  // open: gt, lt
  Comparator #(.width(6), .mode("twosComplement")) comparator_5 (
    .a({OP5, OP4, OP3, OP2, {2{OP0}}}), .b(6'b000011), .eq(JAL));  // open: gt, lt
  Comparator #(.width(6), .mode("twosComplement")) comparator_6 (
    .a({OP5, OP4, OP3, OP2, {2{OP0}}}), .b({6{1'b0}}), .eq(RT));  // open: gt, lt
  Comparator #(.width(6), .mode("twosComplement")) comparator_7 (
    .a({F5, F4, F3, F2, F1, F0}), .b(6'b100000), .eq(comparator_7_eq));  // open: gt, lt
  Comparator #(.width(6), .mode("twosComplement")) comparator_8 (
    .a({F5, F4, F3, F2, F1, F0}), .b(6'b100010), .eq(comparator_8_eq));  // open: gt, lt
  Comparator #(.width(6), .mode("twosComplement")) comparator_9 (
    .a({F5, F4, F3, F2, F1, F0}), .b(6'b101010), .eq(comparator_9_eq));  // open: gt, lt
  or or_1 (S0, SUB, SLT, S1, BEQ);
  or or_2 (S2, BEQ, S1);
  and and_1 (ADD, RT, comparator_7_eq);
  and and_2 (SUB, RT, comparator_8_eq);
  and and_3 (SLT, RT, comparator_9_eq);

  assign OP1 = OP0;

  // Other names for the same wires on the sheet: ORI = S1
endmodule

// 控制信号发生器
module \控制信号发生器  (
  input  OP0,
  input  OP1,
  input  OP2,
  input  OP3,
  input  OP4,
  input  OP5,
  input  F0,
  input  F1,
  input  F2,
  input  F3,
  input  F4,
  input  F5,
  input  in_13,
  output ALUB_src,
  output RegA3_src,
  output [1:0] RegD_src,
  output Jump,
  output Beq,
  output SigneExt,
  output RFWrite,
  output DMWr,
  output NPcop_src
);

  wire ADD, BEQ_t, comparator_7_eq, comparator_8_eq, comparator_9_eq, LW, SUB;

  Comparator #(.width(6), .mode("twosComplement")) comparator_1 (
    .a({OP5, OP4, OP3, OP2, OP1, OP0}), .b(6'b100011), .eq(LW));  // open: gt, lt
  Comparator #(.width(6), .mode("twosComplement")) comparator_2 (
    .a({OP5, OP4, OP3, OP2, OP1, OP0}), .b(6'b101011), .eq(DMWr));  // open: gt, lt
  Comparator #(.width(6), .mode("twosComplement")) comparator_3 (
    .a({OP5, OP4, OP3, OP2, OP1, OP0}), .b(6'b001101), .eq(RegD_src[1]));  // open: gt, lt
  Comparator #(.width(6), .mode("twosComplement")) comparator_4 (
    .a({OP5, OP4, OP3, OP2, OP1, OP0}), .b(6'b000100), .eq(BEQ_t));  // open: gt, lt
  Comparator #(.width(6), .mode("twosComplement")) comparator_5 (
    .a({OP5, OP4, OP3, OP2, OP1, OP0}), .b(6'b000011), .eq(Jump));  // open: gt, lt
  Comparator #(.width(6), .mode("twosComplement")) comparator_6 (
    .a({OP5, OP4, OP3, OP2, OP1, OP0}), .b({6{1'b0}}), .eq(RegA3_src));  // open: gt, lt
  Comparator #(.width(6), .mode("twosComplement")) comparator_7 (
    .a({F5, F4, F3, F2, F1, F0}), .b(6'b100000), .eq(comparator_7_eq));  // open: gt, lt
  Comparator #(.width(6), .mode("twosComplement")) comparator_8 (
    .a({F5, F4, F3, F2, F1, F0}), .b(6'b100010), .eq(comparator_8_eq));  // open: gt, lt
  Comparator #(.width(6), .mode("twosComplement")) comparator_9 (
    .a({F5, F4, F3, F2, F1, F0}), .b(6'b101010), .eq(comparator_9_eq));  // open: gt, lt
  and and_1 (ADD, comparator_7_eq, RegA3_src);
  and and_2 (SUB, comparator_8_eq, RegA3_src);
  and and_3 (RegD_src[0], comparator_9_eq, RegA3_src);
  or or_1 (ALUB_src, DMWr, RegD_src[1], LW);
  and and_4 (Beq, BEQ_t, in_13);
  or or_2 (SigneExt, LW, DMWr, BEQ_t);
  or or_3 (RFWrite, RegD_src[1], LW, RegA3_src);

  assign NPcop_src = Jump;

  // Other names for the same wires on the sheet: JAL = Jump; SLT = RegD_src[0]; ORI = RegD_src[1]; RT = RegA3_src;
  //   SW = DMWr; ZERO = in_13
endmodule

// ALU
module MIPS_ALU (
  input  [31:0] X,
  input  [31:0] Y,
  input  [2:0] AluOP,
  output OF,
  output UOF,
  output ZF,
  output [31:0] S
);

  \_1_3_32位ALU  \u_1_3_32位alu_1  (.X(X), .Y(Y), .AluOp(AluOP), .S(S), .OF(OF), .UOF(UOF), .ZF(ZF));

  // Notes on the sheet:
  //   不要改变此引脚区域内容，也不要改变ALU封装形式
  //   输入引脚
endmodule

module MIPS_Regifile (
  input  [4:0] R1_num,
  input  [4:0] R2_num,
  input  [4:0] W_num,
  input  [31:0] Din,
  input  WE,
  input  Clk,
  output [31:0] R1,
  output [31:0] R2
);

  \_2_2__MIPS_RF模块  \u_2_2_mips_rf模块_1  (
    .RA1(R1_num), .RA2(R2_num), .WA(W_num), .Din(Din), .CLK(Clk), .WE(WE), .RD1(R1), .RD2(R2));
endmodule

module NPC (
  input  Zero,
  input  Jump,
  input  [31:0] Imm,
  input  Clk,
  input  Branch,
  input  RST,
  output [31:0] PC
);

  wire [1:0] undriven;
  wire [15:0] shifter_1_out;
  wire [31:0] adder_2_out, bit_extender_1_out, multiplexer_1_out, PC_4;

  Multiplexer #(.select(2), .width(32), .disabled("Z"), .enable("false")) multiplexer_1 (
    .in0(PC_4), .in1({PC_4[31:28], Imm[25:0], undriven}), .in2(adder_2_out), .out(multiplexer_1_out),
    .sel({Branch, Jump}));  // open: in3
  Register #(.width(32), .trigger("rising"), .Select("low")) register_1 (
    .D(multiplexer_1_out), .Q(PC), .clk(Clk), .clr(RST));  // open: en
  Shifter #(.width(16), .shift("ll")) shifter_1 (.in(Imm[15:0]), .\dist (4'b0010), .out(shifter_1_out));
  Adder #(.width(32)) adder_1 (.a(PC), .b(32'h4), .out(PC_4));  // open: cin, cout
  assign bit_extender_1_out = {{16{shifter_1_out[15]}}, shifter_1_out};  // Bit_Extender bit_extender_1
  Adder #(.width(32)) adder_2 (.a(bit_extender_1_out), .b(PC_4), .out(adder_2_out));  // open: cin, cout

  // Notes on the sheet:
  //   Branch: pull=down
  //   Jump: pull=down
  //   Clk: pull=down
  //   RST: pull=down
  //   Zero: pull=down
  //   Imm: pull=down
  //   输入信号
  //   输出信号
endmodule

module ID (
  input  [31:0] Instruction,
  output [5:0] OP,
  output [5:0] Funct,
  output [4:0] Shamt,
  output [4:0] rs,
  output [4:0] rt,
  output [4:0] rd,
  output [15:0] Imm16,
  output [25:0] Imm20
);


  assign Funct = Instruction[5:0];
  assign Imm16 = Instruction[15:0];
  assign Imm20 = Instruction[25:0];
  assign OP = Instruction[31:26];
  assign rd = Instruction[15:11];
  assign rs = Instruction[25:21];
  assign rt = Instruction[20:16];
  assign Shamt = Instruction[10:6];

  // Other names for the same wires on the sheet: Imm26[25:0] = Instruction[25:0]
endmodule
