// Logisim project ALU2021-KL0902方案2(1).circ as structural Verilog: 5 circuits, main circuit 1-1  8位加法器
module \_1_1__8位加法器  (
  input  [7:0] X,
  input  [7:0] Y,
  input  Cin,
  output [7:0] S,
  output Cout,
  output OF
);

  wire \n1位全加器_2_cout , \n1位全加器_3_cout , \n1位全加器_4_cout , \n1位全加器_5_cout , \n1位全加器_6_cout , \n1位全加器_7_cout ,
       \n1位全加器_8_cout ;

  xor xor_1 (OF, \n1位全加器_2_cout , Cout);
  \_1位全加器  \u_1位全加器_1  (.Cout(Cout), .Si(S[7]), .Cin(\n1位全加器_2_cout ), .Xi(X[7]), .Yi(Y[7]));
  \_1位全加器  \u_1位全加器_2  (.Cout(\n1位全加器_2_cout ), .Si(S[6]), .Cin(\n1位全加器_3_cout ), .Xi(X[6]), .Yi(Y[6]));
  \_1位全加器  \u_1位全加器_3  (.Cout(\n1位全加器_3_cout ), .Si(S[5]), .Cin(\n1位全加器_4_cout ), .Xi(X[5]), .Yi(Y[5]));
  \_1位全加器  \u_1位全加器_4  (.Cout(\n1位全加器_4_cout ), .Si(S[4]), .Cin(\n1位全加器_5_cout ), .Xi(X[4]), .Yi(Y[4]));
  // Probe on X
  // Probe on Y
  // Probe on S
  \_1位全加器  \u_1位全加器_5  (.Cout(\n1位全加器_5_cout ), .Si(S[3]), .Cin(\n1位全加器_6_cout ), .Xi(X[3]), .Yi(Y[3]));
  // Probe on X
  // Probe on Y
  // Probe on S
  \_1位全加器  \u_1位全加器_6  (.Cout(\n1位全加器_6_cout ), .Si(S[2]), .Cin(\n1位全加器_7_cout ), .Xi(X[2]), .Yi(Y[2]));
  \_1位全加器  \u_1位全加器_7  (.Cout(\n1位全加器_7_cout ), .Si(S[1]), .Cin(\n1位全加器_8_cout ), .Xi(X[1]), .Yi(Y[1]));
  \_1位全加器  \u_1位全加器_8  (.Cout(\n1位全加器_8_cout ), .Si(S[0]), .Cin(Cin), .Xi(X[0]), .Yi(Y[0]));

  // Notes on the sheet:
  //   输入引脚区
  //   注：不能增加任何输入输出端口信号
  //   （1）使用1位全加器FA实现8位加法器，给出溢出标志OF
  //   输出引脚区
  //   =
  //   有符号数
  //   （2）封装电路供后续实验使用
  //   =
  //   结果测试区
  //   无符号数
endmodule

// 加减
module \_1_2_32位可控加减器  (
  input  Sub,
  input  [31:0] X,
  input  [31:0] Y,
  output CF,
  output OF,
  output ZF,
  output SF,
  output [31:0] S
);

  wire \n1_1_8位加法器_1_cout , \n1_1_8位加法器_2_cout , \n1_1_8位加法器_3_cout , \n1_1_8位加法器_4_cout , not_1_out;
  wire [2:0] multiplexer_1_out, multiplexer_1_out_2, multiplexer_1_out_3;
  wire [7:0] xor_1_out, xor_2_out, xor_3_out, xor_4_out;
  wire [31:0] not_2_out;

  and and_1 (CF, \n1_1_8位加法器_1_cout , not_1_out);
  not not_1 (not_1_out, Sub);
  \_1_1__8位加法器  \u_1_1_8位加法器_1  (
    .X(X[31:24]), .Y(xor_1_out), .Cin(\n1_1_8位加法器_2_cout ), .S(S[31:24]), .Cout(\n1_1_8位加法器_1_cout ), .OF(OF));
  and and_2 (ZF, not_2_out[15], not_2_out[0], not_2_out[1], not_2_out[2], not_2_out[3], not_2_out[4], not_2_out[5], not_2_out[6], not_2_out[7], not_2_out[8], not_2_out[9], not_2_out[10], not_2_out[11], not_2_out[12], not_2_out[13], not_2_out[14], not_2_out[16], not_2_out[17], not_2_out[18], not_2_out[19], not_2_out[20], not_2_out[21], not_2_out[22], not_2_out[23], not_2_out[24], not_2_out[25], not_2_out[26], not_2_out[27], not_2_out[28], not_2_out[29], not_2_out[30], not_2_out[31]);
  assign xor_1_out = Y[31:24] ^ {8{Sub}};  // XOR_Gate xor_1, 8 bits wide
  // Probe on X
  // Probe on Y
  // Probe on S
  assign not_2_out = ~S;  // NOT_Gate not_2, 32 bits wide
  // Probe on X
  // Probe on Y
  // Probe on S
  \_1_1__8位加法器  \u_1_1_8位加法器_2  (
    .X(X[23:16]), .Y(xor_2_out), .Cin(\n1_1_8位加法器_3_cout ), .S(S[23:16]), .Cout(\n1_1_8位加法器_2_cout ));  // open: OF
  assign xor_2_out = Y[23:16] ^ {8{Sub}};  // XOR_Gate xor_2, 8 bits wide
  \_1_1__8位加法器  \u_1_1_8位加法器_3  (
    .X(X[15:8]), .Y(xor_3_out), .Cin(\n1_1_8位加法器_4_cout ), .S(S[15:8]), .Cout(\n1_1_8位加法器_3_cout ));  // open: OF
  assign xor_3_out = Y[15:8] ^ {8{Sub}};  // XOR_Gate xor_3, 8 bits wide
  DotMatrix #(.matrixcols(3), .matrixrows(3)) dotmatrix_1 (
    .col0(multiplexer_1_out_3), .col1(multiplexer_1_out_2), .col2(multiplexer_1_out));
  Multiplexer #(.width(9), .enable("false")) multiplexer_1 (
    .in0(9'hba), .in1(9'h92), .out({multiplexer_1_out_3, multiplexer_1_out_2, multiplexer_1_out}), .sel(Sub));
  \_1_1__8位加法器  \u_1_1_8位加法器_4  (
    .X(X[7:0]), .Y(xor_4_out), .Cin(Sub), .S(S[7:0]), .Cout(\n1_1_8位加法器_4_cout ));  // open: OF
  assign xor_4_out = Y[7:0] ^ {8{Sub}};  // XOR_Gate xor_4, 8 bits wide

  assign SF = S[31];

  // Other names for the same wires on the sheet: SUM = Sub

  // Notes on the sheet:
  //   加法进位标志
  //   输入引脚区
  //   注：不能增加任何输入输出端口信号
  //   用封装后的8位加法器构成32位加减可控运算器，并产生正确的标志位
  //   输出引脚区
  //   =
  //   有符号数
  //   =
  //   结果测试区
  //   无符号数
endmodule

module \_1_3_32位ALU  (
  input  [2:0] AluOp,
  input  [31:0] X,
  input  [31:0] Y,
  output OF,
  output UOF,
  output ZF,
  output [31:0] S
);

  wire and_2_out, and_3_out, and_4_out, and_5_out, comparator_1_lt, comparator_2_lt, comparator_3_eq,
       comparator_3_lt, \n1_2_32位可控加减器_1_cf , \n1_2_32位可控加减器_1_of , \n1_2_32位可控加减器_2_of ;
  wire [31:0] and_1_out, bit_extender_1_out, bit_extender_2_out, \n1_2_32位可控加减器_1_s , \n1_2_32位可控加减器_2_s ,
       not_1_out, or_1_out, xor_1_out;

  Comparator #(.width(32), .mode("unsigned")) comparator_1 (.a(X), .b(Y), .lt(comparator_1_lt));  // open: gt, eq
  \_1_2_32位可控加减器  \u_1_2_32位可控加减器_1  (
    .X(X), .Y(Y), .Sub(1'b0), .S(\n1_2_32位可控加减器_1_s ), .CF(\n1_2_32位可控加减器_1_cf ), .OF(\n1_2_32位可控加减器_1_of ));  // open: ZF, SF
  \_1_2_32位可控加减器  \u_1_2_32位可控加减器_2  (
    .X(X), .Y(Y), .Sub(1'b1), .S(\n1_2_32位可控加减器_2_s ), .OF(\n1_2_32位可控加减器_2_of ));  // open: CF, ZF, SF
  Comparator #(.width(32)) comparator_2 (.a(X), .b(Y), .lt(comparator_2_lt));  // open: gt, eq
  assign and_1_out = X & Y;  // AND_Gate and_1, 32 bits wide
  assign or_1_out = X | Y;  // OR_Gate or_1, 32 bits wide
  assign xor_1_out = X ^ Y;  // XOR_Gate xor_1, 32 bits wide
  assign not_1_out = ~Y;  // NOT_Gate not_1, 32 bits wide
  assign bit_extender_1_out = {{31{1'b0}}, comparator_2_lt};  // Bit_Extender bit_extender_1
  // Probe on X
  // Probe on Y
  // Probe on S
  // Probe on X
  // Probe on Y
  // Probe on S
  Multiplexer #(.select(3), .width(32), .enable("false")) multiplexer_1 (
    .in0(\n1_2_32位可控加减器_1_s ), .in1(\n1_2_32位可控加减器_2_s ), .in2(and_1_out), .in3(or_1_out), .in4(xor_1_out),
    .in5(Y), .in6(not_1_out), .in7(bit_extender_1_out), .out(S), .sel(AluOp));
  assign bit_extender_2_out = {{31{1'b0}}, 1'b0};  // Bit_Extender bit_extender_2
  Comparator #(.width(3), .mode("unsigned")) comparator_3 (
    .a(AluOp), .b(3'b001), .eq(comparator_3_eq), .lt(comparator_3_lt));  // open: gt
  Comparator #(.width(32)) comparator_4 (.a(bit_extender_2_out), .b(S), .eq(ZF));  // open: gt, lt
  and and_2 (and_2_out, comparator_3_lt, \n1_2_32位可控加减器_1_cf );
  and and_3 (and_3_out, comparator_1_lt, comparator_3_eq);
  and and_4 (and_4_out, \n1_2_32位可控加减器_2_of , comparator_3_eq);
  and and_5 (and_5_out, \n1_2_32位可控加减器_1_of , comparator_3_lt);
  or or_2 (UOF, and_2_out, and_3_out);
  or or_3 (OF, and_4_out, and_5_out);

  // Notes on the sheet:
  //   000 ：S=X+Y
  //   注：不能增加任何输入输出端口信号
  //   输入引脚区
  //   001：S=X-Y
  //   010 ：S=X&Y
  //   实现一个32位的ALU，可以由AluOP控制实现8种运算操作，并产生正确的标志位。AluOp与运算关系如下：
  //   011：S=X|Y
  //   输出引脚区
  //   比大小，进行无符号溢出的判断
  //   100 ：S=X^Y
  //   =
  //   101 ：S=Y
  //   有符号数
  //   =
  //   结果测试区
  //   110 ：S=~Y
  //   无符号数
  //   111 ：S=X<Y?1:0
  //   加运算
  //   减运算
  //   减运算
  //   加运算
  //   无符号的溢出
  //   有符号的溢出
endmodule

module \_1_4_补码一位乘法器  (
  input  [7:0] X,
  input  [7:0] Y,
  output [15:0] S
);

  wire en, multiplexer_2_out, not_1_out, not_2_out, or_1_out, Reset, s_t, Yn_1;
  wire [3:0] counter_1_q;
  wire [7:0] multiplexer_1_out, multiplexer_3_out, \n1_1_8位加法器_1_s , not_3_out;
  wire [7:7] \移位后的Y ;

  Clock clock_1 (.out(s_t));
  Multiplexer #(.width(8), .enable("false")) multiplexer_1 (
    .in0(Y), .in1({\移位后的Y [7], S[7:1]}), .out(multiplexer_1_out), .sel(or_1_out));
  or or_1 (or_1_out, counter_1_q[3], counter_1_q[2], counter_1_q[1], counter_1_q[0]);
  Counter #(.width(4), .max('h9), .ongoal("stay")) counter_1 (
    .Q(counter_1_q), .clk(s_t), .clr(Reset));  // open: load, D, count, carry
  Button \u_复位  (.out(Reset));
  // Probe on S[15:8]
  Register \u_Σ_2  (
    .D({{2{\n1_1_8位加法器_1_s [7]}}, \n1_1_8位加法器_1_s [5:0]}), .en(en), .Q(S[15:8]), .clk(s_t), .clr(Reset));
  Register u_Y (.D(multiplexer_1_out), .en(en), .Q(S[7:0]), .clk(s_t), .clr(Reset));
  \_1_1__8位加法器  \u_1_1_8位加法器_1  (
    .X(S[15:8]), .Y(multiplexer_3_out), .Cin(multiplexer_2_out),
    .S({\n1_1_8位加法器_1_s [7], \n1_1_8位加法器_1_s [5:0], \移位后的Y [7]}));  // open: Cout, OF
  not not_1 (not_1_out, counter_1_q[1]);
  not not_2 (not_2_out, counter_1_q[2]);
  // Probe on S[7:0]
  Register #(.width(1)) u_Yn_1 (.D(S[0]), .en(en), .Q(Yn_1), .clk(s_t), .clr(Reset));
  nand nand_1 (en, counter_1_q[0], not_1_out, not_2_out, counter_1_q[3]);
  // Probe on Yn_1
  Multiplexer #(.select(2), .enable("false")) multiplexer_2 (
    .in0(1'b0), .in1(1'b0), .in2(1'b1), .in3(1'b0), .out(multiplexer_2_out), .sel({S[0], Yn_1}));
  Multiplexer #(.select(2), .width(8), .enable("false")) multiplexer_3 (
    .in0({8{1'b0}}), .in1(X), .in2(not_3_out), .in3({8{1'b0}}), .out(multiplexer_3_out), .sel({S[0], Yn_1}));
  assign not_3_out = ~X;  // NOT_Gate not_3, 8 bits wide
  // Probe on X
  // Probe on Y
  // Probe on S

  // Other names for the same wires on the sheet: Yn = S[0]; 乘积[15:0] = S; M[7:0] = S[15:8]; 移位后的Y[6:0] = S[7:1]

  // Notes on the sheet:
  //   注：不能增加任何输入输出端口信号
  //   输入引脚区
  //   功能说明：补码一位乘法器，S=X×Y，要求采用Booth乘法实现，最终结果输出到乘积引脚上。
  //   算术右移1位
  //   输出引脚区
  //   =
  //   有符号数
  //   核心算法：｛∑，Y｝=｛∑，( Yn+1-Yn ) [X]    ,    Y }  / 2
  //   结果测试区
  //   补
endmodule

module \_1位全加器  (
  input  Cin,
  input  Xi,
  input  Yi,
  output Cout,
  output Si
);

  wire and_1_out, and_2_out, xor_2_out;

  and and_1 (and_1_out, Xi, Yi);
  or or_1 (Cout, and_1_out, and_2_out);
  and and_2 (and_2_out, Cin, xor_2_out);
  xor xor_1 (Si, Cin, xor_2_out);
  xor xor_2 (xor_2_out, Xi, Yi);
endmodule
