// Logisim project storage-Li.circ as structural Verilog: 3 circuits, main circuit 1-memexct
module _1_memexct (
  input  CLK,
  input  WE,
  input  [13:0] Address,
  input  [31:0] DataIn,
  input  \模式选择 ,
  output [31:0] DataOut
);

  wire button_1_out, clock_1_out, decoder_1_out0, decoder_1_out1, decoder_1_out2, decoder_1_out3,
       multiplexer_3_out, not_1_out, not_2_out, not_3_out, not_4_out, not_5_out;
  wire [7:0] multiplexer_2_out_2;
  wire [13:0] adder_1_out, multiplexer_1_out;
  wire [23:0] multiplexer_2_out;
  wire [31:0] adder_2_out, counter_1_q;

  Counter #(.width(32), .max('hb), .ongoal("stay"), .trigger("rising"), .behavior("new")) counter_1 (
    .Q(counter_1_q), .clk(clock_1_out), .clr(button_1_out));  // open: load, D, count, carry, preset, down
  Clock #(.highDuration(1), .lowDuration(1)) clock_1 (.out(clock_1_out));
  Button button_1 (.out(button_1_out));
  Adder #(.width(14)) adder_1 (.a(Address), .b(counter_1_q[13:0]), .out(adder_1_out));  // open: cin, cout
  Adder #(.width(32)) adder_2 (.a(counter_1_q), .b(DataIn), .out(adder_2_out));  // open: cin, cout
  Multiplexer #(.select(1), .width(14), .disabled("Z"), .enable("false")) multiplexer_1 (
    .in0(Address), .in1(adder_1_out), .out(multiplexer_1_out), .sel(\模式选择 ));
  Decoder #(.select(2), .tristate("false"), .disabled(0), .enable("false")) decoder_1 (
    .out0(decoder_1_out0), .out1(decoder_1_out1), .out2(decoder_1_out2), .out3(decoder_1_out3),
    .sel(multiplexer_1_out[13:12]));
  Multiplexer #(.select(1), .width(32), .disabled("Z"), .enable("false")) multiplexer_2 (
    .in0(DataIn), .in1(adder_2_out), .out({multiplexer_2_out_2, multiplexer_2_out}), .sel(\模式选择 ));
  Multiplexer #(.select(1), .width(1), .disabled("Z"), .enable("false")) multiplexer_3 (
    .in0(CLK), .in1(clock_1_out), .out(multiplexer_3_out), .sel(\模式选择 ));
  not not_1 (not_1_out, decoder_1_out0);
  not not_2 (not_2_out, decoder_1_out1);
  not not_3 (not_3_out, decoder_1_out2);
  not not_4 (not_4_out, decoder_1_out3);
  RAM #(.addrWidth(12), .dataWidth(8), .bus("separate"), .Select("low")) ram_1 (
    .addr(multiplexer_1_out[11:0]), .din(multiplexer_2_out[7:0]), .data(DataOut[7:0]), .str(WE),
    .sel(not_1_out), .clk(multiplexer_3_out), .ld(not_5_out));  // open: clr
  RAM #(.addrWidth(12), .dataWidth(8), .bus("separate"), .Select("low")) ram_2 (
    .addr(multiplexer_1_out[11:0]), .din(multiplexer_2_out[7:0]), .data(DataOut[7:0]), .str(WE),
    .sel(not_2_out), .clk(multiplexer_3_out), .ld(not_5_out));  // open: clr
  RAM #(.addrWidth(12), .dataWidth(8), .bus("separate"), .Select("low")) ram_3 (
    .addr(multiplexer_1_out[11:0]), .din(multiplexer_2_out[7:0]), .data(DataOut[7:0]), .str(WE),
    .sel(not_3_out), .clk(multiplexer_3_out), .ld(not_5_out));  // open: clr
  RAM #(.addrWidth(12), .dataWidth(8), .bus("separate"), .Select("low")) ram_4 (
    .addr(multiplexer_1_out[11:0]), .din(multiplexer_2_out[7:0]), .data(DataOut[7:0]), .str(WE),
    .sel(not_4_out), .clk(multiplexer_3_out), .ld(not_5_out));  // open: clr
  // Probe on Address
  // Probe on DataOut
  RAM #(.addrWidth(12), .dataWidth(8), .bus("separate"), .Select("low")) ram_5 (
    .addr(multiplexer_1_out[11:0]), .din(multiplexer_2_out[15:8]), .data(DataOut[15:8]), .str(WE),
    .sel(not_1_out), .clk(multiplexer_3_out), .ld(not_5_out));  // open: clr
  RAM #(.addrWidth(12), .dataWidth(8), .bus("separate"), .Select("low")) ram_6 (
    .addr(multiplexer_1_out[11:0]), .din(multiplexer_2_out[15:8]), .data(DataOut[15:8]), .str(WE),
    .sel(not_2_out), .clk(multiplexer_3_out), .ld(not_5_out));  // open: clr
  RAM #(.addrWidth(12), .dataWidth(8), .bus("separate"), .Select("low")) ram_7 (
    .addr(multiplexer_1_out[11:0]), .din(multiplexer_2_out[15:8]), .data(DataOut[15:8]), .str(WE),
    .sel(not_3_out), .clk(multiplexer_3_out), .ld(not_5_out));  // open: clr
  RAM #(.addrWidth(12), .dataWidth(8), .bus("separate"), .Select("low")) ram_8 (
    .addr(multiplexer_1_out[11:0]), .din(multiplexer_2_out[15:8]), .data(DataOut[15:8]), .str(WE),
    .sel(not_4_out), .clk(multiplexer_3_out), .ld(not_5_out));  // open: clr
  RAM #(.addrWidth(12), .dataWidth(8), .bus("separate"), .Select("low")) ram_9 (
    .addr(multiplexer_1_out[11:0]), .din(multiplexer_2_out[23:16]), .data(DataOut[23:16]), .str(WE),
    .sel(not_1_out), .clk(multiplexer_3_out), .ld(not_5_out));  // open: clr
  RAM #(.addrWidth(12), .dataWidth(8), .bus("separate"), .Select("low")) ram_10 (
    .addr(multiplexer_1_out[11:0]), .din(multiplexer_2_out[23:16]), .data(DataOut[23:16]), .str(WE),
    .sel(not_2_out), .clk(multiplexer_3_out), .ld(not_5_out));  // open: clr
  RAM #(.addrWidth(12), .dataWidth(8), .bus("separate"), .Select("low")) ram_11 (
    .addr(multiplexer_1_out[11:0]), .din(multiplexer_2_out[23:16]), .data(DataOut[23:16]), .str(WE),
    .sel(not_3_out), .clk(multiplexer_3_out), .ld(not_5_out));  // open: clr
  RAM #(.addrWidth(12), .dataWidth(8), .bus("separate"), .Select("low")) ram_12 (
    .addr(multiplexer_1_out[11:0]), .din(multiplexer_2_out[23:16]), .data(DataOut[23:16]), .str(WE),
    .sel(not_4_out), .clk(multiplexer_3_out), .ld(not_5_out));  // open: clr
  RAM #(.addrWidth(12), .dataWidth(8), .bus("separate"), .Select("low")) ram_13 (
    .addr(multiplexer_1_out[11:0]), .din(multiplexer_2_out_2), .data(DataOut[31:24]), .str(WE),
    .sel(not_1_out), .clk(multiplexer_3_out), .ld(not_5_out));  // open: clr
  not not_5 (not_5_out, WE);
  RAM #(.addrWidth(12), .dataWidth(8), .bus("separate"), .Select("low")) ram_14 (
    .addr(multiplexer_1_out[11:0]), .din(multiplexer_2_out_2), .data(DataOut[31:24]), .str(WE),
    .sel(not_2_out), .clk(multiplexer_3_out), .ld(not_5_out));  // open: clr
  RAM #(.addrWidth(12), .dataWidth(8), .bus("separate"), .Select("low")) ram_15 (
    .addr(multiplexer_1_out[11:0]), .din(multiplexer_2_out_2), .data(DataOut[31:24]), .str(WE),
    .sel(not_3_out), .clk(multiplexer_3_out), .ld(not_5_out));  // open: clr
  RAM #(.addrWidth(12), .dataWidth(8), .bus("separate"), .Select("low")) ram_16 (
    .addr(multiplexer_1_out[11:0]), .din(multiplexer_2_out_2), .data(DataOut[31:24]), .str(WE),
    .sel(not_4_out), .clk(multiplexer_3_out), .ld(not_5_out));  // open: clr

  // Other names for the same wires on the sheet: Addr[13:0] = Address; Di[31:0] = DataIn; Do[31:0] = DataOut

  // Notes on the sheet:
  //   用4K*8b的存储芯片扩展构成16K*32b的存储器。
  //   输入引脚区
  //   禁止修改上边的输入输出引脚，请使用隧道连接。
  //   输出引脚区
  //   存储芯片sel为使能端，低有效；str为写入控制，高有效；ld为读出控制，高有效。
  //   存储芯片数据输入和输出使用分离的数据引脚。
  //   输出数据测试区
  //   十六进制输出
endmodule

// RA1
module _2_MIPS_Regfile (
  input  [4:0] RA1,
  input  [31:0] Data_In,
  input  [4:0] RA2,
  input  [4:0] WA,
  input  Clock,
  input  Wite_Enable,
  output [31:0] Reg1Out,
  output [31:0] Reg2Out
);

  wire decoder_1_out0, decoder_1_out1, decoder_1_out2, decoder_1_out3, decoder_1_out4, decoder_1_out5,
       decoder_1_out6, decoder_1_out7, decoder_1_out8, decoder_1_out9, decoder_1_out10, decoder_1_out11,
       decoder_1_out12, decoder_1_out13, decoder_1_out14, decoder_1_out15, decoder_1_out16, decoder_1_out17,
       decoder_1_out18, decoder_1_out19, decoder_1_out20, decoder_1_out21, decoder_1_out22, decoder_1_out23,
       decoder_1_out25, decoder_1_out26, decoder_1_out27, decoder_1_out28, decoder_1_out29, decoder_1_out30,
       decoder_1_out31, undriven;
  wire [31:0] register_1_q, register_2_q, register_3_q, register_4_q, register_5_q, register_6_q,
       register_7_q, register_8_q, register_9_q, register_10_q, register_11_q, register_12_q, register_13_q,
       register_14_q, register_15_q, register_16_q, register_17_q, register_18_q, register_19_q,
       register_20_q, register_21_q, register_22_q, register_23_q, register_24_q, register_25_q,
       register_26_q, register_27_q, register_28_q, register_29_q, register_30_q, register_31_q,
       register_32_q;

  Decoder #(.select(5), .tristate("false"), .disabled(0), .enable("true")) decoder_1 (
    .out0(decoder_1_out0), .out1(decoder_1_out1), .out2(decoder_1_out2), .out3(decoder_1_out3),
    .out4(decoder_1_out4), .out5(decoder_1_out5), .out6(decoder_1_out6), .out7(decoder_1_out7),
    .out8(decoder_1_out8), .out9(decoder_1_out9), .out10(decoder_1_out10), .out11(decoder_1_out11),
    .out12(decoder_1_out12), .out13(decoder_1_out13), .out14(decoder_1_out14), .out15(decoder_1_out15),
    .out16(decoder_1_out16), .out17(decoder_1_out17), .out18(decoder_1_out18), .out19(decoder_1_out19),
    .out20(decoder_1_out20), .out21(decoder_1_out21), .out22(decoder_1_out22), .out23(decoder_1_out23),
    .out24(decoder_1_out23), .out25(decoder_1_out25), .out26(decoder_1_out26), .out27(decoder_1_out27),
    .out28(decoder_1_out28), .out29(decoder_1_out29), .out30(decoder_1_out30), .out31(decoder_1_out31),
    .sel(WA), .en(Wite_Enable));
  Register #(.width(32), .trigger("rising"), .Select("low")) register_1 (
    .D({32{1'b0}}), .en(decoder_1_out0), .Q(register_1_q), .clk(Clock), .cs(1'b0));  // open: clr, preset
  Register #(.width(32), .trigger("rising"), .Select("low")) register_2 (
    .D(Data_In), .en(decoder_1_out2), .Q(register_2_q), .clk(Clock), .cs(1'b0));  // open: clr, preset
  Register #(.width(32), .trigger("rising"), .Select("low")) register_3 (
    .D(Data_In), .en(decoder_1_out4), .Q(register_3_q), .clk(Clock), .cs(1'b0));  // open: clr, preset
  Register #(.width(32), .trigger("rising"), .Select("low")) register_4 (
    .D(Data_In), .en(decoder_1_out6), .Q(register_4_q), .clk(Clock), .cs(1'b0));  // open: clr, preset
  Register #(.width(32), .trigger("rising"), .Select("low")) register_5 (
    .D(Data_In), .en(decoder_1_out8), .Q(register_5_q), .clk(Clock), .cs(1'b0));  // open: clr, preset
  Register #(.width(32), .trigger("rising"), .Select("low")) register_6 (
    .D(Data_In), .en(decoder_1_out10), .Q(register_6_q), .clk(Clock), .cs(1'b0));  // open: clr, preset
  Register #(.width(32), .trigger("rising"), .Select("low")) register_7 (
    .D(Data_In), .en(decoder_1_out12), .Q(register_7_q), .clk(Clock), .cs(1'b0));  // open: clr, preset
  Register #(.width(32), .trigger("rising"), .Select("low")) register_8 (
    .D(Data_In), .en(decoder_1_out14), .Q(register_8_q), .clk(Clock), .cs(1'b0));  // open: clr, preset
  Register #(.width(32), .trigger("rising"), .Select("low")) register_9 (
    .D(Data_In), .en(decoder_1_out16), .Q(register_9_q), .clk(Clock), .cs(1'b0));  // open: clr, preset
  Register #(.width(32), .trigger("rising"), .Select("low")) register_10 (
    .D(Data_In), .en(decoder_1_out18), .Q(register_10_q), .clk(Clock), .cs(1'b0));  // open: clr, preset
  Register #(.width(32), .trigger("rising"), .Select("low")) register_11 (
    .D(Data_In), .en(decoder_1_out20), .Q(register_11_q), .clk(Clock), .cs(1'b0));  // open: clr, preset
  Register #(.width(32), .trigger("rising"), .Select("low")) register_12 (
    .D(Data_In), .en(decoder_1_out22), .Q(register_12_q), .clk(Clock), .cs(1'b0));  // open: clr, preset
  Register #(.width(32), .trigger("rising"), .Select("low")) register_13 (
    .D(Data_In), .en(decoder_1_out23), .Q(register_13_q), .clk(Clock), .cs(1'b0));  // open: clr, preset
  Register #(.width(32), .trigger("rising"), .Select("low")) register_14 (
    .D(Data_In), .en(decoder_1_out26), .Q(register_14_q), .clk(Clock), .cs(1'b0));  // open: clr, preset
  Register #(.width(32), .trigger("rising"), .Select("low")) register_15 (
    .D(Data_In), .en(decoder_1_out28), .Q(register_15_q), .clk(Clock), .cs(1'b0));  // open: clr, preset
  Register #(.width(32), .trigger("rising"), .Select("low")) register_16 (
    .D(Data_In), .en(decoder_1_out30), .Q(register_16_q), .clk(Clock), .cs(1'b0));  // open: clr, preset
  Register #(.width(32), .trigger("rising"), .Select("low")) register_17 (
    .D(Data_In), .en(decoder_1_out1), .Q(register_17_q), .clk(Clock), .cs(1'b0));  // open: clr, preset
  Register #(.width(32), .trigger("rising"), .Select("low")) register_18 (
    .D(Data_In), .en(decoder_1_out3), .Q(register_18_q), .clk(Clock), .cs(1'b0));  // open: clr, preset
  Register #(.width(32), .trigger("rising"), .Select("low")) register_19 (
    .D(Data_In), .en(decoder_1_out5), .Q(register_19_q), .clk(Clock), .cs(1'b0));  // open: clr, preset
  Register #(.width(32), .trigger("rising"), .Select("low")) register_20 (
    .D(Data_In), .en(decoder_1_out7), .Q(register_20_q), .clk(Clock), .cs(1'b0));  // open: clr, preset
  Register #(.width(32), .trigger("rising"), .Select("low")) register_21 (
    .D(Data_In), .en(decoder_1_out9), .Q(register_21_q), .clk(Clock), .cs(1'b0));  // open: clr, preset
  Register #(.width(32), .trigger("rising"), .Select("low")) register_22 (
    .D(Data_In), .en(decoder_1_out11), .Q(register_22_q), .clk(Clock), .cs(1'b0));  // open: clr, preset
  Register #(.width(32), .trigger("rising"), .Select("low")) register_23 (
    .D(Data_In), .en(decoder_1_out13), .Q(register_23_q), .clk(Clock), .cs(1'b0));  // open: clr, preset
  Register #(.width(32), .trigger("rising"), .Select("low")) register_24 (
    .D(Data_In), .en(decoder_1_out15), .Q(register_24_q), .clk(Clock), .cs(1'b0));  // open: clr, preset
  Register #(.width(32), .trigger("rising"), .Select("low")) register_25 (
    .D(Data_In), .en(decoder_1_out17), .Q(register_25_q), .clk(Clock), .cs(1'b0));  // open: clr, preset
  Register #(.width(32), .trigger("rising"), .Select("low")) register_26 (
    .D(Data_In), .en(decoder_1_out19), .Q(register_26_q), .clk(Clock), .cs(1'b0));  // open: clr, preset
  Register #(.width(32), .trigger("rising"), .Select("low")) register_27 (
    .D(Data_In), .en(decoder_1_out21), .Q(register_27_q), .clk(Clock), .cs(1'b0), .preset(undriven));  // open: clr
  Register #(.width(32), .trigger("rising"), .Select("low")) register_28 (
    .D(Data_In), .en(decoder_1_out23), .Q(register_28_q), .clk(Clock), .cs(1'b0));  // open: clr, preset
  Register #(.width(32), .trigger("rising"), .Select("low")) register_29 (
    .D(Data_In), .en(decoder_1_out25), .Q(register_29_q), .clk(Clock), .cs(1'b0));  // open: clr, preset
  Register #(.width(32), .trigger("rising"), .Select("low")) register_30 (
    .D(Data_In), .en(decoder_1_out27), .Q(register_30_q), .clk(Clock), .cs(1'b0));  // open: clr, preset
  Register #(.width(32), .trigger("rising"), .Select("low")) register_31 (
    .D(Data_In), .en(decoder_1_out29), .Q(register_31_q), .clk(Clock), .cs(1'b0));  // open: clr, preset
  Register #(.width(32), .trigger("rising"), .Select("low")) register_32 (
    .D(Data_In), .en(decoder_1_out31), .Q(register_32_q), .clk(Clock), .cs(1'b0));  // open: clr, preset
  Multiplexer #(.select(5), .width(32), .disabled("Z"), .enable("false")) multiplexer_1 (
    .in0(register_1_q), .in1(register_17_q), .in2(register_2_q), .in3(register_18_q), .in4(register_3_q),
    .in5(register_19_q), .in6(register_4_q), .in7(register_20_q), .in8(register_5_q), .in9(register_21_q),
    .in10(register_6_q), .in11(register_22_q), .in12(register_7_q), .in13(register_23_q),
    .in14(register_8_q), .in15(register_24_q), .in16(register_9_q), .in17(register_25_q),
    .in18(register_10_q), .in19(register_26_q), .in20(register_11_q), .in21(register_27_q),
    .in22(register_12_q), .in23(register_28_q), .in24(register_13_q), .in25(register_29_q),
    .in26(register_14_q), .in27(register_30_q), .in28(register_15_q), .in29(register_31_q),
    .in30(register_16_q), .in31(register_32_q), .out(Reg1Out), .sel(RA1));
  Multiplexer #(.select(5), .width(32), .disabled("Z"), .enable("false")) multiplexer_2 (
    .in0(register_1_q), .in1(register_17_q), .in2(register_2_q), .in3(register_18_q), .in4(register_3_q),
    .in5(register_19_q), .in6(register_4_q), .in7(register_20_q), .in8(register_5_q), .in9(register_21_q),
    .in10(register_6_q), .in11(register_22_q), .in12(register_7_q), .in13(register_23_q),
    .in14(register_8_q), .in15(register_24_q), .in16(register_9_q), .in17(register_25_q),
    .in18(register_10_q), .in19(register_26_q), .in20(register_11_q), .in21(register_27_q),
    .in22(register_12_q), .in23(register_28_q), .in24(register_13_q), .in25(register_29_q),
    .in26(register_14_q), .in27(register_30_q), .in28(register_15_q), .in29(register_31_q),
    .in30(register_16_q), .in31(register_32_q), .out(Reg2Out), .sel(RA2));

  // Other names for the same wires on the sheet: CLK = Clock; Din[31:0] = Data_In; RD1[31:0] = Reg1Out;
  //   RD2[31:0] = Reg2Out; WE = Wite_Enable

  // Notes on the sheet:
  //   输入引脚
  //   输出引脚
  //   实现MIPS 32个通用寄存器
  //   RA1是读出寄存器地址1，RD1是地址1读出的数据。
  //   RA2是读出寄存器地址2，RD2是地址2读出的数据。
  //   WA、WE、CLK、Din是写入地址、命令、时钟、数据
  //   注意：0号寄存器的内容要求始终为全0。
  //   注意不要修改输入输出引脚与封装，请使用隧道连接。
endmodule

module _3_MIPS_RegAndMem (
  input  LA1,
  input  CLK,
  input  [1:0] RWSel,
  input  LA2,
  input  RFWr,
  input  [31:0] Din,
  input  LWA,
  input  [2:0] AluOp,
  input  [1:0] DispSel,
  input  AluYSel,
  input  DMWr,
  output [31:0] display
);

  wire [4:0] register_1_q, register_2_q, register_3_q;
  wire [31:0] multiplexer_1_out, multiplexer_2_out, \n1_3_32位alu_1_s , n1_memexct_1_dataout,
       n2_mips_regfile_1_reg1out, n2_mips_regfile_1_reg2out;

  // Probe on Din[4:0]
  Register #(.width(5), .trigger("rising"), .Select("low")) register_1 (
    .D(Din[4:0]), .en(LA1), .Q(register_1_q), .clk(CLK));  // open: clr
  Register #(.width(5), .trigger("rising"), .Select("low")) register_2 (
    .D(Din[4:0]), .en(LA2), .Q(register_2_q), .clk(CLK));  // open: clr
  Register #(.width(5), .trigger("rising"), .Select("low")) register_3 (
    .D(Din[4:0]), .en(LWA), .Q(register_3_q), .clk(CLK));  // open: clr
  _2_MIPS_Regfile u_2_mips_regfile_1 (
    .RA1(register_1_q), .Data_In(multiplexer_2_out), .RA2(register_2_q), .WA(register_3_q), .Clock(CLK),
    .Wite_Enable(RFWr), .Reg1Out(n2_mips_regfile_1_reg1out), .Reg2Out(n2_mips_regfile_1_reg2out));
  Multiplexer #(.select(1), .width(32), .disabled("Z"), .enable("false")) multiplexer_1 (
    .in0(n2_mips_regfile_1_reg2out), .in1(Din), .out(multiplexer_1_out), .sel(AluYSel));
  Multiplexer #(.select(2), .width(32), .disabled("Z"), .enable("false")) multiplexer_2 (
    .in0(Din), .in1(\n1_3_32位alu_1_s ), .in2(n1_memexct_1_dataout), .in3({32{1'b0}}),
    .out(multiplexer_2_out), .sel(RWSel));
  \_1_3_32位ALU  \u_1_3_32位alu_1  (
    .X(n2_mips_regfile_1_reg1out), .Y(multiplexer_1_out), .AluOp(AluOp), .S(\n1_3_32位alu_1_s ));  // open: OF, UOF, ZF
  _1_memexct u_1_memexct_1 (
    .DataIn(n2_mips_regfile_1_reg2out), .Address(\n1_3_32位alu_1_s [13:0]), .CLK(CLK), .WE(DMWr),
    .DataOut(n1_memexct_1_dataout), .\模式选择 (1'b0));
  Hex_Digit_Display hex_digit_display_1 (.value(display[15:12]));  // open: dp
  Hex_Digit_Display hex_digit_display_2 (.value(display[11:8]));  // open: dp
  Hex_Digit_Display hex_digit_display_3 (.value(display[27:24]));  // open: dp
  Hex_Digit_Display hex_digit_display_4 (.value(display[31:28]));  // open: dp
  Hex_Digit_Display hex_digit_display_5 (.value(display[3:0]));  // open: dp
  Hex_Digit_Display hex_digit_display_6 (.value(display[7:4]));  // open: dp
  Hex_Digit_Display hex_digit_display_7 (.value(display[23:20]));  // open: dp
  Hex_Digit_Display hex_digit_display_8 (.value(display[19:16]));  // open: dp
  Multiplexer #(.select(2), .width(32), .disabled("Z"), .enable("false")) multiplexer_3 (
    .in0(n2_mips_regfile_1_reg1out), .in1(n2_mips_regfile_1_reg2out), .in2(\n1_3_32位alu_1_s ),
    .in3(n1_memexct_1_dataout), .out(display), .sel(DispSel));

  // Other names for the same wires on the sheet: Disp[31:0] = display

  // Notes on the sheet:
  //   地址总线
  //   输入引脚区
  //   输出引脚区
  //   输出数据测试区
endmodule
