// Logisim project TTL74161.circ as structural Verilog: 1 circuit, main circuit TTL74161
module TTL74161 (
  input  CTT,
  input  CTP,
  input  LD_n,
  input  [3:0] D,
  input  CP,
  input  CR_n,
  output [3:0] out_7,
  output CO
);

  wire and_1_out, not_1_out, not_2_out;

  and and_1 (and_1_out, CTT, CTP);
  not not_1 (not_1_out, LD_n);
  not not_2 (not_2_out, CR_n);
  Counter #(.width(4), .max('hf), .ongoal("wrap"), .trigger("rising"), .behavior("new")) counter_1 (
    .load(not_1_out), .D(D), .count(and_1_out), .Q(out_7), .carry(CO), .clk(CP), .clr(not_2_out),
    .preset(1'b0));  // open: down
endmodule
