// Logisim project counter.circ as structural Verilog: 1 circuit, main circuit main
module main (
  input  in_1,
  input  [3:0] in_2,
  input  LDn,
  input  CRn,
  output out_5
);

  wire clock_1_out, nand_1_out;
  wire [3:0] ttl74161_1_out_7;

  Clock #(.highDuration(1), .lowDuration(1)) clock_1 (.out(clock_1_out));
  TTL74161 ttl74161_1 (
    .CTT(in_1), .CTP(in_1), .LD_n(LDn), .D(in_2), .CP(clock_1_out), .CR_n(nand_1_out),
    .out_7(ttl74161_1_out_7), .CO(out_5));
  nand nand_1 (nand_1_out, ttl74161_1_out_7[1], ttl74161_1_out_7[3]);
  Hex_Digit_Display hex_digit_display_1 (.value(ttl74161_1_out_7));  // open: dp
endmodule
