// Logisim project shiyan2.circ as structural Verilog: 5 circuits, main circuit 2-1  存储器扩展
module \_2_1__存储器扩展  (
  input  CLK,
  input  WE,
  input  [13:0] Addr,
  input  [31:0] Din,
  output [31:0] Dout
);

  wire decoder_1_out0, decoder_1_out1, decoder_1_out2, decoder_1_out3, not_1_out, not_2_out, not_3_out,
       not_4_out, not_5_out, or_1_out;

  not not_1 (not_1_out, WE);
  not not_2 (not_2_out, decoder_1_out0);
  not not_3 (not_3_out, decoder_1_out1);
  not not_4 (not_4_out, decoder_1_out2);
  not not_5 (not_5_out, decoder_1_out3);
  Decoder #(.select(2), .tristate("false"), .disabled("Z"), .enable("false")) decoder_1 (
    .out0(decoder_1_out0), .out1(decoder_1_out1), .out2(decoder_1_out2), .out3(decoder_1_out3),
    .sel(Addr[13:12]));
  or or_1 (or_1_out, not_1_out, WE);
  RAM #(.addrWidth(12), .dataWidth(8), .bus("separate"), .Select("low")) ram_1 (
    .addr(Addr[11:0]), .din(Din[7:0]), .data(Dout[7:0]), .str(not_1_out), .sel(not_5_out), .clk(CLK),
    .ld(or_1_out));  // open: clr
  RAM #(.addrWidth(12), .dataWidth(8), .bus("separate"), .Select("low")) ram_2 (
    .addr(Addr[11:0]), .din(Din[7:0]), .data(Dout[7:0]), .str(not_1_out), .sel(not_2_out), .clk(CLK),
    .ld(or_1_out));  // open: clr
  RAM #(.addrWidth(12), .dataWidth(8), .bus("separate"), .Select("low")) ram_3 (
    .addr(Addr[11:0]), .din(Din[7:0]), .data(Dout[7:0]), .str(not_1_out), .sel(not_3_out), .clk(CLK),
    .ld(or_1_out));  // open: clr
  RAM #(.addrWidth(12), .dataWidth(8), .bus("separate"), .Select("low")) ram_4 (
    .addr(Addr[11:0]), .din(Din[7:0]), .data(Dout[7:0]), .str(not_1_out), .sel(not_4_out), .clk(CLK),
    .ld(or_1_out));  // open: clr
  RAM #(.addrWidth(12), .dataWidth(8), .bus("separate"), .Select("low")) ram_5 (
    .addr(Addr[11:0]), .din(Din[15:8]), .data(Dout[15:8]), .str(not_1_out), .sel(not_2_out), .clk(CLK),
    .ld(or_1_out));  // open: clr
  Hex_Digit_Display hex_digit_display_1 (.value(Dout[15:12]));  // open: dp
  Hex_Digit_Display hex_digit_display_2 (.value(Dout[31:28]));  // open: dp
  RAM #(.addrWidth(12), .dataWidth(8), .bus("separate"), .Select("low")) ram_6 (
    .addr(Addr[11:0]), .din(Din[15:8]), .data(Dout[15:8]), .str(not_1_out), .sel(not_3_out), .clk(CLK),
    .ld(or_1_out));  // open: clr
  RAM #(.addrWidth(12), .dataWidth(8), .bus("separate"), .Select("low")) ram_7 (
    .addr(Addr[11:0]), .din(Din[15:8]), .data(Dout[15:8]), .str(not_1_out), .sel(not_4_out), .clk(CLK),
    .ld(or_1_out));  // open: clr
  RAM #(.addrWidth(12), .dataWidth(8), .bus("separate"), .Select("low")) ram_8 (
    .addr(Addr[11:0]), .din(Din[15:8]), .data(Dout[15:8]), .str(not_1_out), .sel(not_5_out), .clk(CLK),
    .ld(or_1_out));  // open: clr
  Hex_Digit_Display hex_digit_display_3 (.value(Dout[11:8]));  // open: dp
  Hex_Digit_Display hex_digit_display_4 (.value(Dout[7:4]));  // open: dp
  Hex_Digit_Display hex_digit_display_5 (.value(Dout[27:24]));  // open: dp
  Hex_Digit_Display hex_digit_display_6 (.value(Dout[23:20]));  // open: dp
  Hex_Digit_Display hex_digit_display_7 (.value(Dout[3:0]));  // open: dp
  Hex_Digit_Display hex_digit_display_8 (.value(Dout[19:16]));  // open: dp
  RAM #(.addrWidth(12), .dataWidth(8), .bus("separate"), .Select("low")) ram_9 (
    .addr(Addr[11:0]), .din(Din[23:16]), .data(Dout[23:16]), .str(not_1_out), .sel(not_2_out), .clk(CLK),
    .ld(or_1_out));  // open: clr
  RAM #(.addrWidth(12), .dataWidth(8), .bus("separate"), .Select("low")) ram_10 (
    .addr(Addr[11:0]), .din(Din[23:16]), .data(Dout[23:16]), .str(not_1_out), .sel(not_3_out), .clk(CLK),
    .ld(or_1_out));  // open: clr
  RAM #(.addrWidth(12), .dataWidth(8), .bus("separate"), .Select("low")) ram_11 (
    .addr(Addr[11:0]), .din(Din[23:16]), .data(Dout[23:16]), .str(not_1_out), .sel(not_4_out), .clk(CLK),
    .ld(or_1_out));  // open: clr
  RAM #(.addrWidth(12), .dataWidth(8), .bus("separate"), .Select("low")) ram_12 (
    .addr(Addr[11:0]), .din(Din[23:16]), .data(Dout[23:16]), .str(not_1_out), .sel(not_5_out), .clk(CLK),
    .ld(or_1_out));  // open: clr
  RAM #(.addrWidth(12), .dataWidth(8), .bus("separate"), .Select("low")) ram_13 (
    .addr(Addr[11:0]), .din(Din[31:24]), .data(Dout[31:24]), .str(not_1_out), .sel(not_2_out), .clk(CLK),
    .ld(or_1_out));  // open: clr
  RAM #(.addrWidth(12), .dataWidth(8), .bus("separate"), .Select("low")) ram_14 (
    .addr(Addr[11:0]), .din(Din[31:24]), .data(Dout[31:24]), .str(not_1_out), .sel(not_3_out), .clk(CLK),
    .ld(or_1_out));  // open: clr
  RAM #(.addrWidth(12), .dataWidth(8), .bus("separate"), .Select("low")) ram_15 (
    .addr(Addr[11:0]), .din(Din[31:24]), .data(Dout[31:24]), .str(not_1_out), .sel(not_5_out), .clk(CLK),
    .ld(or_1_out));  // open: clr
  RAM #(.addrWidth(12), .dataWidth(8), .bus("separate"), .Select("low")) ram_16 (
    .addr(Addr[11:0]), .din(Din[31:24]), .data(Dout[31:24]), .str(not_1_out), .sel(not_4_out), .clk(CLK),
    .ld(or_1_out));  // open: clr

  // Notes on the sheet:
  //   注：不能增加任何输入输出端口信号
  //   输入引脚区
  //   输出引脚区
  //   请用4K×8的存储芯片实现16K×32的存储器，并搭建外围电路，自动实现对存储器的读写操作
  //   RAM 4K×8
  //   输出数据测试区
endmodule

module \_2_1测试  (
  input  CLK,
  input  WE,
  input  [13:0] Addr,
  input  [31:0] Din,
  output [31:0] Dout
);

  wire and_1_out, clock_1_out, not_1_out;
  wire [13:0] adder_2_out, counter_1_q, counter_2_q, or_1_out;
  wire [31:0] adder_1_out, bit_extender_1_out;

  Adder #(.width(32)) adder_1 (.a(bit_extender_1_out), .b(Din), .out(adder_1_out));  // open: cin, cout
  Counter #(.width(14), .max('hf), .ongoal("stay"), .trigger("rising"), .behavior("old")) counter_1 (
    .Q(counter_1_q), .clk(and_1_out), .clr(not_1_out));  // open: load, D, count, carry, preset
  not not_1 (not_1_out, WE);
  assign bit_extender_1_out = {{18{1'b0}}, or_1_out};  // Bit_Extender bit_extender_1
  and and_1 (and_1_out, CLK, clock_1_out);
  Clock #(.highDuration(1), .lowDuration(1)) clock_1 (.out(clock_1_out));
  \_2_1__存储器扩展  \u_2_1_存储器扩展_1  (.CLK(and_1_out), .WE(WE), .Addr(adder_2_out), .Din(adder_1_out), .Dout(Dout));
  Counter #(.width(14), .max('h3fff), .ongoal("stay"), .trigger("rising"), .behavior("old")) counter_2 (
    .Q(counter_2_q), .clk(and_1_out), .clr(WE));  // open: load, D, count, carry, preset
  assign or_1_out = counter_2_q | counter_1_q;  // OR_Gate or_1, 14 bits wide
  Adder #(.width(14)) adder_2 (.a(or_1_out), .b(Addr), .out(adder_2_out));  // open: cin, cout
  Hex_Digit_Display hex_digit_display_1 (.value(Dout[15:12]));  // open: dp
  Hex_Digit_Display hex_digit_display_2 (.value(Dout[31:28]));  // open: dp
  Hex_Digit_Display hex_digit_display_3 (.value(Dout[7:4]));  // open: dp
  Hex_Digit_Display hex_digit_display_4 (.value(Dout[11:8]));  // open: dp
  Hex_Digit_Display hex_digit_display_5 (.value(Dout[23:20]));  // open: dp
  Hex_Digit_Display hex_digit_display_6 (.value(Dout[27:24]));  // open: dp
  Hex_Digit_Display hex_digit_display_7 (.value(Dout[3:0]));  // open: dp
  Hex_Digit_Display hex_digit_display_8 (.value(Dout[19:16]));  // open: dp
endmodule

module \_2_2__MIPS_RF模块  (
  input  CLK,
  input  WE,
  input  [4:0] RA1,
  input  [4:0] RA2,
  input  [31:0] Din,
  input  [4:0] WA,
  output [31:0] RD1,
  output [31:0] RD2
);

  wire button_1_out, decoder_1_out0, decoder_1_out1, decoder_1_out2, decoder_1_out3;
  wire [31:0] multiplexer_3_out, \n2_2_8_32寄存器_1_rd1 , \n2_2_8_32寄存器_1_rd2 , \n2_2_8_32寄存器_2_rd1 ,
       \n2_2_8_32寄存器_2_rd2 , \n2_2_8_32寄存器_3_rd1 , \n2_2_8_32寄存器_3_rd2 , \n2_2_8_32寄存器_4_rd1 ,
       \n2_2_8_32寄存器_4_rd2 ;

  Decoder #(.select(2), .tristate("false"), .disabled("Z"), .enable("false")) decoder_1 (
    .out0(decoder_1_out0), .out1(decoder_1_out1), .out2(decoder_1_out2), .out3(decoder_1_out3), .sel(WA[4:3]));
  \_2_2_8_32寄存器  \u_2_2_8_32寄存器_1  (
    .WA(WA), .RA1(RA1[2:0]), .Din(Din), .RD1(\n2_2_8_32寄存器_1_rd1 ), .RA2(RA2[2:0]),
    .RD2(\n2_2_8_32寄存器_1_rd2 ), .CS(decoder_1_out0), .WE(CLK), .CLK(WE));
  \_2_2_8_32寄存器  \u_2_2_8_32寄存器_2  (
    .WA(WA), .RA1(RA1[2:0]), .Din(Din), .RD1(\n2_2_8_32寄存器_2_rd1 ), .RA2(RA2[2:0]),
    .RD2(\n2_2_8_32寄存器_2_rd2 ), .CS(decoder_1_out2), .WE(CLK), .CLK(WE));
  \_2_2_8_32寄存器  \u_2_2_8_32寄存器_3  (
    .WA(WA), .RA1(RA1[2:0]), .Din(Din), .RD1(\n2_2_8_32寄存器_3_rd1 ), .RA2(RA2[2:0]),
    .RD2(\n2_2_8_32寄存器_3_rd2 ), .CS(decoder_1_out1), .WE(CLK), .CLK(WE));
  \_2_2_8_32寄存器  \u_2_2_8_32寄存器_4  (
    .WA(WA), .RA1(RA1[2:0]), .Din(Din), .RD1(\n2_2_8_32寄存器_4_rd1 ), .RA2(RA2[2:0]),
    .RD2(\n2_2_8_32寄存器_4_rd2 ), .CS(decoder_1_out3), .WE(CLK), .CLK(WE));
  Multiplexer #(.select(2), .width(32), .disabled("Z"), .enable("false")) multiplexer_1 (
    .in0(\n2_2_8_32寄存器_1_rd2 ), .in1(\n2_2_8_32寄存器_3_rd2 ), .in2(\n2_2_8_32寄存器_2_rd2 ),
    .in3(\n2_2_8_32寄存器_4_rd2 ), .out(RD2), .sel(RA2[4:3]));
  Multiplexer #(.select(2), .width(32), .disabled("Z"), .enable("false")) multiplexer_2 (
    .in0(\n2_2_8_32寄存器_1_rd1 ), .in1(\n2_2_8_32寄存器_3_rd1 ), .in2(\n2_2_8_32寄存器_2_rd1 ),
    .in3(\n2_2_8_32寄存器_4_rd1 ), .out(RD1), .sel(RA1[4:3]));
  Multiplexer #(.select(1), .width(32), .disabled("Z"), .enable("false")) multiplexer_3 (
    .in0(RD1), .in1(RD2), .out(multiplexer_3_out), .sel(button_1_out));
  Button button_1 (.out(button_1_out));
  Hex_Digit_Display hex_digit_display_1 (.value(multiplexer_3_out[15:12]));  // open: dp
  Hex_Digit_Display hex_digit_display_2 (.value(multiplexer_3_out[31:28]));  // open: dp
  Hex_Digit_Display hex_digit_display_3 (.value(multiplexer_3_out[11:8]));  // open: dp
  Hex_Digit_Display hex_digit_display_4 (.value(multiplexer_3_out[7:4]));  // open: dp
  Hex_Digit_Display hex_digit_display_5 (.value(multiplexer_3_out[27:24]));  // open: dp
  Hex_Digit_Display hex_digit_display_6 (.value(multiplexer_3_out[23:20]));  // open: dp
  Hex_Digit_Display hex_digit_display_7 (.value(multiplexer_3_out[3:0]));  // open: dp
  Hex_Digit_Display hex_digit_display_8 (.value(multiplexer_3_out[19:16]));  // open: dp

  // Notes on the sheet:
  //   输入引脚区
  //   注：不能增加任何输入输出端口信号
  //   输出引脚区
  //   实现MIPS寄存器组，32个寄存器可以采用模块化方法实现，模块规模不限，注意0号寄存器恒为0
  //   输出数据测试区
endmodule

module \_2_3__数据互传  (
  input  CLK,
  input  WE1,
  input  [2:0] AluOp,
  input  [1:0] RWsel,
  input  LA1,
  input  LA2,
  input  [31:0] Din,
  input  LWA,
  input  [1:0] Dispsel,
  input  CH1,
  input  WE2,
  output [31:0] Disp
);

  wire [4:0] register_1_q, register_2_q, register_3_q;
  wire [13:0] \n1_3_32位alu_1_p4 ;
  wire [17:0] \n1_3_32位alu_1_p4_2 ;
  wire [31:0] multiplexer_1_out, \n1_3_32位alu_1_p2 , \n2_1_存储器扩展_1_p5 , \n2_2_mips_rf模块_1_rd1 ,
       \n2_2_mips_rf模块_1_rd2 ;

  // Probe on Din[4:0]
  Register #(.width(5), .trigger("rising"), .Select("low")) register_1 (
    .D(Din[4:0]), .en(LA1), .Q(register_1_q), .clk(CLK));  // open: clr
  Register #(.width(5), .trigger("rising"), .Select("low")) register_2 (
    .D(Din[4:0]), .en(LA2), .Q(register_2_q), .clk(CLK));  // open: clr
  Register #(.width(5), .trigger("rising"), .Select("low")) register_3 (
    .D(Din[4:0]), .en(LWA), .Q(register_3_q), .clk(CLK));  // open: clr
  \_2_2__MIPS_RF模块  \u_2_2_mips_rf模块_1  (
    .RA1(register_1_q), .RA2(register_2_q), .WA(register_3_q), .Din(multiplexer_1_out), .CLK(CLK), .WE(WE1),
    .RD1(\n2_2_mips_rf模块_1_rd1 ), .RD2(\n2_2_mips_rf模块_1_rd2 ));
  Multiplexer #(.select(2), .width(32), .disabled("Z"), .enable("false")) multiplexer_1 (
    .in0(Din), .in1({\n1_3_32位alu_1_p4_2 , \n1_3_32位alu_1_p4 }), .in2(\n2_1_存储器扩展_1_p5 ),
    .in3(\n2_2_mips_rf模块_1_rd1 ), .out(multiplexer_1_out), .sel(RWsel));
  // _1_3_32位ALU 1_3_32位alu_1: pin names not known; wires that end beside it: \n2_2_mips_rf模块_1_rd1 , \n1_3_32位alu_1_p2 , AluOp, {\n1_3_32位alu_1_p4_2 , \n1_3_32位alu_1_p4 }
  Multiplexer #(.select(1), .width(32), .disabled("Z"), .enable("false")) multiplexer_2 (
    .in0(\n2_2_mips_rf模块_1_rd2 ), .in1(Din), .out(\n1_3_32位alu_1_p2 ), .sel(CH1));
  // Probe on \n1_3_32位alu_1_p4 
  // _2_1__存储器扩展 2_1_存储器扩展_1: pin names not known; wires that end beside it: \n1_3_32位alu_1_p4 , \n2_2_mips_rf模块_1_rd2 , WE2, CLK, \n2_1_存储器扩展_1_p5 
  Hex_Digit_Display hex_digit_display_1 (.value(Disp[15:12]));  // open: dp
  Hex_Digit_Display hex_digit_display_2 (.value(Disp[11:8]));  // open: dp
  Hex_Digit_Display hex_digit_display_3 (.value(Disp[31:28]));  // open: dp
  Hex_Digit_Display hex_digit_display_4 (.value(Disp[27:24]));  // open: dp
  Multiplexer #(.select(2), .width(32), .disabled("Z"), .enable("false")) multiplexer_3 (
    .in0(\n2_2_mips_rf模块_1_rd1 ), .in1(\n2_2_mips_rf模块_1_rd2 ),
    .in2({\n1_3_32位alu_1_p4_2 , \n1_3_32位alu_1_p4 }), .in3(\n2_1_存储器扩展_1_p5 ), .out(Disp), .sel(Dispsel));
  Hex_Digit_Display hex_digit_display_5 (.value(Disp[3:0]));  // open: dp
  Hex_Digit_Display hex_digit_display_6 (.value(Disp[7:4]));  // open: dp
  Hex_Digit_Display hex_digit_display_7 (.value(Disp[23:20]));  // open: dp
  Hex_Digit_Display hex_digit_display_8 (.value(Disp[19:16]));  // open: dp
  // Probe on \n2_1_存储器扩展_1_p5 

  // Notes on the sheet:
  //   输入引脚区
  //   注：请完善数据通路可以增加必要的输入控制端口信号
  //   输出引脚区
  //   注：数据通路图中RF使用2-2MIPS RF模块，MEMU是2-1存储器扩展模块
  //   输出数据测试区
endmodule

module \_2_2_8_32寄存器  (
  input  [31:0] Din,
  input  WE,
  input  CS,
  input  CLK,
  input  [2:0] RA1,
  input  [4:0] WA,
  input  [2:0] RA2,
  output [31:0] RD1,
  output [31:0] RD2
);

  wire and_1_out, and_2_out, decoder_1_out0, decoder_1_out1, decoder_1_out2, decoder_1_out3, decoder_1_out4,
       decoder_1_out5, decoder_1_out6, decoder_1_out7, not_1_out, not_2_out;
  wire [31:0] _0_q, _1_q, _2_q, _3_q, _4_q, _5_q, _6_q, _7_q;

  and and_1 (and_1_out, WE, CS, CLK);
  Decoder #(.select(3), .tristate("false"), .disabled("Z"), .enable("false")) decoder_1 (
    .out0(decoder_1_out0), .out1(decoder_1_out1), .out2(decoder_1_out2), .out3(decoder_1_out3),
    .out4(decoder_1_out4), .out5(decoder_1_out5), .out6(decoder_1_out6), .out7(decoder_1_out7), .sel(WA[2:0]));
  not not_1 (not_1_out, WA[3]);
  not not_2 (not_2_out, WA[4]);
  and and_2 (and_2_out, decoder_1_out0, not_1_out, not_2_out);
  Register #(.width(32), .trigger("rising"), .Select("low")) _0 (
    .D(Din), .en(decoder_1_out0), .Q(_0_q), .clk(and_1_out), .clr(and_2_out));
  Register #(.width(32), .trigger("rising"), .Select("low")) _4 (
    .D(Din), .en(decoder_1_out4), .Q(_4_q), .clk(and_1_out));  // open: clr
  Register #(.width(32), .trigger("rising"), .Select("low")) _1 (
    .D(Din), .en(decoder_1_out1), .Q(_1_q), .clk(and_1_out));  // open: clr
  Register #(.width(32), .trigger("rising"), .Select("low")) _5 (
    .D(Din), .en(decoder_1_out5), .Q(_5_q), .clk(and_1_out));  // open: clr
  Register #(.width(32), .trigger("rising"), .Select("low")) _2 (
    .D(Din), .en(decoder_1_out2), .Q(_2_q), .clk(and_1_out));  // open: clr
  Register #(.width(32), .trigger("rising"), .Select("low")) _6 (
    .D(Din), .en(decoder_1_out6), .Q(_6_q), .clk(and_1_out));  // open: clr
  Register #(.width(32), .trigger("rising"), .Select("low")) _3 (
    .D(Din), .en(decoder_1_out3), .Q(_3_q), .clk(and_1_out));  // open: clr
  Register #(.width(32), .trigger("rising"), .Select("low")) _7 (
    .D(Din), .en(decoder_1_out7), .Q(_7_q), .clk(and_1_out));  // open: clr
  Multiplexer #(.select(3), .width(32), .disabled("Z"), .enable("false")) multiplexer_1 (
    .in0(_0_q), .in1(_1_q), .in2(_2_q), .in3(_3_q), .in4(_4_q), .in5(_5_q), .in6(_6_q), .in7(_7_q),
    .out(RD1), .sel(RA1));
  Multiplexer #(.select(3), .width(32), .disabled("Z"), .enable("false")) multiplexer_2 (
    .in0(_0_q), .in1(_1_q), .in2(_2_q), .in3(_3_q), .in4(_4_q), .in5(_5_q), .in6(_6_q), .in7(_7_q),
    .out(RD2), .sel(RA2));
endmodule
