// Logisim project EXP3_MIPSCPU.circ as structural Verilog: 8 circuits, main circuit ◇单周期MIPS
module \单周期MIPS  (
  output [31:0] PC,
  output [31:0] IR,
  output [31:0] RDin,
  output [31:0] MDin,
  output [31:0] LedData
);

  wire CLK, Go, mips_alu_1_zf, Rst, \单周期硬布线控制器_1_c1 , \单周期硬布线控制器_1_c2 , \单周期硬布线控制器_1_c3 , \单周期硬布线控制器_1_c4 ,
       \单周期硬布线控制器_1_c5 , \单周期硬布线控制器_1_c6 , \单周期硬布线控制器_1_c7 , \单周期硬布线控制器_1_c8 ;
  wire [2:0] \单周期硬布线控制器_1_alu_op ;
  wire [4:0] id_1_rd, id_1_rs, id_1_rt, multiplexer_1_out;
  wire [5:0] Funct, OP;
  wire [15:0] \总周期数 ;
  wire [17:2] id_1_imm16;
  wire [27:2] id_1_imm20;
  wire [31:0] bit_extender_1_out, mips_alu_1_s, mips_regifile_1_r1, multiplexer_2_out, multiplexer_3_out,
       ram_1_data;

  Clock #(.highDuration(1), .lowDuration(1)) clock_1 (.out(CLK));
  Button button_1 (.out(Rst));
  // DipSwitch #(.NSwitches(1)) dipswitch_1: pin names not known; wires that end beside it: Go
  NPC npc_1 (
    .Zero(mips_alu_1_zf), .Jump(\单周期硬布线控制器_1_c1 ), .Imm(multiplexer_2_out), .Clk(CLK),
    .Branch(\单周期硬布线控制器_1_c2 ), .RST(Rst), .PC(PC));
  Hex_Digit_Display hex_digit_display_1 (.value(LedData[31:28]));  // open: dp
  Counter #(.width(16), .max('hffff), .ongoal("wrap"), .trigger("rising"), .behavior("new")) counter_1 (
    .count(Go), .Q(\总周期数 ), .clk(CLK), .clr(Rst));  // open: load, D, carry, preset, down
  Hex_Digit_Display hex_digit_display_2 (.value(LedData[27:24]));  // open: dp
  Hex_Digit_Display hex_digit_display_3 (.value(LedData[23:20]));  // open: dp
  Hex_Digit_Display hex_digit_display_4 (.value(LedData[15:12]));  // open: dp
  Hex_Digit_Display hex_digit_display_5 (.value(LedData[19:16]));  // open: dp
  ROM #(.addrWidth(10), .dataWidth(32), .Select("high")) rom_1 (.addr(PC[11:2]), .data(IR), .sel(Go));
  Hex_Digit_Display hex_digit_display_6 (.value(LedData[7:4]));  // open: dp
  Hex_Digit_Display hex_digit_display_7 (.value(LedData[11:8]));  // open: dp
  // Probe on \总周期数 
  ID id_1 (
    .Instruction(IR), .OP(OP), .Funct(Funct), .rs(id_1_rs), .rt(id_1_rt), .rd(id_1_rd), .Imm16(id_1_imm16),
    .Imm20(id_1_imm20));  // open: Shamt
  \单周期硬布线控制器  \u_单周期硬布线控制器_1  (
    .Func(Funct), .OP(OP), .ALU_OP(\单周期硬布线控制器_1_alu_op ), .C1(\单周期硬布线控制器_1_c1 ), .C2(\单周期硬布线控制器_1_c2 ),
    .C3(\单周期硬布线控制器_1_c3 ), .C4(\单周期硬布线控制器_1_c4 ), .C5(\单周期硬布线控制器_1_c5 ), .C6(\单周期硬布线控制器_1_c6 ),
    .C7(\单周期硬布线控制器_1_c7 ), .C8(\单周期硬布线控制器_1_c8 ));
  Hex_Digit_Display hex_digit_display_8 (.value(LedData[3:0]));  // open: dp
  Multiplexer #(.select(1), .width(5), .disabled("Z"), .enable("false")) multiplexer_1 (
    .in0(id_1_rt), .in1(id_1_rd), .out(multiplexer_1_out), .sel(\单周期硬布线控制器_1_c6 ));
  assign bit_extender_1_out = {{16{id_1_imm16[17]}}, id_1_imm16};  // Bit_Extender bit_extender_1
  Multiplexer #(.select(1), .width(32), .disabled("Z"), .enable("false")) multiplexer_2 (
    .in0({{14{1'b0}}, id_1_imm16, 2'b00}), .in1({4'b0000, id_1_imm20, 2'b00}), .out(multiplexer_2_out),
    .sel(\单周期硬布线控制器_1_c3 ));
  MIPS_Regifile mips_regifile_1 (
    .Din(RDin), .W_num(multiplexer_1_out), .R1_num(id_1_rs), .R2_num(id_1_rt), .R2(MDin),
    .R1(mips_regifile_1_r1), .WE(\单周期硬布线控制器_1_c4 ), .Clk(CLK));
  Multiplexer #(.select(1), .width(32), .disabled("Z"), .enable("false")) multiplexer_3 (
    .in0(MDin), .in1(bit_extender_1_out), .out(multiplexer_3_out), .sel(\单周期硬布线控制器_1_c7 ));
  Multiplexer #(.select(1), .width(32), .disabled("Z"), .enable("false")) multiplexer_4 (
    .in0(mips_alu_1_s), .in1(ram_1_data), .out(RDin), .sel(\单周期硬布线控制器_1_c5 ));
  MIPS_ALU mips_alu_1 (
    .X(mips_regifile_1_r1), .Y(multiplexer_3_out), .AluOP(\单周期硬布线控制器_1_alu_op ), .S(mips_alu_1_s),
    .ZF(mips_alu_1_zf));  // open: OF, UOF
  RAM #(.addrWidth(10), .dataWidth(32), .bus("separate"), .Select("high")) ram_1 (
    .addr(mips_alu_1_s[11:2]), .din(MDin), .data(ram_1_data), .str(\单周期硬布线控制器_1_c8 ), .sel(Go), .clk(CLK),
    .ld(Go));  // open: clr
  Register #(.width(32), .trigger("rising"), .Select("low")) register_1 (
    .D(ram_1_data), .Q(LedData), .clk(CLK));  // open: en, clr

  // Notes on the sheet:
  //   总复位信号应将除ROM以外所有存储组件全部清零
  //   指令存储器
  //   ALUOP
  //   数码管输出
  //   contents of rom_1 (hex, n*v repeats v):
  //   8c080000 8c090000 200a0004 200d0001 200e002c 2010002c 20110030 8d4c0000 12c582a 116d0008 188582a
  //   116d0008 214a0004 14e582a 116dfff8 ae080000 ae290000 8000c16 1804820 8000c0c 1804020 8000c0c 8000c16
  //   JMP
  //   BEQ
  //   数码管输出应该用寄存器锁存，否则显示数据只能一闪而过
  //   SIGNEEXT
  //   此连线不得改动
  //   此连线不得改动
  //   RFWRITE
  //   REGD_SRC
  //   REGA3_SRC
  //   ALUB_SRC
  //   此连线不得改动
  //   DMWR
  //   为方便自动评测，需要输出PC，IR，寄存器文件写入端口RDin，内存写入端口MDin等信号
  //   数据存储器
endmodule

// 单周期硬布线控制器
module \单周期硬布线控制器  (
  input  [5:0] OP,
  input  [5:0] Func,
  output [2:0] ALU_OP,
  output C1,
  output C2,
  output C3,
  output C4,
  output C5,
  output C6,
  output C7,
  output C8
);

  \运算控制信号自动生成器  \u_运算控制信号自动生成器_1  (
    .OP0(OP[0]), .OP1(OP[1]), .OP2(OP[2]), .OP3(OP[3]), .OP4(OP[4]), .OP5(OP[5]), .F0(Func[0]), .F1(Func[1]),
    .F2(Func[2]), .F3(Func[3]), .F4(Func[4]), .F5(Func[5]), .S0(ALU_OP[0]), .S1(ALU_OP[1]), .S2(ALU_OP[2]));
  \控制信号发生器  \u_控制信号发生器_1  (
    .OP0(OP[0]), .OP1(OP[1]), .OP2(OP[2]), .OP3(OP[3]), .OP4(OP[4]), .OP5(OP[5]), .F0(Func[0]), .F1(Func[1]),
    .F2(Func[2]), .F3(Func[3]), .F4(Func[4]), .F5(Func[5]), .Jump(C1), .Beq(C2), .SigneExt(C3), .RFWrite(C4),
    .RegD_src(C5), .RegA3_src(C6), .ALUB_src(C7), .DMWr(C8));

  // Other names for the same wires on the sheet: OP_CODE[5:0] = OP

  // Notes on the sheet:
  //   运算器控制器，根据指令生成运算器功能选择信号
endmodule

// 运算控制信号发射器
module \运算控制信号自动生成器  (
  input  OP0,
  input  OP1,
  input  OP2,
  input  OP3,
  input  OP4,
  input  OP5,
  input  F0,
  input  F1,
  input  F2,
  input  F3,
  input  F4,
  input  F5,
  output S0,
  output S1,
  output S2
);

  wire and_1_out, and_2_out, and_3_out, and_4_out, and_5_out, and_6_out, not_1_out, not_2_out, not_3_out,
       not_4_out, not_5_out, not_6_out, not_7_out, not_8_out, not_9_out, not_10_out, not_11_out, not_12_out,
       not_13_out, not_14_out, not_15_out, not_16_out, not_17_out, not_18_out, not_19_out, not_20_out,
       not_21_out, not_22_out, not_23_out, not_24_out, not_25_out, not_26_out, not_27_out, not_28_out,
       not_29_out, not_30_out, not_31_out, not_32_out, not_33_out, not_34_out, not_35_out, not_36_out,
       not_37_out, not_38_out, not_39_out, not_40_out, not_41_out, not_42_out, not_43_out, not_44_out,
       not_45_out, not_46_out, not_47_out, not_48_out;

  not not_1 (not_1_out, OP5);
  not not_2 (not_2_out, OP4);
  not not_3 (not_3_out, OP3);
  not not_4 (not_4_out, OP2);
  not not_5 (not_5_out, OP1);
  not not_6 (not_6_out, OP0);
  not not_7 (not_7_out, F4);
  not not_8 (not_8_out, F2);
  not not_9 (not_9_out, F0);
  not not_10 (not_10_out, OP5);
  not not_11 (not_11_out, OP4);
  not not_12 (not_12_out, OP1);
  not not_13 (not_13_out, OP5);
  not not_14 (not_14_out, OP4);
  not not_15 (not_15_out, OP3);
  not not_16 (not_16_out, OP1);
  not not_17 (not_17_out, OP0);
  not not_18 (not_18_out, OP5);
  not not_19 (not_19_out, OP4);
  not not_20 (not_20_out, OP3);
  not not_21 (not_21_out, OP2);
  not not_22 (not_22_out, OP1);
  not not_23 (not_23_out, OP0);
  not not_24 (not_24_out, F4);
  not not_25 (not_25_out, F3);
  not not_26 (not_26_out, F2);
  not not_27 (not_27_out, F0);
  not not_28 (not_28_out, OP0);
  not not_29 (not_29_out, OP1);
  not not_30 (not_30_out, OP2);
  not not_31 (not_31_out, OP3);
  not not_32 (not_32_out, OP4);
  not not_33 (not_33_out, OP5);
  not not_34 (not_34_out, F0);
  not not_35 (not_35_out, F2);
  not not_36 (not_36_out, F4);
  not not_37 (not_37_out, OP1);
  not not_38 (not_38_out, OP4);
  not not_39 (not_39_out, OP5);
  not not_40 (not_40_out, OP0);
  not not_41 (not_41_out, OP1);
  not not_42 (not_42_out, OP2);
  not not_43 (not_43_out, OP3);
  not not_44 (not_44_out, OP4);
  not not_45 (not_45_out, OP5);
  not not_46 (not_46_out, F0);
  not not_47 (not_47_out, F2);
  not not_48 (not_48_out, F4);
  and and_1 (and_1_out, not_1_out, not_2_out, not_3_out, not_4_out, not_5_out, not_6_out, F5, not_7_out, F3, not_8_out, F1, not_9_out);
  and and_2 (and_2_out, not_10_out, not_11_out, OP3, OP2, not_12_out, OP0);
  and and_3 (and_3_out, not_13_out, not_14_out, not_15_out, OP2, not_16_out, not_17_out);
  and and_4 (and_4_out, not_18_out, not_19_out, not_20_out, not_21_out, not_22_out, not_23_out, F5, not_24_out, not_25_out, not_26_out, F1, not_27_out);
  and and_5 (and_5_out, not_28_out, not_29_out, not_30_out, not_31_out, not_32_out, not_33_out, not_34_out, F1, not_35_out, F3, not_36_out, F5);
  and and_6 (and_6_out, OP0, not_37_out, OP2, OP3, not_38_out, not_39_out);
  and and_7 (S2, not_40_out, not_41_out, not_42_out, not_43_out, not_44_out, not_45_out, not_46_out, F1, not_47_out, F3, not_48_out, F5);
  or or_1 (S0, and_1_out, and_2_out, and_3_out, and_4_out);
  or or_2 (S1, and_5_out, and_6_out);
endmodule

// 控制信号发生器
module \控制信号发生器  (
  input  OP0,
  input  OP1,
  input  OP2,
  input  OP3,
  input  OP4,
  input  OP5,
  input  F0,
  input  F1,
  input  F2,
  input  F3,
  input  F4,
  input  F5,
  output Jump,
  output Beq,
  output SigneExt,
  output RFWrite,
  output RegD_src,
  output RegA3_src,
  output ALUB_src,
  output DMWr
);

  wire and_4_out, and_5_out, and_6_out, and_7_out, and_8_out, and_10_out, and_11_out, and_12_out, and_13_out,
       and_14_out, and_15_out, not_1_out, not_2_out, not_3_out, not_4_out, not_5_out, not_6_out, not_7_out,
       not_8_out, not_9_out, not_10_out, not_11_out, not_12_out, not_13_out, not_14_out, not_15_out,
       not_16_out, not_17_out, not_18_out, not_19_out, not_20_out, not_21_out, not_22_out, not_23_out,
       not_24_out, not_25_out, not_26_out, not_27_out, not_28_out, not_29_out, not_30_out, not_31_out,
       not_32_out, not_33_out, not_34_out, not_35_out, not_36_out, not_37_out, not_38_out, not_39_out,
       not_40_out, not_41_out, not_42_out, not_43_out, not_44_out, not_45_out, not_46_out, not_47_out,
       not_48_out, not_49_out, not_50_out, not_51_out, not_52_out, not_53_out, not_54_out, not_55_out,
       not_56_out, not_57_out, not_58_out, not_59_out, not_60_out, not_61_out, not_62_out, not_63_out,
       not_64_out, not_65_out, not_66_out, not_67_out, not_68_out, not_69_out, not_70_out, not_71_out,
       not_72_out, not_73_out, not_74_out, not_75_out, not_76_out, not_77_out, not_78_out, not_79_out,
       not_80_out, not_81_out, not_82_out, not_83_out, not_84_out, not_85_out, not_86_out, not_87_out,
       not_88_out, not_89_out, not_90_out, not_91_out, not_92_out, not_93_out, not_94_out;

  not not_1 (not_1_out, OP5);
  not not_2 (not_2_out, OP4);
  not not_3 (not_3_out, OP3);
  not not_4 (not_4_out, OP2);
  not not_5 (not_5_out, OP0);
  not not_6 (not_6_out, OP5);
  not not_7 (not_7_out, OP4);
  not not_8 (not_8_out, OP3);
  not not_9 (not_9_out, OP1);
  not not_10 (not_10_out, OP0);
  not not_11 (not_11_out, OP5);
  not not_12 (not_12_out, OP4);
  not not_13 (not_13_out, OP3);
  not not_14 (not_14_out, OP1);
  not not_15 (not_15_out, OP0);
  not not_16 (not_16_out, OP5);
  not not_17 (not_17_out, OP4);
  not not_18 (not_18_out, OP3);
  not not_19 (not_19_out, OP2);
  not not_20 (not_20_out, OP1);
  not not_21 (not_21_out, OP0);
  not not_22 (not_22_out, F4);
  not not_23 (not_23_out, F3);
  not not_24 (not_24_out, F2);
  not not_25 (not_25_out, F1);
  not not_26 (not_26_out, F0);
  not not_27 (not_27_out, OP5);
  not not_28 (not_28_out, OP4);
  not not_29 (not_29_out, OP3);
  not not_30 (not_30_out, OP2);
  not not_31 (not_31_out, OP1);
  not not_32 (not_32_out, OP0);
  not not_33 (not_33_out, F4);
  not not_34 (not_34_out, F3);
  not not_35 (not_35_out, F2);
  not not_36 (not_36_out, F0);
  not not_37 (not_37_out, OP5);
  not not_38 (not_38_out, OP4);
  not not_39 (not_39_out, OP1);
  not not_40 (not_40_out, OP4);
  not not_41 (not_41_out, OP3);
  not not_42 (not_42_out, OP2);
  not not_43 (not_43_out, OP5);
  not not_44 (not_44_out, OP4);
  not not_45 (not_45_out, OP3);
  not not_46 (not_46_out, OP2);
  not not_47 (not_47_out, OP1);
  not not_48 (not_48_out, OP0);
  not not_49 (not_49_out, F4);
  not not_50 (not_50_out, F2);
  not not_51 (not_51_out, F0);
  not not_52 (not_52_out, OP4);
  not not_53 (not_53_out, OP3);
  not not_54 (not_54_out, OP2);
  not not_55 (not_55_out, OP5);
  not not_56 (not_56_out, OP4);
  not not_57 (not_57_out, OP3);
  not not_58 (not_58_out, OP2);
  not not_59 (not_59_out, OP1);
  not not_60 (not_60_out, OP0);
  not not_61 (not_61_out, F4);
  not not_62 (not_62_out, F3);
  not not_63 (not_63_out, F2);
  not not_64 (not_64_out, F1);
  not not_65 (not_65_out, F0);
  not not_66 (not_66_out, OP5);
  not not_67 (not_67_out, OP4);
  not not_68 (not_68_out, OP3);
  not not_69 (not_69_out, OP2);
  not not_70 (not_70_out, OP1);
  not not_71 (not_71_out, OP0);
  not not_72 (not_72_out, F4);
  not not_73 (not_73_out, F3);
  not not_74 (not_74_out, F2);
  not not_75 (not_75_out, F0);
  not not_76 (not_76_out, OP5);
  not not_77 (not_77_out, OP4);
  not not_78 (not_78_out, OP3);
  not not_79 (not_79_out, OP2);
  not not_80 (not_80_out, OP1);
  not not_81 (not_81_out, OP0);
  not not_82 (not_82_out, F4);
  not not_83 (not_83_out, F2);
  not not_84 (not_84_out, F0);
  not not_85 (not_85_out, OP5);
  not not_86 (not_86_out, OP4);
  not not_87 (not_87_out, OP1);
  not not_88 (not_88_out, OP4);
  not not_89 (not_89_out, OP3);
  not not_90 (not_90_out, OP2);
  not not_91 (not_91_out, OP4);
  not not_92 (not_92_out, OP2);
  not not_93 (not_93_out, OP4);
  not not_94 (not_94_out, OP2);
  and and_1 (Jump, not_1_out, not_2_out, not_3_out, not_4_out, OP1, not_5_out);
  and and_2 (Beq, not_6_out, not_7_out, not_8_out, OP2, not_9_out, not_10_out);
  and and_3 (SigneExt, not_11_out, not_12_out, not_13_out, OP2, not_14_out, not_15_out);
  and and_4 (and_4_out, not_16_out, not_17_out, not_18_out, not_19_out, not_20_out, not_21_out, F5, not_22_out, not_23_out, not_24_out, not_25_out, not_26_out);
  and and_5 (and_5_out, not_27_out, not_28_out, not_29_out, not_30_out, not_31_out, not_32_out, F5, not_33_out, not_34_out, not_35_out, F1, not_36_out);
  and and_6 (and_6_out, not_37_out, not_38_out, OP3, OP2, not_39_out, OP0);
  and and_7 (and_7_out, OP5, not_40_out, not_41_out, not_42_out, OP1, OP0);
  and and_8 (and_8_out, not_43_out, not_44_out, not_45_out, not_46_out, not_47_out, not_48_out, F5, not_49_out, F3, not_50_out, F1, not_51_out);
  and and_9 (RegD_src, OP5, not_52_out, not_53_out, not_54_out, OP1, OP0);
  and and_10 (and_10_out, not_55_out, not_56_out, not_57_out, not_58_out, not_59_out, not_60_out, F5, not_61_out, not_62_out, not_63_out, not_64_out, not_65_out);
  and and_11 (and_11_out, not_66_out, not_67_out, not_68_out, not_69_out, not_70_out, not_71_out, F5, not_72_out, not_73_out, not_74_out, F1, not_75_out);
  and and_12 (and_12_out, not_76_out, not_77_out, not_78_out, not_79_out, not_80_out, not_81_out, F5, not_82_out, F3, not_83_out, F1, not_84_out);
  and and_13 (and_13_out, not_85_out, not_86_out, OP3, OP2, not_87_out, OP0);
  and and_14 (and_14_out, OP5, not_88_out, not_89_out, not_90_out, OP1, OP0);
  and and_15 (and_15_out, OP5, not_91_out, OP3, not_92_out, OP1, OP0);
  and and_16 (DMWr, OP5, not_93_out, OP3, not_94_out, OP1, OP0);
  or or_1 (RFWrite, and_4_out, and_5_out, and_6_out, and_7_out, and_8_out);
  or or_2 (RegA3_src, and_10_out, and_11_out, and_12_out);
  or or_3 (ALUB_src, and_13_out, and_14_out, and_15_out);
endmodule

// ALU
module MIPS_ALU (
  input  [31:0] X,
  input  [31:0] Y,
  input  [2:0] AluOP,
  output OF,
  output UOF,
  output ZF,
  output [31:0] S
);

  // _1_3_32位ALU 1_3_32位alu_1: pin names not known; wires that end beside it: X, Y, OF, AluOP, UOF, ZF, S

  // Notes on the sheet:
  //   不要改变此引脚区域内容，也不要改变ALU封装形式
  //   输入引脚
endmodule

module MIPS_Regifile (
  input  [4:0] R1_num,
  input  [4:0] R2_num,
  input  [4:0] W_num,
  input  [31:0] Din,
  input  WE,
  input  Clk,
  output [31:0] R1,
  output [31:0] R2
);

  \_2_2__MIPS_RF模块  \u_2_2_mips_rf模块_1  (
    .RA1(R1_num), .RA2(R2_num), .WA(W_num), .Din(Din), .CLK(Clk), .WE(WE), .RD1(R1), .RD2(R2));
endmodule

module NPC (
  input  Zero,
  input  Jump,
  input  [31:0] Imm,
  input  Clk,
  input  Branch,
  input  RST,
  output [31:0] PC
);

  wire and_1_out, or_1_out;
  wire [31:0] adder_1_out, adder_2_out, multiplexer_1_out, multiplexer_2_out;

  and and_1 (and_1_out, Zero, Branch);
  or or_1 (or_1_out, Jump, and_1_out);
  Adder #(.width(32)) adder_1 (.a(PC), .b(32'h4), .out(adder_1_out));  // open: cin, cout
  Adder #(.width(32)) adder_2 (.a(Imm), .b(adder_1_out), .out(adder_2_out));  // open: cin, cout
  Multiplexer #(.select(1), .width(32), .disabled("Z"), .enable("false")) multiplexer_1 (
    .in0(adder_1_out), .in1(adder_2_out), .out(multiplexer_1_out), .sel(or_1_out));
  Multiplexer #(.select(1), .width(32), .disabled("Z"), .enable("false")) multiplexer_2 (
    .in0(multiplexer_1_out), .in1(Imm), .out(multiplexer_2_out), .sel(Jump));
  Register #(.width(32), .trigger("rising"), .Select("low")) register_1 (
    .D(multiplexer_2_out), .Q(PC), .clk(Clk), .clr(RST));  // open: en

  // Notes on the sheet:
  //   Branch: pull=down
  //   Jump: pull=down
  //   Clk: pull=down
  //   RST: pull=down
  //   Imm: pull=down
  //   Zero: pull=down
  //   输入信号
  //   输出信号
endmodule

module ID (
  input  [31:0] Instruction,
  output [5:0] OP,
  output [5:0] Funct,
  output [4:0] Shamt,
  output [4:0] rs,
  output [4:0] rt,
  output [4:0] rd,
  output [15:0] Imm16,
  output [25:0] Imm20
);


  assign Funct = Instruction[5:0];
  assign Imm16 = Instruction[15:0];
  assign Imm20 = Instruction[25:0];
  assign OP = Instruction[31:26];
  assign rd = Instruction[15:11];
  assign rs = Instruction[25:21];
  assign rt = Instruction[20:16];
  assign Shamt = Instruction[10:6];

  // Other names for the same wires on the sheet: Imm26[25:0] = Instruction[25:0]
endmodule
