// Logisim project shiyan3.circ as structural Verilog: 8 circuits, main circuit ◇单周期MIPS
module \单周期MIPS  (
  output [31:0] PC,
  output [31:0] IR,
  output [31:0] RDin,
  output [31:0] MDin,
  output [31:0] LedData
);

  wire ALUB_src, Beq, CLK, DMWr, Go, Jump, RegA3_src, RFWrite, Rst, SignExt, ZERO, \单周期硬布线控制器_1_npcop_src ;
  wire [1:0] RegD_src;
  wire [2:0] ALU_OP;
  wire [4:0] multiplexer_3_out;
  wire [9:0] PC_4;
  wire [15:0] bit_extender_2_out, \总周期数 ;
  wire [25:0] bit_extender_1_out;
  wire [31:0] bit_extender_3_out, bit_extender_4_out, mips_alu_1_s, mips_regifile_1_rd1, multiplexer_2_out,
       multiplexer_4_out, npc_1_p3, npc_1_p6, rom_1_data, undriven, undriven_2;

  Clock #(.highDuration(1), .lowDuration(1)) clock_1 (.out(CLK));
  Button button_1 (.out(Rst));
  // DipSwitch #(.NSwitches(1)) dipswitch_1: pin names not known; wires that end beside it: Go
  // NPC npc_1: pin names not known; wires that end beside it: Jump, Beq, npc_1_p3, CLK, Rst, {npc_1_p6[31:12], PC_4, npc_1_p6[1:0]}
  Hex_Digit_Display hex_digit_display_1 (.value(LedData[31:28]));  // open: dp
  Multiplexer #(.select(1), .width(32), .disabled("Z"), .enable("false")) multiplexer_1 (
    .in0(undriven_2), .in1(undriven), .out(npc_1_p3), .sel(\单周期硬布线控制器_1_npcop_src ));
  Hex_Digit_Display hex_digit_display_2 (.value(LedData[23:20]));  // open: dp
  Hex_Digit_Display hex_digit_display_3 (.value(LedData[27:24]));  // open: dp
  Bit_Extender #(.in_width(32), .out_width(26), .\type ("zero")) bit_extender_1 (
    .in(undriven_2), .out(bit_extender_1_out));
  Bit_Extender #(.in_width(32), .out_width(16), .\type ("zero")) bit_extender_2 (
    .in(undriven), .out(bit_extender_2_out));
  Hex_Digit_Display hex_digit_display_4 (.value(LedData[19:16]));  // open: dp
  Hex_Digit_Display hex_digit_display_5 (.value(LedData[15:12]));  // open: dp
  ROM #(.addrWidth(10), .dataWidth(32), .Select("high")) rom_1 (.addr(PC_4), .data(rom_1_data));
  Hex_Digit_Display hex_digit_display_6 (.value(LedData[7:4]));  // open: dp
  Hex_Digit_Display hex_digit_display_7 (.value(LedData[11:8]));  // open: dp
  // Probe on \总周期数 
  ID id_1 (
    .OP(IR[31:26]), .Funct(IR[5:0]), .Shamt(IR[10:6]), .rs(IR[25:21]), .rt(IR[20:16]), .rd(IR[15:11]),
    .Instruction(rom_1_data), .Imm16(bit_extender_2_out), .Imm20(bit_extender_1_out));
  assign bit_extender_3_out = {{16{1'b0}}, bit_extender_2_out};  // Bit_Extender bit_extender_3
  assign bit_extender_4_out = {{16{1'b0}}, bit_extender_2_out};  // Bit_Extender bit_extender_4
  \单周期硬布线控制器  \u_单周期硬布线控制器_1  (
    .Func(IR[5:0]), .OP(IR[31:26]), .ALU_OP(ALU_OP), .in_3(ZERO), .ALUB_src(ALUB_src), .SigneExt(SignExt),
    .Beq(Beq), .NPCOP_src(\单周期硬布线控制器_1_npcop_src ), .Jump(Jump), .RegA3_src(RegA3_src), .RFWrite(RFWrite),
    .DMWr(DMWr), .RegD_src(RegD_src));
  Hex_Digit_Display hex_digit_display_8 (.value(LedData[3:0]));  // open: dp
  Multiplexer #(.select(1), .width(32), .disabled("Z"), .enable("false")) multiplexer_2 (
    .in0(bit_extender_3_out), .in1(bit_extender_4_out), .out(multiplexer_2_out), .sel(SignExt));
  Multiplexer #(.select(1), .width(5), .disabled("Z"), .enable("false")) multiplexer_3 (
    .in0(IR[20:16]), .in1(IR[15:11]), .out(multiplexer_3_out), .sel(RegA3_src));
  MIPS_Regifile mips_regifile_1 (
    .CLK(CLK), .WE(RFWrite), .RA1(IR[25:21]), .RA2(IR[20:16]), .Din(RDin), .RD1(mips_regifile_1_rd1),
    .RD2(MDin), .WA(multiplexer_3_out));
  Multiplexer #(.select(1), .width(32), .disabled("Z"), .enable("false")) multiplexer_4 (
    .in0(MDin), .in1(multiplexer_2_out), .out(multiplexer_4_out), .sel(ALUB_src));
  MIPS_ALU mips_alu_1 (
    .AluOp(ALU_OP), .ZF(ZERO), .S(mips_alu_1_s), .X(mips_regifile_1_rd1), .Y(multiplexer_4_out));  // open: OF, UOF
  Multiplexer #(.select(2), .width(32), .disabled("Z"), .enable("false")) multiplexer_5 (
    .in0(mips_alu_1_s), .in1(LedData), .out(RDin), .sel(RegD_src));  // open: in2, in3
  RAM #(.addrWidth(10), .dataWidth(32), .bus("separate"), .Select("high")) ram_1 (
    .addr(mips_alu_1_s[11:2]), .din(MDin), .data(LedData), .str(DMWr), .clk(CLK));  // open: sel, ld, clr
  Register #(.width(16), .trigger("rising"), .Select("low")) register_1 (.Q(\总周期数 ));  // open: D, en, clk, clr

  // Other names for the same wires on the sheet: Funct[5:0] = IR[5:0]; Imm16[15:0] = IR[15:0]; Imm26[25:0] = IR[25:0];
  //   Shamt[4:0] = IR[10:6]; rd[4:0] = IR[15:11]; rt[4:0] = IR[20:16]; rs[4:0] = IR[25:21]; OP[5:0] = IR[31:26]

  // Notes on the sheet:
  //   总复位信号应将除ROM以外所有存储组件全部清零
  //   指令存储器
  //   数码管输出
  //   contents of rom_1 (hex, n*v repeats v):
  //   8c030000 34050001 34020001 20630001 2020 852020 a22820 a3082a 10200001 c000c05 ac040004 c000c0b
  //   数码管输出应该用寄存器锁存，否则显示数据只能一闪而过
  //   此连线不得改动
  //   此连线不得改动
  //   此连线不得改动
  //   为方便自动评测，需要输出PC，IR，寄存器文件写入端口RDin，内存写入端口MDin等信号
  //   数据存储器
endmodule

// 单周期硬布线控制器
module \单周期硬布线控制器  (
  input  [5:0] OP,
  input  [5:0] Func,
  input  in_3,
  output [2:0] ALU_OP,
  output ALUB_src,
  output SigneExt,
  output Beq,
  output NPCOP_src,
  output Jump,
  output [1:0] RegD_src,
  output RegA3_src,
  output RFWrite,
  output DMWr
);

  \运算控制信号自动生成器  \u_运算控制信号自动生成器_1  (
    .OP0(OP[0]), .OP1(OP[1]), .OP2(OP[2]), .OP3(OP[3]), .OP4(OP[4]), .OP5(OP[5]), .F0(Func[0]), .F1(Func[1]),
    .F2(Func[2]), .F3(Func[3]), .F4(Func[4]), .F5(Func[5]), .S2(ALU_OP[0]), .S1(ALU_OP[1]), .S0(ALU_OP[2]));
  \控制信号发生器  \u_控制信号发生器_1  (
    .OP0(OP[0]), .OP1(OP[1]), .OP2(OP[2]), .OP3(OP[3]), .OP4(OP[4]), .in_6(OP[5]), .OP5(Func[0]),
    .F0(Func[1]), .F1(Func[2]), .F2(Func[3]), .F3(Func[4]), .F4(Func[5]), .F5(in_3), .ALUB_src(ALUB_src),
    .SigneExt(SigneExt), .Beq(Beq), .NPCOP_src(NPCOP_src), .Jump(Jump), .RegD_src(RegD_src),
    .RegA3_src(RegA3_src), .RFWrite(RFWrite), .DMWr(DMWr));

  // Other names for the same wires on the sheet: OP_CODE[5:0] = OP

  // Notes on the sheet:
  //   运算器控制器，根据指令生成运算器功能选择信号
endmodule

// 运算控制信号发射器
module \运算控制信号自动生成器  (
  input  OP0,
  input  OP1,
  input  OP2,
  input  OP3,
  input  OP4,
  input  OP5,
  input  F0,
  input  F1,
  input  F2,
  input  F3,
  input  F4,
  input  F5,
  output S2,
  output S1,
  output S0
);

  wire Add, and_2_out, and_3_out, comparator_4_eq, comparator_6_eq, comparator_7_eq, comparator_8_eq,
       comparator_9_eq, jal, LW, SW;

  Comparator #(.width(6), .mode("twosComplement")) comparator_1 (
    .a({OP5, OP4, OP3, OP2, OP1, OP0}), .b(6'b100000), .eq(LW));  // open: gt, lt
  Comparator #(.width(6), .mode("twosComplement")) comparator_2 (
    .a({OP5, OP4, OP3, OP2, OP1, OP0}), .b(6'b101011), .eq(SW));  // open: gt, lt
  Comparator #(.width(6), .mode("twosComplement")) comparator_3 (
    .a({OP5, OP4, OP3, OP2, OP1, OP0}), .b(6'b001101), .eq(S1));  // open: gt, lt
  Comparator #(.width(6), .mode("twosComplement")) comparator_4 (
    .a({OP5, OP4, OP3, OP2, OP1, OP0}), .b(6'b000100), .eq(comparator_4_eq));  // open: gt, lt
  Comparator #(.width(6), .mode("twosComplement")) comparator_5 (
    .a({OP5, OP4, OP3, OP2, OP1, OP0}), .b(6'b000011), .eq(jal));  // open: gt, lt
  Comparator #(.width(6), .mode("twosComplement")) comparator_6 (
    .a({OP5, OP4, OP3, OP2, OP1, OP0}), .b({6{1'b0}}), .eq(comparator_6_eq));  // open: gt, lt
  Comparator #(.width(6), .mode("twosComplement")) comparator_7 (
    .a({F5, F4, F3, F2, F1, F0}), .b(6'b100000), .eq(comparator_7_eq));  // open: gt, lt
  Comparator #(.width(6), .mode("twosComplement")) comparator_8 (
    .a({F5, F4, F3, F2, F1, F0}), .b(6'b100010), .eq(comparator_8_eq));  // open: gt, lt
  Comparator #(.width(6), .mode("twosComplement")) comparator_9 (
    .a({F5, F4, F3, F2, F1, F0}), .b(6'b101010), .eq(comparator_9_eq));  // open: gt, lt
  and and_1 (Add, comparator_6_eq, comparator_7_eq);
  and and_2 (and_2_out, comparator_6_eq, comparator_8_eq);
  and and_3 (and_3_out, comparator_6_eq, comparator_9_eq);
  or or_1 (S2, comparator_4_eq, S1);
  or or_2 (S0, S1, comparator_4_eq, and_2_out, and_3_out);

  // Notes on the sheet:
  //   LW
  //   SW
  //   orl
  //   beq
  //   jal
  //   Rtype
  //   Add
  //   Sub
  //   Sit
endmodule

// 控制信号发生器
module \控制信号发生器  (
  input  OP0,
  input  OP1,
  input  OP2,
  input  OP3,
  input  OP4,
  input  in_6,
  input  OP5,
  input  F0,
  input  F1,
  input  F2,
  input  F3,
  input  F4,
  input  F5,
  output ALUB_src,
  output SigneExt,
  output Beq,
  output NPCOP_src,
  output Jump,
  output [1:0] RegD_src,
  output RegA3_src,
  output RFWrite,
  output DMWr
);

  wire Add, comparator_2_eq, comparator_4_eq, comparator_7_eq, comparator_8_eq, comparator_9_eq, Sub;

  Comparator #(.width(6), .mode("twosComplement")) comparator_1 (
    .a({OP5, OP4, OP3, OP2, OP1, OP0}), .b(6'b100000), .eq(DMWr));  // open: gt, lt
  Comparator #(.width(6), .mode("twosComplement")) comparator_2 (
    .a({OP5, OP4, OP3, OP2, OP1, OP0}), .b(6'b101011), .eq(comparator_2_eq));  // open: gt, lt
  Comparator #(.width(6), .mode("twosComplement")) comparator_3 (
    .a({OP5, OP4, OP3, OP2, OP1, OP0}), .b(6'b001101), .eq(RegD_src[1]));  // open: gt, lt
  Comparator #(.width(6), .mode("twosComplement")) comparator_4 (
    .a({OP5, OP4, OP3, OP2, OP1, OP0}), .b(6'b000100), .eq(comparator_4_eq));  // open: gt, lt
  Comparator #(.width(6), .mode("twosComplement")) comparator_5 (
    .a({OP5, OP4, OP3, OP2, OP1, OP0}), .b(6'b000011), .eq(Jump));  // open: gt, lt
  Comparator #(.width(6), .mode("twosComplement")) comparator_6 (
    .a({OP5, OP4, OP3, OP2, OP1, OP0}), .b({6{1'b0}}), .eq(RegA3_src));  // open: gt, lt
  Comparator #(.width(6), .mode("twosComplement")) comparator_7 (
    .a({F5, F4, F3, F2, F1, F0}), .b(6'b100000), .eq(comparator_7_eq));  // open: gt, lt
  Comparator #(.width(6), .mode("twosComplement")) comparator_8 (
    .a({F5, F4, F3, F2, F1, F0}), .b(6'b100010), .eq(comparator_8_eq));  // open: gt, lt
  Comparator #(.width(6), .mode("twosComplement")) comparator_9 (
    .a({F5, F4, F3, F2, F1, F0}), .b(6'b101010), .eq(comparator_9_eq));  // open: gt, lt
  and and_1 (Add, RegA3_src, comparator_7_eq);
  and and_2 (Sub, RegA3_src, comparator_8_eq);
  and and_3 (RegD_src[0], RegA3_src, comparator_9_eq);
  or or_1 (ALUB_src, DMWr, comparator_2_eq, RegD_src[1]);
  or or_2 (SigneExt, DMWr, comparator_2_eq, comparator_4_eq);
  and and_4 (Beq, in_6, comparator_4_eq);
  or or_3 (RFWrite, RegA3_src, RegD_src[1], DMWr);

  assign NPCOP_src = Jump;

  // Notes on the sheet:
  //   LW
  //   SW
  //   orl
  //   beq
  //   jal
  //   Rtype
  //   Add
  //   Sub
  //   Sit
endmodule

// ALU
module MIPS_ALU (
  input  [2:0] AluOp,
  input  [31:0] X,
  input  [31:0] Y,
  output OF,
  output UOF,
  output ZF,
  output [31:0] S
);

  wire comparator_1_lt, \n1_2_32位可控加减器_3_p5 , \n1_2_32位可控加减器_3_p6 , \n1_2_32位可控加减器_3_p7 ,
       \n1_2_32位可控加减器_4_p3 , \n1_2_32位可控加减器_5_p4 , \n1_2_32位可控加减器_6_p4 , xor_2_out, xor_3_out;
  wire [31:0] and_1_out, bit_extender_1_out, buffer_1_out, \n1_2_32位可控加减器_1_p4 , \n1_2_32位可控加减器_2_p4 ,
       not_1_out, or_1_out, xor_1_out;

  // _1_2_32位可控加减器 1_2_32位可控加减器_1: pin names not known; wires that end beside it: AluOp[0], Y, X, \n1_2_32位可控加减器_1_p4 
  // _1_2_32位可控加减器 1_2_32位可控加减器_2: pin names not known; wires that end beside it: AluOp[0], Y, X, \n1_2_32位可控加减器_2_p4 
  assign buffer_1_out = Y;  // Buffer buffer_1, 32 bits wide
  assign not_1_out = ~Y;  // NOT_Gate not_1, 32 bits wide
  assign and_1_out = Y & X;  // AND_Gate and_1, 32 bits wide
  assign or_1_out = Y | X;  // OR_Gate or_1, 32 bits wide
  assign xor_1_out = Y ^ X;  // XOR_Gate xor_1, 32 bits wide
  Comparator #(.width(32), .mode("twosComplement")) comparator_1 (.a(X), .b(Y), .lt(comparator_1_lt));  // open: gt, eq
  assign bit_extender_1_out = {{31{1'b0}}, comparator_1_lt};  // Bit_Extender bit_extender_1
  Multiplexer #(.select(3), .width(32), .disabled("Z"), .enable("false")) multiplexer_1 (
    .in0(\n1_2_32位可控加减器_1_p4 ), .in1(\n1_2_32位可控加减器_2_p4 ), .in2(and_1_out), .in3(or_1_out), .in4(xor_1_out),
    .in5(buffer_1_out), .in6(not_1_out), .in7(bit_extender_1_out), .out(S), .sel(AluOp));
  // Probe on X
  // Probe on Y
  // Probe on S
  Comparator #(.width(32), .mode("twosComplement")) comparator_2 (.a(S), .b({32{1'b0}}), .eq(ZF));  // open: gt, lt
  // Probe on X
  // Probe on Y
  // Probe on S
  // _1_2_32位可控加减器 1_2_32位可控加减器_3: pin names not known; wires that end beside it: AluOp[0], X, Y, AluOp[0], \n1_2_32位可控加减器_3_p5 , \n1_2_32位可控加减器_3_p6 , \n1_2_32位可控加减器_3_p7 
  // _1_2_32位可控加减器 1_2_32位可控加减器_4: pin names not known; wires that end beside it: X, Y, \n1_2_32位可控加减器_4_p3 
  // _1_2_32位可控加减器 1_2_32位可控加减器_5: pin names not known; wires that end beside it: AluOp[0], X, Y, \n1_2_32位可控加减器_5_p4 
  // _1_2_32位可控加减器 1_2_32位可控加减器_6: pin names not known; wires that end beside it: AluOp[0], X, Y, \n1_2_32位可控加减器_6_p4 
  xor xor_2 (xor_2_out, \n1_2_32位可控加减器_3_p5 , \n1_2_32位可控加减器_3_p7 );
  xor xor_3 (xor_3_out, \n1_2_32位可控加减器_3_p6 , \n1_2_32位可控加减器_4_p3 );
  Multiplexer #(.select(3), .width(1), .disabled("Z"), .enable("false")) multiplexer_2 (
    .in0(xor_2_out), .in1(xor_3_out), .in2(1'b0), .in3(1'b0), .in4(1'b0), .in5(1'b0), .in6(1'b0), .in7(1'b0),
    .out(OF), .sel(AluOp));
  Multiplexer #(.select(3), .width(1), .disabled("Z"), .enable("false")) multiplexer_3 (
    .in0(\n1_2_32位可控加减器_6_p4 ), .in1(\n1_2_32位可控加减器_5_p4 ), .in2(1'b0), .in3(1'b0), .in4(1'b0), .in5(1'b0),
    .in6(1'b0), .in7(1'b0), .out(UOF), .sel(AluOp));

  // Notes on the sheet:
  //   000 ：S=X+Y
  //   输入引脚区
  //   注：不能增加任何输入输出端口信号
  //   001：S=X-Y
  //   010 ：S=X&Y
  //   输出引脚区
  //   实现一个32位的ALU，可以由AluOP控制实现8种运算操作，并产生正确的标志位。AluOp与运算关系如下：
  //   011：S=X|Y
  //   100 ：S=X^Y
  //   =
  //   有符号数
  //   101 ：S=Y
  //   =
  //   结果测试区
  //   110 ：S=~Y
  //   无符号数
  //   111 ：S=X<Y?1:0
endmodule

module MIPS_Regifile (
  input  CLK,
  input  WE,
  input  [4:0] RA1,
  input  [4:0] RA2,
  input  [31:0] Din,
  input  [4:0] WA,
  output [31:0] RD1,
  output [31:0] RD2
);

  wire button_1_out, decoder_1_out0, decoder_1_out1, decoder_1_out2, decoder_1_out3;
  wire [31:0] multiplexer_3_out, \n2_2_8_32寄存器_1_rd1 , \n2_2_8_32寄存器_1_rd2 , \n2_2_8_32寄存器_2_rd1 ,
       \n2_2_8_32寄存器_2_rd2 , \n2_2_8_32寄存器_3_rd1 , \n2_2_8_32寄存器_3_rd2 , \n2_2_8_32寄存器_4_rd1 ,
       \n2_2_8_32寄存器_4_rd2 ;

  Decoder #(.select(2), .tristate("false"), .disabled("Z"), .enable("false")) decoder_1 (
    .out0(decoder_1_out0), .out1(decoder_1_out1), .out2(decoder_1_out2), .out3(decoder_1_out3), .sel(WA[4:3]));
  \_2_2_8_32寄存器  \u_2_2_8_32寄存器_1  (
    .WA(WA), .RA1(RA1[2:0]), .Din(Din), .RD1(\n2_2_8_32寄存器_1_rd1 ), .RA2(RA2[2:0]),
    .RD2(\n2_2_8_32寄存器_1_rd2 ), .CS(decoder_1_out0), .WE(CLK), .CLK(WE));
  \_2_2_8_32寄存器  \u_2_2_8_32寄存器_2  (
    .WA(WA), .RA1(RA1[2:0]), .Din(Din), .RD1(\n2_2_8_32寄存器_2_rd1 ), .RA2(RA2[2:0]),
    .RD2(\n2_2_8_32寄存器_2_rd2 ), .CS(decoder_1_out2), .WE(CLK), .CLK(WE));
  \_2_2_8_32寄存器  \u_2_2_8_32寄存器_3  (
    .WA(WA), .RA1(RA1[2:0]), .Din(Din), .RD1(\n2_2_8_32寄存器_3_rd1 ), .RA2(RA2[2:0]),
    .RD2(\n2_2_8_32寄存器_3_rd2 ), .CS(decoder_1_out1), .WE(CLK), .CLK(WE));
  \_2_2_8_32寄存器  \u_2_2_8_32寄存器_4  (
    .WA(WA), .RA1(RA1[2:0]), .Din(Din), .RD1(\n2_2_8_32寄存器_4_rd1 ), .RA2(RA2[2:0]),
    .RD2(\n2_2_8_32寄存器_4_rd2 ), .CS(decoder_1_out3), .WE(CLK), .CLK(WE));
  Multiplexer #(.select(2), .width(32), .disabled("Z"), .enable("false")) multiplexer_1 (
    .in0(\n2_2_8_32寄存器_1_rd2 ), .in1(\n2_2_8_32寄存器_3_rd2 ), .in2(\n2_2_8_32寄存器_2_rd2 ),
    .in3(\n2_2_8_32寄存器_4_rd2 ), .out(RD2), .sel(RA2[4:3]));
  Multiplexer #(.select(2), .width(32), .disabled("Z"), .enable("false")) multiplexer_2 (
    .in0(\n2_2_8_32寄存器_1_rd1 ), .in1(\n2_2_8_32寄存器_3_rd1 ), .in2(\n2_2_8_32寄存器_2_rd1 ),
    .in3(\n2_2_8_32寄存器_4_rd1 ), .out(RD1), .sel(RA1[4:3]));
  Multiplexer #(.select(1), .width(32), .disabled("Z"), .enable("false")) multiplexer_3 (
    .in0(RD1), .in1(RD2), .out(multiplexer_3_out), .sel(button_1_out));
  Button button_1 (.out(button_1_out));
  Hex_Digit_Display hex_digit_display_1 (.value(multiplexer_3_out[15:12]));  // open: dp
  Hex_Digit_Display hex_digit_display_2 (.value(multiplexer_3_out[31:28]));  // open: dp
  Hex_Digit_Display hex_digit_display_3 (.value(multiplexer_3_out[11:8]));  // open: dp
  Hex_Digit_Display hex_digit_display_4 (.value(multiplexer_3_out[7:4]));  // open: dp
  Hex_Digit_Display hex_digit_display_5 (.value(multiplexer_3_out[23:20]));  // open: dp
  Hex_Digit_Display hex_digit_display_6 (.value(multiplexer_3_out[27:24]));  // open: dp
  Hex_Digit_Display hex_digit_display_7 (.value(multiplexer_3_out[3:0]));  // open: dp
  Hex_Digit_Display hex_digit_display_8 (.value(multiplexer_3_out[19:16]));  // open: dp

  // Notes on the sheet:
  //   输入引脚区
  //   注：不能增加任何输入输出端口信号
  //   输出引脚区
  //   实现MIPS寄存器组，32个寄存器可以采用模块化方法实现，模块规模不限，注意0号寄存器恒为0
  //   输出数据测试区
endmodule

module NPC (
  input  Zero,
  input  Jump,
  input  [31:0] Imm,
  input  Clk,
  input  Branch,
  input  RST,
  output [31:0] PC
);

  wire and_1_out, or_1_out;
  wire [31:0] adder_1_out, adder_2_out, multiplexer_1_out, multiplexer_2_out;

  and and_1 (and_1_out, Zero, Branch);
  or or_1 (or_1_out, Jump, and_1_out);
  Adder #(.width(32)) adder_1 (.a(PC), .b(32'h4), .out(adder_1_out));  // open: cin, cout
  Adder #(.width(32)) adder_2 (.a(Imm), .b(adder_1_out), .out(adder_2_out));  // open: cin, cout
  Multiplexer #(.select(1), .width(32), .disabled("Z"), .enable("false")) multiplexer_1 (
    .in0(adder_1_out), .in1(adder_2_out), .out(multiplexer_1_out), .sel(or_1_out));
  Multiplexer #(.select(1), .width(32), .disabled("Z"), .enable("false")) multiplexer_2 (
    .in0(multiplexer_1_out), .in1(Imm), .out(multiplexer_2_out), .sel(Jump));
  Register #(.width(32), .trigger("rising"), .Select("low")) register_1 (
    .D(multiplexer_2_out), .Q(PC), .clk(Clk), .clr(RST));  // open: en

  // Notes on the sheet:
  //   RST: pull=down
  //   Branch: pull=down
  //   Imm: pull=down
  //   Jump: pull=down
  //   Clk: pull=down
  //   Zero: pull=down
  //   输入信号
  //   输出信号
endmodule

module ID (
  input  [31:0] Instruction,
  output [5:0] OP,
  output [5:0] Funct,
  output [4:0] Shamt,
  output [4:0] rs,
  output [4:0] rt,
  output [4:0] rd,
  output [15:0] Imm16,
  output [25:0] Imm20
);


  assign Funct = Instruction[5:0];
  assign Imm16 = Instruction[15:0];
  assign Imm20 = Instruction[25:0];
  assign OP = Instruction[31:26];
  assign rd = Instruction[15:11];
  assign rs = Instruction[25:21];
  assign rt = Instruction[20:16];
  assign Shamt = Instruction[10:6];

  // Other names for the same wires on the sheet: Imm26[25:0] = Instruction[25:0]
endmodule
