// Logisim project 实验3-EXP3_MIPSCPU.circ as structural Verilog: 8 circuits, main circuit ◇单周期MIPS
module \单周期MIPS  (
  output [31:0] PC,
  output [31:0] IR,
  output [31:0] RDin,
  output [31:0] MDin,
  output [31:0] LedData
);

  wire CLK, Go, Rst;
  wire [4:0] id_1_rs, id_1_rt;
  wire [5:0] Funct, OP;
  wire [9:0] mips_alu_1_p2, npc_1_p3;
  wire [15:0] \总周期数 ;
  wire [31:0] mips_regifile_1_r1, rom_1_data;

  Clock clock_1 (.out(CLK));
  Button button_1 (.out(Rst));
  // DipSwitch #(.NSwitches(1)) dipswitch_1: pin names not known; wires that end beside it: Go
  // NPC npc_1: pin names not known; wires that end beside it: CLK, Rst, npc_1_p3
  Hex_Digit_Display hex_digit_display_1 (.value(LedData[31:28]));  // open: dp
  Hex_Digit_Display hex_digit_display_2 (.value(LedData[27:24]));  // open: dp
  Hex_Digit_Display hex_digit_display_3 (.value(LedData[23:20]));  // open: dp
  Hex_Digit_Display hex_digit_display_4 (.value(LedData[15:12]));  // open: dp
  Hex_Digit_Display hex_digit_display_5 (.value(LedData[19:16]));  // open: dp
  ROM #(.addrWidth(10), .dataWidth(32), .Select("high")) rom_1 (.addr(npc_1_p3), .data(rom_1_data));
  Hex_Digit_Display hex_digit_display_6 (.value(LedData[7:4]));  // open: dp
  Hex_Digit_Display hex_digit_display_7 (.value(LedData[11:8]));  // open: dp
  // Probe on \总周期数 
  ID id_1 (
    .Instruction(rom_1_data), .OP(OP), .Funct(Funct), .rs(id_1_rs), .rt(id_1_rt));  // open: Shamt, rd, Imm16, Imm20
  \单周期硬布线控制器  \u_单周期硬布线控制器_1  (.Func(Funct), .OP(OP));  // open: ALU_OP, C1, C2, C3, C4, C5, C6, C7, C8
  Hex_Digit_Display hex_digit_display_8 (.value(LedData[3:0]));  // open: dp
  MIPS_Regifile mips_regifile_1 (
    .R1(mips_regifile_1_r1), .R1_num(id_1_rs), .R2_num(id_1_rt));  // open: Din, Clk, R2, WE, W_num
  // MIPS_ALU mips_alu_1: pin names not known; wires that end beside it: mips_regifile_1_r1, mips_alu_1_p2
  RAM #(.addrWidth(10), .dataWidth(32), .bus("separate"), .Select("high")) ram_1 (.addr(mips_alu_1_p2));  // open: din, data, str, sel, clk, ld, clr

  // Notes on the sheet:
  //   总复位信号应将除ROM以外所有存储组件全部清零
  //   指令存储器
  //   数码管输出
  //   contents of rom_1 (hex, n*v repeats v):
  //   8c030000 34050001 34020001 20630001 2020 852020 a22820 a3082a 10200001 c000c05 ac040004 c000c0b
  //   数码管输出应该用寄存器锁存，否则显示数据只能一闪而过
  //   此连线不得改动
  //   此连线不得改动
  //   此连线不得改动
  //   为方便自动评测，需要输出PC，IR，寄存器文件写入端口RDin，内存写入端口MDin等信号
  //   数据存储器
endmodule

// 单周期硬布线控制器
module \单周期硬布线控制器  (
  input  [5:0] OP,
  input  [5:0] Func,
  output [2:0] ALU_OP,
  output C1,
  output C2,
  output C3,
  output C4,
  output C5,
  output C6,
  output C7,
  output C8
);

  \运算控制信号自动生成器  \u_运算控制信号自动生成器_1  (
    .OP0(OP[0]), .OP1(OP[1]), .OP2(OP[2]), .OP3(OP[3]), .OP4(OP[4]), .OP5(OP[5]), .F0(Func[0]), .F1(Func[1]),
    .F2(Func[2]), .F3(Func[3]), .F4(Func[4]), .F5(Func[5]), .S0(ALU_OP[0]), .S1(ALU_OP[1]), .S2(ALU_OP[2]));
  \控制信号发生器  \u_控制信号发生器_1  (
    .OP0(OP[0]), .OP1(OP[1]), .OP2(OP[2]), .OP3(OP[3]), .OP4(OP[4]), .OP5(OP[5]), .F0(Func[0]), .F1(Func[1]),
    .F2(Func[2]), .F3(Func[3]), .F4(Func[4]), .F5(Func[5]), .Jump(C1), .Beq(C2), .SigneExt(C3), .RFWrite(C4),
    .RegD_src(C5), .RegA3_src(C6), .ALUB_src(C7), .DMWr(C8));

  // Other names for the same wires on the sheet: OP_CODE[5:0] = OP

  // Notes on the sheet:
  //   运算器控制器，根据指令生成运算器功能选择信号
endmodule

// 运算控制信号发射器
module \运算控制信号自动生成器  (
  input  OP0,
  input  OP1,
  input  OP2,
  input  OP3,
  input  OP4,
  input  OP5,
  input  F0,
  input  F1,
  input  F2,
  input  F3,
  input  F4,
  input  F5,
  output S0,
  output S1,
  output S2
);
endmodule

// 控制信号发生器
module \控制信号发生器  (
  input  OP0,
  input  OP1,
  input  OP2,
  input  OP3,
  input  OP4,
  input  OP5,
  input  F0,
  input  F1,
  input  F2,
  input  F3,
  input  F4,
  input  F5,
  output Jump,
  output Beq,
  output SigneExt,
  output RFWrite,
  output RegD_src,
  output RegA3_src,
  output ALUB_src,
  output DMWr
);
endmodule

// ALU
module MIPS_ALU (
  input  [31:0] X,
  input  [31:0] Y,
  input  [2:0] AluOP,
  output OF,
  output UOF,
  output ZF,
  output [31:0] S
);


  // Notes on the sheet:
  //   不要改变此引脚区域内容，也不要改变ALU封装形式
  //   输入引脚
endmodule

module MIPS_Regifile (
  input  [31:0] Din,
  input  Clk,
  input  WE,
  input  [4:0] R1_num,
  input  [4:0] W_num,
  input  [4:0] R2_num,
  output [31:0] R1,
  output [31:0] R2
);
endmodule

module NPC (
  input  Zero,
  input  Jump,
  input  [31:0] Imm,
  input  Clk,
  input  Branch,
  input  RST,
  output [31:0] PC
);


  // Notes on the sheet:
  //   Branch: pull=down
  //   Jump: pull=down
  //   Clk: pull=down
  //   Imm: pull=down
  //   RST: pull=down
  //   Zero: pull=down
  //   输入信号
  //   输出信号
endmodule

module ID (
  input  [31:0] Instruction,
  output [5:0] OP,
  output [5:0] Funct,
  output [4:0] Shamt,
  output [4:0] rs,
  output [4:0] rt,
  output [4:0] rd,
  output [15:0] Imm16,
  output [25:0] Imm20
);


  // Other names for the same wires on the sheet: Imm26[25:0] = Imm20
endmodule
