// Logisim project 11.11.circ as structural Verilog
module \一位全加器  (
  input  An,
  input  Bn,
  input  Cn_1,
  output Cn,
  output Fn
);

  wire nand_1_out, nand_2_out, xor_1_out;

  nand nand_1 (nand_1_out, An, Bn);
  nand nand_2 (nand_2_out, Cn_1, xor_1_out);
  xor xor_1 (xor_1_out, An, Bn);
  nand nand_3 (Cn, nand_1_out, nand_2_out);
  xor xor_2 (Fn, Cn_1, xor_1_out);
endmodule

module \_8位可控加法器  (
  input  Cin,
  input  K1,
  input  K0,
  input  [7:0] \Y加数_减数 ,
  input  [7:0] \X被加数_被减数 ,
  output \ZF_结果为0_ZF_1 ,
  output \OF_有溢出_OF_1 ,
  output \SF_结果为负_SF_1 ,
  output [7:0] \计算结果 ,
  output \CF_进位_借位_有进位_借位_CF_1 ,
  output Cout
);

  wire and_1_out, and_2_out, not_1_out, or_1_out, xor_3_out, xor_4_out, xor_5_out, xor_6_out, xor_7_out,
       xor_8_out, xor_9_out, xor_10_out, xor_11_out, \一位全加器_2_cn , \一位全加器_3_cn , \一位全加器_4_cn , \一位全加器_5_cn ,
       \一位全加器_6_cn , \一位全加器_7_cn , \一位全加器_8_cn ;

  xor xor_1 (\CF_进位_借位_有进位_借位_CF_1 , Cout, K1);
  \一位全加器  \u_一位全加器_1  (.An(\X被加数_被减数 [7]), .Bn(xor_3_out), .Cn_1(\一位全加器_2_cn ), .Cn(Cout), .Fn(\SF_结果为负_SF_1 ));
  xor xor_2 (\OF_有溢出_OF_1 , Cout, \一位全加器_2_cn );
  xor xor_3 (xor_3_out, \Y加数_减数 [7], K1);
  \一位全加器  \u_一位全加器_2  (.An(\X被加数_被减数 [6]), .Bn(xor_4_out), .Cn_1(\一位全加器_3_cn ), .Cn(\一位全加器_2_cn ), .Fn(\计算结果 [6]));
  xor xor_4 (xor_4_out, \Y加数_减数 [6], K1);
  \一位全加器  \u_一位全加器_3  (.An(\X被加数_被减数 [5]), .Bn(xor_5_out), .Cn_1(\一位全加器_4_cn ), .Cn(\一位全加器_3_cn ), .Fn(\计算结果 [5]));
  xor xor_5 (xor_5_out, \Y加数_减数 [5], K1);
  \一位全加器  \u_一位全加器_4  (.An(\X被加数_被减数 [4]), .Bn(xor_6_out), .Cn_1(\一位全加器_5_cn ), .Cn(\一位全加器_4_cn ), .Fn(\计算结果 [4]));
  xor xor_6 (xor_6_out, \Y加数_减数 [4], K1);
  \一位全加器  \u_一位全加器_5  (.An(\X被加数_被减数 [3]), .Bn(xor_7_out), .Cn_1(\一位全加器_6_cn ), .Cn(\一位全加器_5_cn ), .Fn(\计算结果 [3]));
  xor xor_7 (xor_7_out, \Y加数_减数 [3], K1);
  \一位全加器  \u_一位全加器_6  (.An(\X被加数_被减数 [2]), .Bn(xor_8_out), .Cn_1(\一位全加器_7_cn ), .Cn(\一位全加器_6_cn ), .Fn(\计算结果 [2]));
  nor nor_1 (\ZF_结果为0_ZF_1 , \SF_结果为负_SF_1 , \计算结果 [6], \计算结果 [5], \计算结果 [4], \计算结果 [3], \计算结果 [2], \计算结果 [1], \计算结果 [0]);
  xor xor_8 (xor_8_out, \Y加数_减数 [2], K1);
  \一位全加器  \u_一位全加器_7  (.An(\X被加数_被减数 [1]), .Bn(xor_9_out), .Cn_1(\一位全加器_8_cn ), .Cn(\一位全加器_7_cn ), .Fn(\计算结果 [1]));
  xor xor_9 (xor_9_out, \Y加数_减数 [1], K1);
  \一位全加器  \u_一位全加器_8  (.An(\X被加数_被减数 [0]), .Bn(xor_10_out), .Cn_1(or_1_out), .Cn(\一位全加器_8_cn ), .Fn(\计算结果 [0]));
  xor xor_10 (xor_10_out, \Y加数_减数 [0], K1);
  and and_1 (and_1_out, K1, not_1_out);
  not not_1 (not_1_out, Cin);
  or or_1 (or_1_out, and_1_out, and_2_out);
  and and_2 (and_2_out, Cin, xor_11_out);
  xor xor_11 (xor_11_out, K1, K0);

  assign \计算结果 [7] = \SF_结果为负_SF_1 ;

  // Notes on the sheet:
  //   K1 K0=0 0:X+Y
  //   K1 K0=0 1:X+Y+Cin
  //   K1 K0=1 0:X-Y
  //   K1 K0=1 1:X-Y-Cin
endmodule

module \_32位可控加减器2_0  (
  input  in_1,
  input  [31:0] in_2,
  input  [31:0] in_3,
  output \ZF_结果为0_ZF_1 ,
  output [31:0] out_5,
  output \SF_结果为负_SF_1 ,
  output \OF_有溢出_OF_1 ,
  output \CF_进位_借位_有进位_借位_CF_1 
);

  wire \n8位可控加法器_1_cout , \n8位可控加法器_1_zf_结果为0_zf_1 , \n8位可控加法器_2_cf_进位_借位_有进位_借位_cf_1 ,
       \n8位可控加法器_2_zf_结果为0_zf_1 , \n8位可控加法器_3_cf_进位_借位_有进位_借位_cf_1 , \n8位可控加法器_3_zf_结果为0_zf_1 ,
       \n8位可控加法器_4_cf_进位_借位_有进位_借位_cf_1 , \n8位可控加法器_4_zf_结果为0_zf_1 ;

  xor xor_1 (\CF_进位_借位_有进位_借位_CF_1 , in_1, \n8位可控加法器_1_cout );
  \_8位可控加法器  \u_8位可控加法器_1  (
    .\OF_有溢出_OF_1 (\OF_有溢出_OF_1 ), .\计算结果 (out_5[31:24]), .\Y加数_减数 (in_3[31:24]), .\X被加数_被减数 (in_2[31:24]),
    .K0(1'b1), .K1(in_1), .Cin(\n8位可控加法器_2_cf_进位_借位_有进位_借位_cf_1 ),
    .\ZF_结果为0_ZF_1 (\n8位可控加法器_1_zf_结果为0_zf_1 ), .Cout(\n8位可控加法器_1_cout ));  // open: CF_进位_借位_有进位_借位_CF_1, SF_结果为负_SF_1
  and and_1 (\ZF_结果为0_ZF_1 , \n8位可控加法器_1_zf_结果为0_zf_1 , \n8位可控加法器_2_zf_结果为0_zf_1 , \n8位可控加法器_3_zf_结果为0_zf_1 , \n8位可控加法器_4_zf_结果为0_zf_1 );
  \_8位可控加法器  \u_8位可控加法器_2  (
    .\CF_进位_借位_有进位_借位_CF_1 (\n8位可控加法器_2_cf_进位_借位_有进位_借位_cf_1 ), .\计算结果 (out_5[23:16]),
    .\Y加数_减数 (in_3[23:16]), .\X被加数_被减数 (in_2[23:16]), .K0(1'b1), .K1(in_1),
    .Cin(\n8位可控加法器_3_cf_进位_借位_有进位_借位_cf_1 ), .\ZF_结果为0_ZF_1 (\n8位可控加法器_2_zf_结果为0_zf_1 ));  // open: OF_有溢出_OF_1, SF_结果为负_SF_1, Cout
  \_8位可控加法器  \u_8位可控加法器_3  (
    .\CF_进位_借位_有进位_借位_CF_1 (\n8位可控加法器_3_cf_进位_借位_有进位_借位_cf_1 ), .\计算结果 (out_5[15:8]), .\Y加数_减数 (in_3[15:8]),
    .\X被加数_被减数 (in_2[15:8]), .K0(1'b1), .K1(in_1), .Cin(\n8位可控加法器_4_cf_进位_借位_有进位_借位_cf_1 ),
    .\ZF_结果为0_ZF_1 (\n8位可控加法器_3_zf_结果为0_zf_1 ));  // open: OF_有溢出_OF_1, SF_结果为负_SF_1, Cout
  \_8位可控加法器  \u_8位可控加法器_4  (
    .\CF_进位_借位_有进位_借位_CF_1 (\n8位可控加法器_4_cf_进位_借位_有进位_借位_cf_1 ), .\计算结果 (out_5[7:0]), .\Y加数_减数 (in_3[7:0]),
    .\X被加数_被减数 (in_2[7:0]), .K0(1'b1), .K1(in_1), .Cin(1'b0), .\ZF_结果为0_ZF_1 (\n8位可控加法器_4_zf_结果为0_zf_1 ));  // open: OF_有溢出_OF_1, SF_结果为负_SF_1, Cout

  assign \SF_结果为负_SF_1  = out_5[31];
endmodule

module \_32位ALU  (
  input  [31:0] x,
  input  [31:0] y,
  input  [2:0] AluOp,
  output OF,
  output UOF,
  output ZF,
  output [31:0] out_7,
  output \S_只有111时作用_判断x_y大小 
);

  wire and_1_out, and_2_out, \n32位可控加减器2_0_1_cf_进位_借位_有进位_借位_cf_1 , \n32位可控加减器2_0_1_of_有溢出_of_1 ,
       \n32位可控加减器2_0_2_cf_进位_借位_有进位_借位_cf_1 , \n32位可控加减器2_0_2_of_有溢出_of_1 , \n32位比较_1_out_4 , not_2_out,
       not_3_out;
  wire [31:0] bit_extender_1_out, controlled_buffer_2_out, \n8选1_1_out_12 , \n32位与_1_out_3 ,
       \n32位可控加减器2_0_1_out_5 , \n32位可控加减器2_0_2_out_5 , \n32位异或_1_out_3 , \n32位或_1_out_3 , not_1_out,
       \赋值_1_out_2 ;

  \_32位异或  \u_32位异或_1  (.in_2(x), .in_1(y), .out_3(\n32位异或_1_out_3 ));
  \_32位或  \u_32位或_1  (.in_2(x), .in_1(y), .out_3(\n32位或_1_out_3 ));
  \_32位与  \u_32位与_1  (.in_2(x), .in_1(y), .out_3(\n32位与_1_out_3 ));
  \_32位可控加减器2_0  \u_32位可控加减器2_0_1  (
    .\CF_进位_借位_有进位_借位_CF_1 (\n32位可控加减器2_0_1_cf_进位_借位_有进位_借位_cf_1 ),
    .\OF_有溢出_OF_1 (\n32位可控加减器2_0_1_of_有溢出_of_1 ), .out_5(\n32位可控加减器2_0_1_out_5 ), .in_2(x), .in_3(y),
    .in_1(1'b0));  // open: SF_结果为负_SF_1, ZF_结果为0_ZF_1
  \_32位可控加减器2_0  \u_32位可控加减器2_0_2  (
    .\CF_进位_借位_有进位_借位_CF_1 (\n32位可控加减器2_0_2_cf_进位_借位_有进位_借位_cf_1 ),
    .\OF_有溢出_OF_1 (\n32位可控加减器2_0_2_of_有溢出_of_1 ), .\ZF_结果为0_ZF_1 (ZF), .out_5(\n32位可控加减器2_0_2_out_5 ),
    .in_2(x), .in_3(y), .in_1(1'b1));  // open: SF_结果为负_SF_1
  \赋值  \u_赋值_1  (.in_1(y), .out_2(\赋值_1_out_2 ));
  \_32位比较  \u_32位比较_1  (.in_1(x), .in_2(y), .out_4(\n32位比较_1_out_4 ));  // open: out_3, out_5
  assign bit_extender_1_out = {{31{\n32位比较_1_out_4 }}, \n32位比较_1_out_4 };  // Bit_Extender bit_extender_1
  assign not_1_out = ~\赋值_1_out_2 ;  // NOT_Gate not_1, 32 bits wide
  and and_1 (and_1_out, \n32位可控加减器2_0_1_cf_进位_借位_有进位_借位_cf_1 , not_2_out);
  not not_2 (not_2_out, AluOp[0]);
  \_32位比较  \u_32位比较_2  (.in_1(x), .in_2(y));  // open: out_3, out_4, out_5
  \_8选1  \u_8选1_1  (
    .in_1(\n32位可控加减器2_0_1_out_5 ), .in_2(\n32位可控加减器2_0_2_out_5 ), .in_3(\n32位与_1_out_3 ),
    .in_4(\n32位或_1_out_3 ), .in_5(\n32位异或_1_out_3 ), .in_6(\赋值_1_out_2 ), .in_7(not_1_out),
    .in_8(bit_extender_1_out), .in_9(AluOp[2]), .in_10(AluOp[1]), .in_11(AluOp[0]), .out_12(\n8选1_1_out_12 ));
  not not_3 (not_3_out, and_2_out);
  and and_2 (and_2_out, AluOp[0], AluOp[1], AluOp[2]);
  or or_1 (UOF, \n32位可控加减器2_0_2_cf_进位_借位_有进位_借位_cf_1 , and_1_out);
  assign out_7 = not_3_out ? \n8选1_1_out_12  : 32'bz;  // Controlled_Buffer controlled_buffer_1
  assign controlled_buffer_2_out = and_2_out ? \n8选1_1_out_12  : 32'bz;  // Controlled_Buffer controlled_buffer_2
  or or_2 (OF, \n32位可控加减器2_0_2_of_有溢出_of_1 , \n32位可控加减器2_0_1_of_有溢出_of_1 );
  Bit_Extender #(.in_width(32), .out_width(1), .\type ("sign")) bit_extender_2 (
    .in(controlled_buffer_2_out), .out(\S_只有111时作用_判断x_y大小 ));

  // Other names for the same wires on the sheet: 加减法 = AluOp[0]; 相等 = ZF
endmodule

module \_32位异或  (
  input  [31:0] in_1,
  input  [31:0] in_2,
  output [31:0] out_3
);

  assign out_3 = in_2 ^ in_1;  // XOR_Gate xor_1, 32 bits wide
endmodule

module \_32位与  (
  input  [31:0] in_1,
  input  [31:0] in_2,
  output [31:0] out_3
);

  assign out_3 = in_2 & in_1;  // AND_Gate and_1, 32 bits wide
endmodule

module \_32位或  (
  input  [31:0] in_1,
  input  [31:0] in_2,
  output [31:0] out_3
);

  assign out_3 = in_2 | in_1;  // OR_Gate or_1, 32 bits wide
endmodule

module \_1位比较  (
  input  in_1,
  input  in_2,
  output \相等 ,
  output \小于 ,
  output \大于 
);

  wire not_2_out, xor_1_out;

  not not_1 (\相等 , xor_1_out);
  xor xor_1 (xor_1_out, in_1, in_2);
  not not_2 (not_2_out, in_2);
  and and_1 (\大于 , not_2_out, in_1);
  nor nor_1 (\小于 , \相等 , \大于 );
endmodule

module \_8位比较  (
  input  [7:0] in_1,
  input  [7:0] in_2,
  output out_3,
  output out_4,
  output out_5
);

  wire and_1_out, and_2_out, \n4位比较_1_out_3 , \n4位比较_1_out_4 , \n4位比较_1_out_5 , \n4位比较_2_out_3 ,
       \n4位比较_2_out_4 , \n4位比较_2_out_5 ;

  \_4位比较  \u_4位比较_1  (
    .in_1(in_1[7:4]), .in_2(in_2[7:4]), .out_3(\n4位比较_1_out_3 ), .out_4(\n4位比较_1_out_4 ),
    .out_5(\n4位比较_1_out_5 ));
  \_4位比较  \u_4位比较_2  (
    .in_1(in_1[3:0]), .in_2(in_2[3:0]), .out_3(\n4位比较_2_out_3 ), .out_4(\n4位比较_2_out_4 ),
    .out_5(\n4位比较_2_out_5 ));
  and and_1 (and_1_out, \n4位比较_1_out_3 , \n4位比较_2_out_4 );
  and and_2 (and_2_out, \n4位比较_1_out_3 , \n4位比较_2_out_5 );
  and and_3 (out_3, \n4位比较_1_out_3 , \n4位比较_2_out_3 );
  or or_1 (out_4, \n4位比较_1_out_4 , and_1_out);
  or or_2 (out_5, and_2_out, \n4位比较_1_out_5 );
endmodule

module \_4位比较  (
  input  [3:0] in_1,
  input  [3:0] in_2,
  output out_3,
  output out_4,
  output out_5
);

  wire and_1_out, and_2_out, and_3_out, and_4_out, and_5_out, and_6_out, \n1位比较_1_大于 , \n1位比较_1_小于 ,
       \n1位比较_1_相等 , \n1位比较_2_大于 , \n1位比较_2_小于 , \n1位比较_2_相等 , \n1位比较_3_大于 , \n1位比较_3_小于 , \n1位比较_3_相等 ,
       \n1位比较_4_大于 , \n1位比较_4_小于 , \n1位比较_4_相等 ;

  \_1位比较  \u_1位比较_1  (.in_1(in_1[3]), .in_2(in_2[3]), .\相等 (\n1位比较_1_相等 ), .\小于 (\n1位比较_1_小于 ), .\大于 (\n1位比较_1_大于 ));
  \_1位比较  \u_1位比较_2  (.in_1(in_1[2]), .in_2(in_2[2]), .\相等 (\n1位比较_2_相等 ), .\小于 (\n1位比较_2_小于 ), .\大于 (\n1位比较_2_大于 ));
  and and_1 (and_1_out, \n1位比较_1_相等 , \n1位比较_2_大于 );
  and and_2 (and_2_out, \n1位比较_1_相等 , \n1位比较_2_小于 );
  \_1位比较  \u_1位比较_3  (.in_1(in_1[1]), .in_2(in_2[1]), .\相等 (\n1位比较_3_相等 ), .\小于 (\n1位比较_3_小于 ), .\大于 (\n1位比较_3_大于 ));
  and and_3 (and_3_out, \n1位比较_1_相等 , \n1位比较_2_相等 , \n1位比较_3_大于 );
  and and_4 (and_4_out, \n1位比较_1_相等 , \n1位比较_2_相等 , \n1位比较_3_小于 );
  \_1位比较  \u_1位比较_4  (.in_1(in_1[0]), .in_2(in_2[0]), .\相等 (\n1位比较_4_相等 ), .\小于 (\n1位比较_4_小于 ), .\大于 (\n1位比较_4_大于 ));
  and and_5 (and_5_out, \n1位比较_3_相等 , \n1位比较_1_相等 , \n1位比较_2_相等 , \n1位比较_4_小于 );
  and and_6 (and_6_out, \n1位比较_3_相等 , \n1位比较_1_相等 , \n1位比较_2_相等 , \n1位比较_4_大于 );
  and and_7 (out_3, \n1位比较_1_相等 , \n1位比较_2_相等 , \n1位比较_3_相等 , \n1位比较_4_相等 );
  or or_1 (out_4, and_5_out, and_4_out, and_2_out, \n1位比较_1_小于 );
  or or_2 (out_5, \n1位比较_1_大于 , and_1_out, and_3_out, and_6_out);
endmodule

module \_16位比较  (
  input  [15:0] in_1,
  input  [15:0] in_2,
  output out_3,
  output out_4,
  output out_5
);

  wire and_1_out, and_2_out, \n8位比较_1_out_3 , \n8位比较_1_out_4 , \n8位比较_1_out_5 , \n8位比较_2_out_3 ,
       \n8位比较_2_out_4 , \n8位比较_2_out_5 ;

  \_8位比较  \u_8位比较_1  (
    .in_1(in_1[15:8]), .in_2(in_2[15:8]), .out_3(\n8位比较_1_out_3 ), .out_4(\n8位比较_1_out_4 ),
    .out_5(\n8位比较_1_out_5 ));
  \_8位比较  \u_8位比较_2  (
    .in_1(in_1[7:0]), .in_2(in_2[7:0]), .out_3(\n8位比较_2_out_3 ), .out_4(\n8位比较_2_out_4 ),
    .out_5(\n8位比较_2_out_5 ));
  and and_1 (and_1_out, \n8位比较_1_out_3 , \n8位比较_2_out_4 );
  and and_2 (and_2_out, \n8位比较_1_out_3 , \n8位比较_2_out_5 );
  and and_3 (out_3, \n8位比较_1_out_3 , \n8位比较_2_out_3 );
  or or_1 (out_4, \n8位比较_1_out_4 , and_1_out);
  or or_2 (out_5, and_2_out, \n8位比较_1_out_5 );
endmodule

module \_32位比较  (
  input  [31:0] in_1,
  input  [31:0] in_2,
  output out_3,
  output out_4,
  output out_5
);

  wire and_1_out, and_2_out, \n16位比较_1_out_3 , \n16位比较_1_out_4 , \n16位比较_1_out_5 , \n16位比较_2_out_3 ,
       \n16位比较_2_out_4 , \n16位比较_2_out_5 ;

  \_16位比较  \u_16位比较_1  (
    .in_1(in_1[31:16]), .in_2(in_2[31:16]), .out_3(\n16位比较_1_out_3 ), .out_4(\n16位比较_1_out_4 ),
    .out_5(\n16位比较_1_out_5 ));
  \_16位比较  \u_16位比较_2  (
    .in_1(in_1[15:0]), .in_2(in_2[15:0]), .out_3(\n16位比较_2_out_3 ), .out_4(\n16位比较_2_out_4 ),
    .out_5(\n16位比较_2_out_5 ));
  and and_1 (and_1_out, \n16位比较_1_out_3 , \n16位比较_2_out_4 );
  and and_2 (and_2_out, \n16位比较_1_out_3 , \n16位比较_2_out_5 );
  and and_3 (out_3, \n16位比较_1_out_3 , \n16位比较_2_out_3 );
  or or_1 (out_4, \n16位比较_1_out_4 , and_1_out);
  or or_2 (out_5, and_2_out, \n16位比较_1_out_5 );
endmodule

module \赋值  (
  input  [31:0] in_1,
  output [31:0] out_2
);

  wire [31:0] bit_extender_1_out;

  assign bit_extender_1_out = {{31{1'b1}}, 1'b1};  // Bit_Extender bit_extender_1
  assign out_2 = bit_extender_1_out & in_1;  // AND_Gate and_1, 32 bits wide
endmodule

module \_8选1  (
  input  [31:0] in_1,
  input  [31:0] in_2,
  input  [31:0] in_3,
  input  [31:0] in_4,
  input  [31:0] in_5,
  input  [31:0] in_6,
  input  [31:0] in_7,
  input  [31:0] in_8,
  input  in_9,
  input  in_10,
  input  in_11,
  output [31:0] out_12
);

  wire [31:0] and_1_out, and_2_out, and_3_out, and_4_out, and_5_out, and_6_out, and_7_out, and_8_out,
       bit_extender_1_out, bit_extender_2_out, bit_extender_3_out, not_1_out, not_2_out, not_3_out;

  assign bit_extender_1_out = {{31{in_9}}, in_9};  // Bit_Extender bit_extender_1
  assign bit_extender_2_out = {{31{in_10}}, in_10};  // Bit_Extender bit_extender_2
  assign bit_extender_3_out = {{31{in_11}}, in_11};  // Bit_Extender bit_extender_3
  assign not_1_out = ~bit_extender_1_out;  // NOT_Gate not_1, 32 bits wide
  assign not_2_out = ~bit_extender_2_out;  // NOT_Gate not_2, 32 bits wide
  assign not_3_out = ~bit_extender_3_out;  // NOT_Gate not_3, 32 bits wide
  assign and_1_out = not_1_out & in_1 & not_2_out & not_3_out;  // AND_Gate and_1, 32 bits wide
  assign and_2_out = not_1_out & not_2_out & bit_extender_3_out & in_2;  // AND_Gate and_2, 32 bits wide
  assign and_3_out = not_1_out & bit_extender_2_out & not_3_out & in_3;  // AND_Gate and_3, 32 bits wide
  assign and_4_out = in_4 & not_1_out & bit_extender_2_out & bit_extender_3_out;  // AND_Gate and_4, 32 bits wide
  assign and_5_out = bit_extender_1_out & not_2_out & not_3_out & in_5;  // AND_Gate and_5, 32 bits wide
  assign and_6_out = bit_extender_1_out & not_2_out & bit_extender_3_out & in_6;  // AND_Gate and_6, 32 bits wide
  assign and_7_out = bit_extender_1_out & bit_extender_2_out & not_3_out & in_7;  // AND_Gate and_7, 32 bits wide
  assign and_8_out = bit_extender_1_out & bit_extender_2_out & bit_extender_3_out & in_8;  // AND_Gate and_8, 32 bits wide
  assign out_12 = and_1_out | and_2_out | and_3_out | and_4_out | and_5_out | and_6_out | and_7_out | and_8_out;  // OR_Gate or_1, 32 bits wide
endmodule

module \_1最终  (
  input  [2:0] in_1,
  input  [31:0] in_2,
  input  [31:0] in_3,
  output \有符号溢出 ,
  output \无符号溢出 ,
  output \X_Y相等标志 ,
  output [31:0] out_7,
  output \S_只有111_作用_判断X_Y大小 
);

  // _32位ALU 32位alu_1: pin names not known; wires that end beside it: in_2, in_1, in_3, \有符号溢出 , \无符号溢出 , \X_Y相等标志 , out_7, \S_只有111_作用_判断X_Y大小 , \S_只有111_作用_判断X_Y大小 , \S_只有111_作用_判断X_Y大小 
endmodule
