// Logisim project 2.111.circ as structural Verilog: 4 circuits, main circuit 4k*8b
module _4k_8b (
  input  [7:0] \要写入数据 ,
  input  \_1写0读 ,
  input  [11:0] \访问地址 ,
  output [7:0] \当前读取_写入的数据 
);

  wire clock_1_out, not_1_out;

  assign \当前读取_写入的数据  = \_1写0读  ? \要写入数据  : 8'bz;  // Controlled_Buffer controlled_buffer_1
  not not_1 (not_1_out, \_1写0读 );
  Clock clock_1 (.out(clock_1_out));
  RAM #(.addrWidth(12)) ram_1 (
    .addr(\访问地址 ), .data(\当前读取_写入的数据 ), .sel(1'b1), .clk(clock_1_out), .ld(not_1_out));  // open: clr
endmodule

module _4k_32b (
  input  [31:0] in_1,
  input  in_2,
  input  [11:0] in_3,
  output [31:0] out_4
);

  _4k_8b u_4k_8b_1 (.\要写入数据 (in_1[7:0]), .\_1写0读 (in_2), .\访问地址 (in_3), .\当前读取_写入的数据 (out_4[7:0]));
  _4k_8b u_4k_8b_2 (.\要写入数据 (in_1[15:8]), .\_1写0读 (in_2), .\访问地址 (in_3), .\当前读取_写入的数据 (out_4[15:8]));
  _4k_8b u_4k_8b_3 (.\要写入数据 (in_1[23:16]), .\_1写0读 (in_2), .\访问地址 (in_3), .\当前读取_写入的数据 (out_4[23:16]));
  _4k_8b u_4k_8b_4 (.\要写入数据 (in_1[31:24]), .\_1写0读 (in_2), .\访问地址 (in_3), .\当前读取_写入的数据 (out_4[31:24]));
endmodule

module _16k_32b (
  input  [31:0] in_1,
  input  in_2,
  input  [15:0] in_3,
  output [31:0] out_4
);

  wire [31:0] n4k_32b_1_out_4, n4k_32b_2_out_4, n4k_32b_3_out_4, n4k_32b_4_out_4;

  _4k_32b u_4k_32b_1 (.in_1(in_1), .in_2(in_2), .in_3(in_3[15:4]), .out_4(n4k_32b_1_out_4));
  _4k_32b u_4k_32b_2 (.in_1(in_1), .in_2(in_2), .in_3(in_3[15:4]), .out_4(n4k_32b_2_out_4));
  _4k_32b u_4k_32b_3 (.in_1(in_1), .in_2(in_2), .in_3(in_3[15:4]), .out_4(n4k_32b_3_out_4));
  _4k_32b u_4k_32b_4 (.in_1(in_1), .in_2(in_2), .in_3(in_3[15:4]), .out_4(n4k_32b_4_out_4));
  Multiplexer #(.select(2), .width(32)) multiplexer_1 (
    .in0(n4k_32b_1_out_4), .in1(n4k_32b_2_out_4), .in2(n4k_32b_3_out_4), .in3(n4k_32b_4_out_4), .out(out_4),
    .sel(in_3[3:2]), .en(1'b1));
endmodule

module \存储器end  (
  input  [31:0] \写入数据 ,
  input  \_0读1写 ,
  input  [15:0] \操作地址 ,
  output [31:0] \读出数据_写数据时不显示 
);

  wire not_1_out;
  wire [31:0] n16k_32b_1_out_4;

  _16k_32b u_16k_32b_1 (.in_1(\写入数据 ), .in_2(\_0读1写 ), .in_3(\操作地址 ), .out_4(n16k_32b_1_out_4));
  assign \读出数据_写数据时不显示  = not_1_out ? n16k_32b_1_out_4 : 32'bz;  // Controlled_Buffer controlled_buffer_1
  not not_1 (not_1_out, \_0读1写 );
endmodule
