// Logisim project 2.2.circ as structural Verilog: 6 circuits, main circuit 4k*8b
module _4k_8b (
  input  [7:0] \要写入数据 ,
  input  \_1写0读 ,
  input  [11:0] \访问地址 ,
  input  in_4,
  output [7:0] \当前读取_写入的数据 
);

  wire not_1_out;

  assign \当前读取_写入的数据  = \_1写0读  ? \要写入数据  : 8'bz;  // Controlled_Buffer controlled_buffer_1
  not not_1 (not_1_out, \_1写0读 );
  RAM #(.addrWidth(12)) ram_1 (
    .addr(\访问地址 ), .data(\当前读取_写入的数据 ), .sel(1'b1), .clk(in_4), .ld(not_1_out));  // open: clr
endmodule

module _4k_32b (
  input  [31:0] in_1,
  input  in_2,
  input  [11:0] in_3,
  input  in_4,
  output [31:0] out_5
);

  _4k_8b u_4k_8b_1 (.\要写入数据 (in_1[7:0]), .\_1写0读 (in_2), .\访问地址 (in_3), .in_4(in_4), .\当前读取_写入的数据 (out_5[7:0]));
  _4k_8b u_4k_8b_2 (.\要写入数据 (in_1[15:8]), .\_1写0读 (in_2), .\访问地址 (in_3), .in_4(in_4), .\当前读取_写入的数据 (out_5[15:8]));
  _4k_8b u_4k_8b_3 (.\要写入数据 (in_1[23:16]), .\_1写0读 (in_2), .\访问地址 (in_3), .in_4(in_4), .\当前读取_写入的数据 (out_5[23:16]));
  _4k_8b u_4k_8b_4 (.\要写入数据 (in_1[31:24]), .\_1写0读 (in_2), .\访问地址 (in_3), .in_4(in_4), .\当前读取_写入的数据 (out_5[31:24]));
endmodule

module _16k_32b (
  input  [31:0] in_1,
  input  in_2,
  input  [15:0] in_3,
  input  in_4,
  output [31:0] out_5
);

  wire [31:0] n4k_32b_1_out_5, n4k_32b_2_out_5, n4k_32b_3_out_5, n4k_32b_4_out_5;

  _4k_32b u_4k_32b_1 (.in_1(in_1), .in_2(in_2), .in_3(in_3[15:4]), .in_4(in_4), .out_5(n4k_32b_1_out_5));
  _4k_32b u_4k_32b_2 (.in_1(in_1), .in_2(in_2), .in_3(in_3[15:4]), .in_4(in_4), .out_5(n4k_32b_2_out_5));
  _4k_32b u_4k_32b_3 (.in_1(in_1), .in_2(in_2), .in_3(in_3[15:4]), .in_4(in_4), .out_5(n4k_32b_3_out_5));
  _4k_32b u_4k_32b_4 (.in_1(in_1), .in_2(in_2), .in_3(in_3[15:4]), .in_4(in_4), .out_5(n4k_32b_4_out_5));
  Multiplexer #(.select(2), .width(32)) multiplexer_1 (
    .in0(n4k_32b_1_out_5), .in1(n4k_32b_2_out_5), .in2(n4k_32b_3_out_5), .in3(n4k_32b_4_out_5), .out(out_5),
    .sel(in_3[3:2]), .en(1'b1));
endmodule

module \存储器end  (
  input  [31:0] \写入数据 ,
  input  \_0读1写 ,
  input  [15:0] \操作地址 ,
  input  in_4,
  output [31:0] \读出数据_写数据时不显示 
);

  wire not_1_out;
  wire [31:0] n16k_32b_1_out_5;

  _16k_32b u_16k_32b_1 (.in_1(\写入数据 ), .in_2(\_0读1写 ), .in_3(\操作地址 ), .in_4(in_4), .out_5(n16k_32b_1_out_5));
  assign \读出数据_写数据时不显示  = not_1_out ? n16k_32b_1_out_5 : 32'bz;  // Controlled_Buffer controlled_buffer_1
  not not_1 (not_1_out, \_0读1写 );
endmodule

module RegFile (
  input  [31:0] in_1,
  input  [4:0] in_2,
  input  [4:0] in_3,
  input  [4:0] in_4,
  input  we,
  input  in_6,
  output [31:0] out_7,
  output [31:0] out_8
);

  wire and_1_out, and_2_out, and_3_out, and_4_out, and_5_out, and_6_out, and_7_out, and_8_out, and_9_out,
       and_10_out, and_11_out, and_12_out, and_13_out, and_14_out, and_15_out, and_16_out, and_17_out,
       and_18_out, and_19_out, and_20_out, and_21_out, and_22_out, and_23_out, and_24_out, and_25_out,
       and_26_out, and_27_out, and_28_out, and_29_out, and_30_out, and_31_out, and_32_out, decoder_1_out0,
       decoder_1_out1, decoder_1_out2, decoder_1_out3, decoder_1_out4, decoder_1_out5, decoder_1_out6,
       decoder_1_out7, decoder_1_out8, decoder_1_out9, decoder_1_out10, decoder_1_out11, decoder_1_out12,
       decoder_1_out13, decoder_1_out14, decoder_1_out15, decoder_1_out16, decoder_1_out17, decoder_1_out18,
       decoder_1_out19, decoder_1_out20, decoder_1_out21, decoder_1_out22, decoder_1_out23, decoder_1_out24,
       decoder_1_out25, decoder_1_out26, decoder_1_out27, decoder_1_out28, decoder_1_out29, decoder_1_out30,
       decoder_1_out31;
  wire [31:0] register_1_q, register_2_q, register_3_q, register_4_q, register_5_q, register_6_q,
       register_7_q, register_8_q, register_9_q, register_10_q, register_11_q, register_12_q, register_13_q,
       register_14_q, register_15_q, register_16_q, register_17_q, register_18_q, register_19_q,
       register_20_q, register_21_q, register_22_q, register_23_q, register_24_q, register_25_q,
       register_26_q, register_27_q, register_28_q, register_29_q, register_30_q, register_31_q,
       register_32_q;

  Decoder #(.select(5)) decoder_1 (
    .out0(decoder_1_out0), .out1(decoder_1_out1), .out2(decoder_1_out2), .out3(decoder_1_out3),
    .out4(decoder_1_out4), .out5(decoder_1_out5), .out6(decoder_1_out6), .out7(decoder_1_out7),
    .out8(decoder_1_out8), .out9(decoder_1_out9), .out10(decoder_1_out10), .out11(decoder_1_out11),
    .out12(decoder_1_out12), .out13(decoder_1_out13), .out14(decoder_1_out14), .out15(decoder_1_out15),
    .out16(decoder_1_out16), .out17(decoder_1_out17), .out18(decoder_1_out18), .out19(decoder_1_out19),
    .out20(decoder_1_out20), .out21(decoder_1_out21), .out22(decoder_1_out22), .out23(decoder_1_out23),
    .out24(decoder_1_out24), .out25(decoder_1_out25), .out26(decoder_1_out26), .out27(decoder_1_out27),
    .out28(decoder_1_out28), .out29(decoder_1_out29), .out30(decoder_1_out30), .out31(decoder_1_out31),
    .sel(in_3));  // open: en
  and and_1 (and_1_out, decoder_1_out0, in_6, we);
  and and_2 (and_2_out, decoder_1_out1, in_6, we);
  and and_3 (and_3_out, decoder_1_out2, in_6, we);
  and and_4 (and_4_out, decoder_1_out3, in_6, we);
  and and_5 (and_5_out, decoder_1_out4, in_6, we);
  and and_6 (and_6_out, decoder_1_out5, in_6, we);
  and and_7 (and_7_out, decoder_1_out6, in_6, we);
  and and_8 (and_8_out, decoder_1_out7, in_6, we);
  and and_9 (and_9_out, decoder_1_out8, in_6, we);
  and and_10 (and_10_out, decoder_1_out9, in_6, we);
  and and_11 (and_11_out, decoder_1_out10, in_6, we);
  and and_12 (and_12_out, decoder_1_out11, in_6, we);
  and and_13 (and_13_out, decoder_1_out12, in_6, we);
  and and_14 (and_14_out, decoder_1_out13, in_6, we);
  and and_15 (and_15_out, decoder_1_out14, in_6, we);
  and and_16 (and_16_out, decoder_1_out15, in_6, we);
  and and_17 (and_17_out, decoder_1_out16, in_6, we);
  and and_18 (and_18_out, decoder_1_out17, in_6, we);
  and and_19 (and_19_out, decoder_1_out18, in_6, we);
  and and_20 (and_20_out, decoder_1_out19, in_6, we);
  and and_21 (and_21_out, decoder_1_out20, in_6, we);
  and and_22 (and_22_out, decoder_1_out21, in_6, we);
  and and_23 (and_23_out, decoder_1_out22, in_6, we);
  and and_24 (and_24_out, decoder_1_out23, in_6, we);
  and and_25 (and_25_out, decoder_1_out24, in_6, we);
  and and_26 (and_26_out, decoder_1_out25, in_6, we);
  and and_27 (and_27_out, decoder_1_out26, in_6, we);
  and and_28 (and_28_out, decoder_1_out27, in_6, we);
  and and_29 (and_29_out, decoder_1_out28, in_6, we);
  and and_30 (and_30_out, decoder_1_out29, in_6, we);
  and and_31 (and_31_out, decoder_1_out30, in_6, we);
  and and_32 (and_32_out, decoder_1_out31, in_6, we);
  Register #(.width(32), .trigger("high")) register_1 (
    .D({32{1'b0}}), .en(and_1_out), .Q(register_1_q), .clk(in_6));  // open: clr
  Register #(.width(32), .trigger("high")) register_2 (
    .D(in_1), .en(and_2_out), .Q(register_2_q), .clk(in_6));  // open: clr
  Register #(.width(32), .trigger("high")) register_3 (
    .D(in_1), .en(and_3_out), .Q(register_3_q), .clk(in_6));  // open: clr
  Register #(.width(32), .trigger("high")) register_4 (
    .D(in_1), .en(and_4_out), .Q(register_4_q), .clk(in_6));  // open: clr
  Register #(.width(32), .trigger("high")) register_5 (
    .D(in_1), .en(and_5_out), .Q(register_5_q), .clk(in_6));  // open: clr
  Register #(.width(32), .trigger("high")) register_6 (
    .D(in_1), .en(and_6_out), .Q(register_6_q), .clk(in_6));  // open: clr
  Register #(.width(32), .trigger("high")) register_7 (
    .D(in_1), .en(and_7_out), .Q(register_7_q), .clk(in_6));  // open: clr
  Register #(.width(32), .trigger("high")) register_8 (
    .D(in_1), .en(and_8_out), .Q(register_8_q), .clk(in_6));  // open: clr
  Register #(.width(32), .trigger("high")) register_9 (
    .D(in_1), .en(and_9_out), .Q(register_9_q), .clk(in_6));  // open: clr
  Register #(.width(32), .trigger("high")) register_10 (
    .D(in_1), .en(and_10_out), .Q(register_10_q), .clk(in_6));  // open: clr
  Register #(.width(32), .trigger("high")) register_11 (
    .D(in_1), .en(and_11_out), .Q(register_11_q), .clk(in_6));  // open: clr
  Register #(.width(32), .trigger("high")) register_12 (
    .D(in_1), .en(and_12_out), .Q(register_12_q), .clk(in_6));  // open: clr
  Register #(.width(32), .trigger("high")) register_13 (
    .D(in_1), .en(and_13_out), .Q(register_13_q), .clk(in_6));  // open: clr
  Register #(.width(32), .trigger("high")) register_14 (
    .D(in_1), .en(and_14_out), .Q(register_14_q), .clk(in_6));  // open: clr
  Register #(.width(32), .trigger("high")) register_15 (
    .D(in_1), .en(and_15_out), .Q(register_15_q), .clk(in_6));  // open: clr
  Register #(.width(32), .trigger("high")) register_16 (
    .D(in_1), .en(and_16_out), .Q(register_16_q), .clk(in_6));  // open: clr
  Register #(.width(32), .trigger("high")) register_17 (
    .D(in_1), .en(and_17_out), .Q(register_17_q), .clk(in_6));  // open: clr
  Register #(.width(32), .trigger("high")) register_18 (
    .D(in_1), .en(and_18_out), .Q(register_18_q), .clk(in_6));  // open: clr
  Register #(.width(32), .trigger("high")) register_19 (
    .D(in_1), .en(and_19_out), .Q(register_19_q), .clk(in_6));  // open: clr
  Register #(.width(32), .trigger("high")) register_20 (
    .D(in_1), .en(and_20_out), .Q(register_20_q), .clk(in_6));  // open: clr
  Register #(.width(32), .trigger("high")) register_21 (
    .D(in_1), .en(and_21_out), .Q(register_21_q), .clk(in_6));  // open: clr
  Register #(.width(32), .trigger("high")) register_22 (
    .D(in_1), .en(and_22_out), .Q(register_22_q), .clk(in_6));  // open: clr
  Register #(.width(32), .trigger("high")) register_23 (
    .D(in_1), .en(and_23_out), .Q(register_23_q), .clk(in_6));  // open: clr
  Register #(.width(32), .trigger("high")) register_24 (
    .D(in_1), .en(and_24_out), .Q(register_24_q), .clk(in_6));  // open: clr
  Register #(.width(32), .trigger("high")) register_25 (
    .D(in_1), .en(and_25_out), .Q(register_25_q), .clk(in_6));  // open: clr
  Register #(.width(32), .trigger("high")) register_26 (
    .D(in_1), .en(and_26_out), .Q(register_26_q), .clk(in_6));  // open: clr
  Register #(.width(32), .trigger("high")) register_27 (
    .D(in_1), .en(and_27_out), .Q(register_27_q), .clk(in_6));  // open: clr
  Register #(.width(32), .trigger("high")) register_28 (
    .D(in_1), .en(and_28_out), .Q(register_28_q), .clk(in_6));  // open: clr
  Register #(.width(32), .trigger("high")) register_29 (
    .D(in_1), .en(and_29_out), .Q(register_29_q), .clk(in_6));  // open: clr
  Register #(.width(32), .trigger("high")) register_30 (
    .D(in_1), .en(and_30_out), .Q(register_30_q), .clk(in_6));  // open: clr
  Register #(.width(32), .trigger("high")) register_31 (
    .D(in_1), .en(and_31_out), .Q(register_31_q), .clk(in_6));  // open: clr
  Register #(.width(32), .trigger("high")) register_32 (
    .D(in_1), .en(and_32_out), .Q(register_32_q), .clk(in_6));  // open: clr
  Multiplexer #(.select(5), .width(32)) multiplexer_1 (
    .in0(register_1_q), .in1(register_2_q), .in2(register_3_q), .in3(register_4_q), .in4(register_5_q),
    .in5(register_6_q), .in6(register_7_q), .in7(register_8_q), .in8(register_9_q), .in9(register_10_q),
    .in10(register_11_q), .in11(register_12_q), .in12(register_13_q), .in13(register_14_q),
    .in14(register_15_q), .in15(register_16_q), .in16(register_17_q), .in17(register_18_q),
    .in18(register_19_q), .in19(register_20_q), .in20(register_21_q), .in21(register_22_q),
    .in22(register_23_q), .in23(register_24_q), .in24(register_25_q), .in25(register_26_q),
    .in26(register_27_q), .in27(register_28_q), .in28(register_29_q), .in29(register_30_q),
    .in30(register_31_q), .in31(register_32_q), .out(out_7), .sel(in_2));  // open: en
  Multiplexer #(.select(5), .width(32)) multiplexer_2 (
    .in0(register_1_q), .in1(register_2_q), .in2(register_3_q), .in3(register_4_q), .in4(register_5_q),
    .in5(register_6_q), .in6(register_7_q), .in7(register_8_q), .in8(register_9_q), .in9(register_10_q),
    .in10(register_11_q), .in11(register_12_q), .in12(register_13_q), .in13(register_14_q),
    .in14(register_15_q), .in15(register_16_q), .in16(register_17_q), .in17(register_18_q),
    .in18(register_19_q), .in19(register_20_q), .in20(register_21_q), .in21(register_22_q),
    .in22(register_23_q), .in23(register_24_q), .in24(register_25_q), .in25(register_26_q),
    .in26(register_27_q), .in27(register_28_q), .in28(register_29_q), .in29(register_30_q),
    .in30(register_31_q), .in31(register_32_q), .out(out_8), .sel(in_4));  // open: en
endmodule

module \数据互传  (
  input  [1:0] DISSEL,
  input  [4:0] in_2,
  input  [4:0] in_3,
  input  [4:0] in_4,
  input  ALUYSEL,
  input  [2:0] ALUOP,
  input  in_7,
  input  [31:0] in_8,
  input  DMwr,
  input  [1:0] RWSEL,
  output [31:0] out_11
);

  wire clock_1_out;
  wire [15:0] \n32位alu_1_out_7 , \n32位alu_1_out_7_2 ;
  wire [31:0] multiplexer_1_out, multiplexer_2_out, regfile_1_out_7, regfile_1_out_8, \存储器end_1_读出数据_写数据时不显示 ;

  Multiplexer #(.select(2), .width(32)) multiplexer_1 (
    .in0(in_8), .in1(\存储器end_1_读出数据_写数据时不显示 ), .in2(multiplexer_2_out), .in3({32{1'b0}}),
    .out(multiplexer_1_out), .sel(RWSEL));  // open: en
  RegFile regfile_1 (
    .in_1(multiplexer_1_out), .in_3(in_4), .in_4(in_3), .out_7(regfile_1_out_7), .out_8(regfile_1_out_8),
    .we(in_7), .in_2(in_2), .in_6(clock_1_out));
  Clock clock_1 (.out(clock_1_out));
  Multiplexer #(.width(32)) multiplexer_2 (
    .in0(regfile_1_out_8), .in1(in_8), .out(multiplexer_2_out), .sel(ALUYSEL));  // open: en
  \_32位ALU  \u_32位alu_1  (
    .AluOp(ALUOP), .out_7({\n32位alu_1_out_7_2 , \n32位alu_1_out_7 }), .x(regfile_1_out_7),
    .y(multiplexer_2_out));  // open: OF, UOF, ZF, S_只有111时作用_判断x_y大小
  Multiplexer #(.select(2), .width(32)) multiplexer_3 (
    .in0({\n32位alu_1_out_7_2 , \n32位alu_1_out_7 }), .in1(regfile_1_out_8), .in2(\存储器end_1_读出数据_写数据时不显示 ),
    .in3(multiplexer_1_out), .out(out_11), .sel(DISSEL));  // open: en
  \存储器end  \u_存储器end_1  (
    .\写入数据 (regfile_1_out_8), .\_0读1写 (DMwr), .\操作地址 (\n32位alu_1_out_7 ), .in_4(clock_1_out),
    .\读出数据_写数据时不显示 (\存储器end_1_读出数据_写数据时不显示 ));

  // Notes on the sheet:
  //   读数据
  //   寄存器地址
  //   寄存器地址
  //   写数据
endmodule
