// Logisim project 32位ALU.circ as structural Verilog: 7 circuits, main circuit 8位加法器
module ALU (
  input  \使能 ,
  input  [2:0] ALuOp,
  input  [31:0] X,
  input  [31:0] Y,
  output OF,
  output UOF,
  output ZF,
  output [31:0] S
);

  wire _000, _001, _007, nand_1_out, OF_t, or_1_out, or_3_out, UOF_t, xor_3_out, y0, ZF_t, \全0判断_1_out_2 ;
  wire [0:0] _7;
  wire [31:0] _0, _2, _3, _4, _5, _6, bit_extender_1_out, xor_1_out;

  \_32位加法器  \u_32位加法器_1  (
    .\进位 (or_1_out), .UOF_CF(UOF_t), .OF(OF_t), .SF(_7[0]), .ZF(ZF_t), .X(X), .Y(xor_1_out), .OUT(_0));
  \全0判断  \u_全0判断_1  (.in_1(Y), .out_2(\全0判断_1_out_2 ));
  assign xor_1_out = Y ^ bit_extender_1_out;  // XOR_Gate xor_1, 32 bits wide
  or or_1 (or_1_out, _001, _007);
  not not_1 (y0, \全0判断_1_out_2 );
  assign bit_extender_1_out = {{31{1'b1}}, or_1_out};  // Bit_Extender bit_extender_1
  \_38译码器  \u_38译码器_1  (.in_1(ALuOp), .\使能 (\使能 ), ._0(_000), ._1(_001), ._7(_007));  // open: _2, _3, _4, _5, _6
  assign _2 = X & Y;  // AND_Gate and_1, 32 bits wide
  assign _3 = X | Y;  // OR_Gate or_2, 32 bits wide
  assign _4 = X ^ Y;  // XOR_Gate xor_2, 32 bits wide
  assign _5 = Y;  // Buffer buffer_1, 32 bits wide
  assign _6 = ~Y;  // NOT_Gate not_2, 32 bits wide
  and and_2 (UOF, or_3_out, nand_1_out, xor_3_out);
  and and_3 (OF, or_3_out, OF_t);
  nand nand_1 (nand_1_out, ~y0, _001);  // NAND_Gate
  and and_4 (ZF, or_3_out, ZF_t);
  xor xor_3 (xor_3_out, UOF_t, _001);
  Multiplexer #(.select(3), .width(32), .disabled(0)) multiplexer_1 (
    .in0(_0), .in1(_0), .in2(_2), .in3(_3), .in4(_4), .in5(_5), .in6(_6), .in7({{31{1'b0}}, _7[0]}), .out(S),
    .sel(ALuOp), .en(\使能 ));
  or or_3 (or_3_out, _001, _000);

  // Other names for the same wires on the sheet: _1[31:0] = _0
endmodule

module \_32位加法器  (
  input  [31:0] X,
  input  [31:0] Y,
  input  \进位 ,
  output UOF_CF,
  output OF,
  output SF,
  output ZF,
  output [31:0] OUT
);

  wire \n8位加法器_1_进位输出 , \n8位加法器_2_进位输出 , \n8位加法器_3_进位输出 , xnor_1_out, xor_1_out;

  \_8位加法器  \u_8位加法器_1  (.\进位输入 (\进位 ), .\进位输出 (\n8位加法器_1_进位输出 ), .X(X[7:0]), .Y(Y[7:0]), .\结果 (OUT[7:0]));
  \_8位加法器  \u_8位加法器_2  (.\进位输入 (\n8位加法器_1_进位输出 ), .\进位输出 (\n8位加法器_2_进位输出 ), .X(X[15:8]), .Y(Y[15:8]), .\结果 (OUT[15:8]));
  \_8位加法器  \u_8位加法器_3  (
    .\进位输入 (\n8位加法器_2_进位输出 ), .\进位输出 (\n8位加法器_3_进位输出 ), .X(X[23:16]), .Y(Y[23:16]), .\结果 (OUT[23:16]));
  xnor xnor_1 (xnor_1_out, X[31], Y[31]);
  \_8位加法器  \u_8位加法器_4  (.\进位输入 (\n8位加法器_3_进位输出 ), .\进位输出 (UOF_CF), .X(Y[31:24]), .Y(X[31:24]), .\结果 (OUT[31:24]));
  \全0判断  \u_全0判断_1  (.in_1(OUT), .out_2(ZF));
  and and_1 (OF, xnor_1_out, xor_1_out);
  xor xor_1 (xor_1_out, Y[31], OUT[31]);

  assign SF = OUT[31];
endmodule

module \_8位加法器  (
  input  [7:0] X,
  input  [7:0] Y,
  input  \进位输入 ,
  output \进位输出 ,
  output [7:0] \结果 
);

  wire \一位全加器_1_进位输出 , \一位全加器_2_进位输出 , \一位全加器_3_进位输出 , \一位全加器_4_进位输出 , \一位全加器_5_进位输出 , \一位全加器_6_进位输出 ,
       \一位全加器_7_进位输出 ;

  \一位全加器  \u_一位全加器_1  (.X(X[0]), .Y(Y[0]), .\进位输入 (\进位输入 ), .\进位输出 (\一位全加器_1_进位输出 ), .\结果 (\结果 [0]));
  \一位全加器  \u_一位全加器_2  (.X(Y[4]), .Y(X[4]), .\进位输入 (\一位全加器_7_进位输出 ), .\进位输出 (\一位全加器_2_进位输出 ), .\结果 (\结果 [4]));
  \一位全加器  \u_一位全加器_3  (.X(X[1]), .Y(Y[1]), .\进位输入 (\一位全加器_1_进位输出 ), .\进位输出 (\一位全加器_3_进位输出 ), .\结果 (\结果 [1]));
  \一位全加器  \u_一位全加器_4  (.X(Y[5]), .Y(X[5]), .\进位输入 (\一位全加器_2_进位输出 ), .\进位输出 (\一位全加器_4_进位输出 ), .\结果 (\结果 [5]));
  \一位全加器  \u_一位全加器_5  (.X(X[2]), .Y(Y[2]), .\进位输入 (\一位全加器_3_进位输出 ), .\进位输出 (\一位全加器_5_进位输出 ), .\结果 (\结果 [2]));
  \一位全加器  \u_一位全加器_6  (.X(X[6]), .Y(Y[6]), .\进位输入 (\一位全加器_4_进位输出 ), .\进位输出 (\一位全加器_6_进位输出 ), .\结果 (\结果 [6]));
  \一位全加器  \u_一位全加器_7  (.X(Y[3]), .Y(X[3]), .\进位输入 (\一位全加器_5_进位输出 ), .\进位输出 (\一位全加器_7_进位输出 ), .\结果 (\结果 [3]));
  \一位全加器  \u_一位全加器_8  (.X(X[7]), .Y(Y[7]), .\进位输入 (\一位全加器_6_进位输出 ), .\进位输出 (\进位输出 ), .\结果 (\结果 [7]));
endmodule

module \一位全加器  (
  input  X,
  input  Y,
  input  \进位输入 ,
  output \进位输出 ,
  output \结果 
);

  wire and_1_out, and_2_out, and_3_out, and_4_out, and_5_out, and_6_out, and_7_out, not_1_out, not_2_out,
       not_3_out, not_4_out, not_5_out, not_6_out;

  and and_1 (and_1_out, Y, \进位输入 );
  and and_2 (and_2_out, X, \进位输入 );
  and and_3 (and_3_out, X, Y);
  not not_1 (not_1_out, X);
  not not_2 (not_2_out, Y);
  not not_3 (not_3_out, X);
  not not_4 (not_4_out, \进位输入 );
  not not_5 (not_5_out, Y);
  not not_6 (not_6_out, \进位输入 );
  or or_1 (\进位输出 , and_1_out, and_2_out, and_3_out);
  and and_4 (and_4_out, not_1_out, not_2_out, \进位输入 );
  and and_5 (and_5_out, not_3_out, Y, not_4_out);
  and and_6 (and_6_out, X, not_5_out, not_6_out);
  and and_7 (and_7_out, X, Y, \进位输入 );
  or or_2 (\结果 , and_4_out, and_5_out, and_6_out, and_7_out);
endmodule

module \全0判断  (
  input  [31:0] in_1,
  output out_2
);

  wire or_2_out;
  wire [1:0] or_3_out;
  wire [7:0] or_1_out;

  assign or_1_out = in_1[7:0] | in_1[15:8] | in_1[23:16] | in_1[31:24] | in_1[31:24];  // OR_Gate or_1, 8 bits wide
  or or_2 (or_2_out, or_3_out[0], or_3_out[1]);
  assign or_3_out = or_1_out[1:0] | or_1_out[3:2] | or_1_out[5:4] | or_1_out[7:6] | or_1_out[7:6];  // OR_Gate or_3, 2 bits wide
  not not_1 (out_2, or_2_out);
endmodule

module \_38译码器  (
  input  [2:0] in_1,
  input  \使能 ,
  output _0,
  output _1,
  output _2,
  output _3,
  output _4,
  output _5,
  output _6,
  output _7
);

  wire and_1_out, and_2_out, and_3_out, and_4_out, and_5_out, and_6_out, and_7_out, and_8_out, not_1_out,
       not_2_out, not_3_out, not_4_out, not_5_out, not_6_out, not_7_out, not_8_out, not_9_out, not_10_out,
       not_11_out, not_12_out;

  not not_1 (not_1_out, in_1[2]);
  not not_2 (not_2_out, in_1[1]);
  not not_3 (not_3_out, in_1[0]);
  not not_4 (not_4_out, in_1[2]);
  not not_5 (not_5_out, in_1[1]);
  not not_6 (not_6_out, in_1[2]);
  not not_7 (not_7_out, in_1[0]);
  not not_8 (not_8_out, in_1[2]);
  not not_9 (not_9_out, in_1[1]);
  not not_10 (not_10_out, in_1[0]);
  not not_11 (not_11_out, in_1[1]);
  not not_12 (not_12_out, in_1[0]);
  and and_1 (and_1_out, in_1[2], in_1[1], in_1[0]);
  and and_2 (and_2_out, not_1_out, not_2_out, not_3_out);
  and and_3 (and_3_out, not_4_out, not_5_out, in_1[0]);
  and and_4 (and_4_out, not_6_out, in_1[1], not_7_out);
  and and_5 (and_5_out, not_8_out, in_1[1], in_1[0]);
  and and_6 (and_6_out, in_1[2], not_9_out, not_10_out);
  and and_7 (and_7_out, in_1[2], not_11_out, in_1[0]);
  and and_8 (and_8_out, in_1[2], in_1[1], not_12_out);
  and and_9 (_0, and_2_out, \使能 );
  and and_10 (_1, and_3_out, \使能 );
  and and_11 (_2, and_4_out, \使能 );
  and and_12 (_3, and_5_out, \使能 );
  and and_13 (_4, and_6_out, \使能 );
  and and_14 (_5, and_7_out, \使能 );
  and and_15 (_6, and_8_out, \使能 );
  and and_16 (_7, and_1_out, \使能 );
endmodule

module Test (
  input  [31:0] X,
  input  in_2,
  input  [31:0] Y,
  input  [2:0] in_4
);

  wire alu_1_of, alu_1_uof, alu_1_zf;
  wire [31:0] alu_1_s;

  ALU alu_1 (.X(X), .Y(Y), .ALuOp(in_4), .S(alu_1_s), .OF(alu_1_of), .UOF(alu_1_uof), .ZF(alu_1_zf), .\使能 (in_2));
  // Probe on alu_1_of
  // Probe on alu_1_uof
  // Probe on alu_1_zf
  // Probe on alu_1_s

  // Notes on the sheet:
  //   OF
  //   UOF
  //   ZF
  //   OF：有符号溢出标志
  //   UOF：无符号溢出标志
  //   ZF：0标志
endmodule
