// Logisim project 计算机组成实验.circ as structural Verilog: 10 circuits, main circuit 8位加法器
module ALU (
  input  \使能 ,
  input  [2:0] ALuOp,
  input  [31:0] X,
  input  [31:0] Y,
  output OF,
  output UOF,
  output ZF,
  output [31:0] S
);

  wire _000, _001, _007, nand_1_out, OF_t, or_1_out, or_3_out, UOF_t, xor_3_out, y0, ZF_t, \全0判断_1_out_2 ;
  wire [0:0] _7;
  wire [31:0] _0, _2, _3, _4, _5, _6, bit_extender_1_out, xor_1_out;

  \_32位加法器  \u_32位加法器_1  (
    .\进位 (or_1_out), .UOF_CF(UOF_t), .OF(OF_t), .SF(_7[0]), .ZF(ZF_t), .X(X), .Y(xor_1_out), .OUT(_0));
  \全0判断  \u_全0判断_1  (.in_1(Y), .out_2(\全0判断_1_out_2 ));
  assign xor_1_out = Y ^ bit_extender_1_out;  // XOR_Gate xor_1, 32 bits wide
  or or_1 (or_1_out, _001, _007);
  not not_1 (y0, \全0判断_1_out_2 );
  assign bit_extender_1_out = {{31{1'b1}}, or_1_out};  // Bit_Extender bit_extender_1
  \_38译码器  \u_38译码器_1  (.in_1(ALuOp), .\使能 (\使能 ), ._0(_000), ._1(_001), ._7(_007));  // open: _2, _3, _4, _5, _6
  assign _2 = X & Y;  // AND_Gate and_1, 32 bits wide
  assign _3 = X | Y;  // OR_Gate or_2, 32 bits wide
  assign _4 = X ^ Y;  // XOR_Gate xor_2, 32 bits wide
  assign _5 = Y;  // Buffer buffer_1, 32 bits wide
  assign _6 = ~Y;  // NOT_Gate not_2, 32 bits wide
  and and_2 (OF, or_3_out, OF_t);
  and and_3 (UOF, or_3_out, nand_1_out, xor_3_out);
  nand nand_1 (nand_1_out, ~y0, _001);  // NAND_Gate
  and and_4 (ZF, or_3_out, ZF_t);
  xor xor_3 (xor_3_out, UOF_t, _001);
  Multiplexer #(.select(3), .width(32), .disabled(0)) multiplexer_1 (
    .in0(_0), .in1(_0), .in2(_2), .in3(_3), .in4(_4), .in5(_5), .in6(_6), .in7({{31{1'b0}}, _7[0]}), .out(S),
    .sel(ALuOp), .en(\使能 ));
  or or_3 (or_3_out, _001, _000);

  // Other names for the same wires on the sheet: _1[31:0] = _0
endmodule

module \_32位加法器  (
  input  [31:0] X,
  input  [31:0] Y,
  input  \进位 ,
  output UOF_CF,
  output OF,
  output SF,
  output ZF,
  output [31:0] OUT
);

  wire \n8位加法器_1_进位输出 , \n8位加法器_2_进位输出 , \n8位加法器_3_进位输出 , xnor_1_out, xor_1_out;

  \_8位加法器  \u_8位加法器_1  (.\进位输入 (\进位 ), .\进位输出 (\n8位加法器_1_进位输出 ), .X(X[7:0]), .Y(Y[7:0]), .\结果 (OUT[7:0]));
  \_8位加法器  \u_8位加法器_2  (.\进位输入 (\n8位加法器_1_进位输出 ), .\进位输出 (\n8位加法器_2_进位输出 ), .X(X[15:8]), .Y(Y[15:8]), .\结果 (OUT[15:8]));
  \_8位加法器  \u_8位加法器_3  (
    .\进位输入 (\n8位加法器_2_进位输出 ), .\进位输出 (\n8位加法器_3_进位输出 ), .X(X[23:16]), .Y(Y[23:16]), .\结果 (OUT[23:16]));
  xnor xnor_1 (xnor_1_out, X[31], Y[31]);
  \_8位加法器  \u_8位加法器_4  (.\进位输入 (\n8位加法器_3_进位输出 ), .\进位输出 (UOF_CF), .X(Y[31:24]), .Y(X[31:24]), .\结果 (OUT[31:24]));
  \全0判断  \u_全0判断_1  (.in_1(OUT), .out_2(ZF));
  and and_1 (OF, xnor_1_out, xor_1_out);
  xor xor_1 (xor_1_out, Y[31], OUT[31]);

  assign SF = OUT[31];
endmodule

module \_8位加法器  (
  input  [7:0] X,
  input  [7:0] Y,
  input  \进位输入 ,
  output \进位输出 ,
  output [7:0] \结果 
);

  wire \一位全加器_1_进位输出 , \一位全加器_2_进位输出 , \一位全加器_3_进位输出 , \一位全加器_4_进位输出 , \一位全加器_5_进位输出 , \一位全加器_6_进位输出 ,
       \一位全加器_7_进位输出 ;

  \一位全加器  \u_一位全加器_1  (.X(X[0]), .Y(Y[0]), .\进位输入 (\进位输入 ), .\进位输出 (\一位全加器_1_进位输出 ), .\结果 (\结果 [0]));
  \一位全加器  \u_一位全加器_2  (.X(Y[4]), .Y(X[4]), .\进位输入 (\一位全加器_7_进位输出 ), .\进位输出 (\一位全加器_2_进位输出 ), .\结果 (\结果 [4]));
  \一位全加器  \u_一位全加器_3  (.X(X[1]), .Y(Y[1]), .\进位输入 (\一位全加器_1_进位输出 ), .\进位输出 (\一位全加器_3_进位输出 ), .\结果 (\结果 [1]));
  \一位全加器  \u_一位全加器_4  (.X(Y[5]), .Y(X[5]), .\进位输入 (\一位全加器_2_进位输出 ), .\进位输出 (\一位全加器_4_进位输出 ), .\结果 (\结果 [5]));
  \一位全加器  \u_一位全加器_5  (.X(X[2]), .Y(Y[2]), .\进位输入 (\一位全加器_3_进位输出 ), .\进位输出 (\一位全加器_5_进位输出 ), .\结果 (\结果 [2]));
  \一位全加器  \u_一位全加器_6  (.X(X[6]), .Y(Y[6]), .\进位输入 (\一位全加器_4_进位输出 ), .\进位输出 (\一位全加器_6_进位输出 ), .\结果 (\结果 [6]));
  \一位全加器  \u_一位全加器_7  (.X(Y[3]), .Y(X[3]), .\进位输入 (\一位全加器_5_进位输出 ), .\进位输出 (\一位全加器_7_进位输出 ), .\结果 (\结果 [3]));
  \一位全加器  \u_一位全加器_8  (.X(X[7]), .Y(Y[7]), .\进位输入 (\一位全加器_6_进位输出 ), .\进位输出 (\进位输出 ), .\结果 (\结果 [7]));
endmodule

module \一位全加器  (
  input  X,
  input  Y,
  input  \进位输入 ,
  output \进位输出 ,
  output \结果 
);

  wire and_1_out, and_2_out, and_3_out, and_4_out, and_5_out, and_6_out, and_7_out, not_1_out, not_2_out,
       not_3_out, not_4_out, not_5_out, not_6_out;

  and and_1 (and_1_out, Y, \进位输入 );
  and and_2 (and_2_out, X, \进位输入 );
  and and_3 (and_3_out, X, Y);
  not not_1 (not_1_out, X);
  not not_2 (not_2_out, Y);
  not not_3 (not_3_out, X);
  not not_4 (not_4_out, \进位输入 );
  not not_5 (not_5_out, Y);
  not not_6 (not_6_out, \进位输入 );
  or or_1 (\进位输出 , and_1_out, and_2_out, and_3_out);
  and and_4 (and_4_out, not_1_out, not_2_out, \进位输入 );
  and and_5 (and_5_out, not_3_out, Y, not_4_out);
  and and_6 (and_6_out, X, not_5_out, not_6_out);
  and and_7 (and_7_out, X, Y, \进位输入 );
  or or_2 (\结果 , and_4_out, and_5_out, and_6_out, and_7_out);
endmodule

module \全0判断  (
  input  [31:0] in_1,
  output out_2
);

  wire or_2_out;
  wire [1:0] or_3_out;
  wire [7:0] or_1_out;

  assign or_1_out = in_1[7:0] | in_1[15:8] | in_1[23:16] | in_1[31:24] | in_1[31:24];  // OR_Gate or_1, 8 bits wide
  or or_2 (or_2_out, or_3_out[0], or_3_out[1]);
  assign or_3_out = or_1_out[1:0] | or_1_out[3:2] | or_1_out[5:4] | or_1_out[7:6] | or_1_out[7:6];  // OR_Gate or_3, 2 bits wide
  not not_1 (out_2, or_2_out);
endmodule

module \_38译码器  (
  input  [2:0] in_1,
  input  \使能 ,
  output _0,
  output _1,
  output _2,
  output _3,
  output _4,
  output _5,
  output _6,
  output _7
);

  wire and_1_out, and_2_out, and_3_out, and_4_out, and_5_out, and_6_out, and_7_out, and_8_out, not_1_out,
       not_2_out, not_3_out, not_4_out, not_5_out, not_6_out, not_7_out, not_8_out, not_9_out, not_10_out,
       not_11_out, not_12_out;

  not not_1 (not_1_out, in_1[2]);
  not not_2 (not_2_out, in_1[1]);
  not not_3 (not_3_out, in_1[0]);
  not not_4 (not_4_out, in_1[2]);
  not not_5 (not_5_out, in_1[1]);
  not not_6 (not_6_out, in_1[2]);
  not not_7 (not_7_out, in_1[0]);
  not not_8 (not_8_out, in_1[2]);
  not not_9 (not_9_out, in_1[1]);
  not not_10 (not_10_out, in_1[0]);
  not not_11 (not_11_out, in_1[1]);
  not not_12 (not_12_out, in_1[0]);
  and and_1 (and_1_out, in_1[2], in_1[1], in_1[0]);
  and and_2 (and_2_out, not_1_out, not_2_out, not_3_out);
  and and_3 (and_3_out, not_4_out, not_5_out, in_1[0]);
  and and_4 (and_4_out, not_6_out, in_1[1], not_7_out);
  and and_5 (and_5_out, not_8_out, in_1[1], in_1[0]);
  and and_6 (and_6_out, in_1[2], not_9_out, not_10_out);
  and and_7 (and_7_out, in_1[2], not_11_out, in_1[0]);
  and and_8 (and_8_out, in_1[2], in_1[1], not_12_out);
  and and_9 (_0, and_2_out, \使能 );
  and and_10 (_1, and_3_out, \使能 );
  and and_11 (_2, and_4_out, \使能 );
  and and_12 (_3, and_5_out, \使能 );
  and and_13 (_4, and_6_out, \使能 );
  and and_14 (_5, and_7_out, \使能 );
  and and_15 (_6, and_8_out, \使能 );
  and and_16 (_7, and_1_out, \使能 );
endmodule

module Test (
  input  [31:0] X,
  input  in_2,
  input  [31:0] Y,
  input  [2:0] in_4
);

  wire alu_1_of, alu_1_uof, alu_1_zf;
  wire [31:0] alu_1_s;

  ALU alu_1 (.X(X), .Y(Y), .ALuOp(in_4), .S(alu_1_s), .OF(alu_1_of), .UOF(alu_1_uof), .ZF(alu_1_zf), .\使能 (in_2));
  // Probe on alu_1_of
  // Probe on alu_1_uof
  // Probe on alu_1_zf
  // Probe on alu_1_s

  // Notes on the sheet:
  //   OF
  //   UOF
  //   ZF
  //   OF：有符号溢出标志
  //   UOF：无符号溢出标志
  //   ZF：0标志
endmodule

module \存储器  (
  input  [13:0] \地址 ,
  input  [31:0] \数据 ,
  input  WE,
  input  CLK,
  output [31:0] \输出 
);

  wire decoder_1_out0, decoder_1_out1, decoder_1_out2, decoder_1_out3, not_1_out, or_1_out;

  not not_1 (not_1_out, WE);
  or or_1 (or_1_out, not_1_out, WE);
  Decoder #(.select(2)) decoder_1 (
    .out0(decoder_1_out0), .out1(decoder_1_out1), .out2(decoder_1_out2), .out3(decoder_1_out3),
    .sel(\地址 [13:12]));  // open: en
  RAM #(.addrWidth(12), .bus("separate")) ram_1 (
    .addr(\地址 [11:0]), .din(\数据 [7:0]), .data(\输出 [7:0]), .str(not_1_out), .sel(decoder_1_out0), .clk(CLK),
    .ld(or_1_out));  // open: clr
  RAM #(.addrWidth(12), .bus("separate")) ram_2 (
    .addr(\地址 [11:0]), .din(\数据 [7:0]), .data(\输出 [7:0]), .str(not_1_out), .sel(decoder_1_out1), .clk(CLK),
    .ld(or_1_out));  // open: clr
  RAM #(.addrWidth(12), .bus("separate")) ram_3 (
    .addr(\地址 [11:0]), .din(\数据 [7:0]), .data(\输出 [7:0]), .str(not_1_out), .sel(decoder_1_out2), .clk(CLK),
    .ld(or_1_out));  // open: clr
  RAM #(.addrWidth(12), .bus("separate")) ram_4 (
    .addr(\地址 [11:0]), .din(\数据 [7:0]), .data(\输出 [7:0]), .str(not_1_out), .sel(decoder_1_out3), .clk(CLK),
    .ld(or_1_out));  // open: clr
  RAM #(.addrWidth(12), .bus("separate")) ram_5 (
    .addr(\地址 [11:0]), .din(\数据 [15:8]), .data(\输出 [15:8]), .str(not_1_out), .sel(decoder_1_out0), .clk(CLK),
    .ld(or_1_out));  // open: clr
  RAM #(.addrWidth(12), .bus("separate")) ram_6 (
    .addr(\地址 [11:0]), .din(\数据 [15:8]), .data(\输出 [15:8]), .str(not_1_out), .sel(decoder_1_out1), .clk(CLK),
    .ld(or_1_out));  // open: clr
  RAM #(.addrWidth(12), .bus("separate")) ram_7 (
    .addr(\地址 [11:0]), .din(\数据 [15:8]), .data(\输出 [15:8]), .str(not_1_out), .sel(decoder_1_out2), .clk(CLK),
    .ld(or_1_out));  // open: clr
  RAM #(.addrWidth(12), .bus("separate")) ram_8 (
    .addr(\地址 [11:0]), .din(\数据 [15:8]), .data(\输出 [15:8]), .str(not_1_out), .sel(decoder_1_out3), .clk(CLK),
    .ld(or_1_out));  // open: clr
  RAM #(.addrWidth(12), .bus("separate")) ram_9 (
    .addr(\地址 [11:0]), .din(\数据 [23:16]), .data(\输出 [23:16]), .str(not_1_out), .sel(decoder_1_out0),
    .clk(CLK), .ld(or_1_out));  // open: clr
  RAM #(.addrWidth(12), .bus("separate")) ram_10 (
    .addr(\地址 [11:0]), .din(\数据 [23:16]), .data(\输出 [23:16]), .str(not_1_out), .sel(decoder_1_out1),
    .clk(CLK), .ld(or_1_out));  // open: clr
  RAM #(.addrWidth(12), .bus("separate")) ram_11 (
    .addr(\地址 [11:0]), .din(\数据 [23:16]), .data(\输出 [23:16]), .str(not_1_out), .sel(decoder_1_out2),
    .clk(CLK), .ld(or_1_out));  // open: clr
  RAM #(.addrWidth(12), .bus("separate")) ram_12 (
    .addr(\地址 [11:0]), .din(\数据 [23:16]), .data(\输出 [23:16]), .str(not_1_out), .sel(decoder_1_out3),
    .clk(CLK), .ld(or_1_out));  // open: clr
  RAM #(.addrWidth(12), .bus("separate")) ram_13 (
    .addr(\地址 [11:0]), .din(\数据 [31:24]), .data(\输出 [31:24]), .str(not_1_out), .sel(decoder_1_out0),
    .clk(CLK), .ld(or_1_out));  // open: clr
  RAM #(.addrWidth(12), .bus("separate")) ram_14 (
    .addr(\地址 [11:0]), .din(\数据 [31:24]), .data(\输出 [31:24]), .str(not_1_out), .sel(decoder_1_out1),
    .clk(CLK), .ld(or_1_out));  // open: clr
  RAM #(.addrWidth(12), .bus("separate")) ram_15 (
    .addr(\地址 [11:0]), .din(\数据 [31:24]), .data(\输出 [31:24]), .str(not_1_out), .sel(decoder_1_out2),
    .clk(CLK), .ld(or_1_out));  // open: clr
  RAM #(.addrWidth(12), .bus("separate")) ram_16 (
    .addr(\地址 [11:0]), .din(\数据 [31:24]), .data(\输出 [31:24]), .str(not_1_out), .sel(decoder_1_out3),
    .clk(CLK), .ld(or_1_out));  // open: clr
endmodule

module RegFile (
  input  [31:0] in_1,
  input  [4:0] in_2,
  input  in_3,
  input  in_4,
  input  [4:0] in_5,
  input  [4:0] in_6,
  output [31:0] out_7,
  output [31:0] out_8
);

  wire and_1_out, and_2_out, and_3_out, and_4_out, and_5_out, and_6_out, and_7_out, and_8_out, and_9_out,
       and_10_out, and_11_out, and_12_out, and_13_out, and_14_out, and_15_out, and_16_out, and_17_out,
       and_18_out, and_19_out, and_20_out, and_21_out, and_22_out, and_23_out, and_24_out, and_25_out,
       and_26_out, and_27_out, and_28_out, and_29_out, and_30_out, and_31_out, and_32_out, decoder_1_out0,
       decoder_1_out1, decoder_1_out2, decoder_1_out3, decoder_1_out4, decoder_1_out5, decoder_1_out6,
       decoder_1_out7, decoder_1_out8, decoder_1_out9, decoder_1_out10, decoder_1_out11, decoder_1_out12,
       decoder_1_out13, decoder_1_out14, decoder_1_out15, decoder_1_out16, decoder_1_out17, decoder_1_out18,
       decoder_1_out19, decoder_1_out20, decoder_1_out21, decoder_1_out22, decoder_1_out23, decoder_1_out24,
       decoder_1_out25, decoder_1_out26, decoder_1_out27, decoder_1_out28, decoder_1_out29, decoder_1_out30,
       decoder_1_out31;
  wire [31:0] register_1_q, register_2_q, register_3_q, register_4_q, register_5_q, register_6_q,
       register_7_q, register_8_q, register_9_q, register_10_q, register_11_q, register_12_q, register_13_q,
       register_14_q, register_15_q, register_16_q, register_17_q, register_18_q, register_19_q,
       register_20_q, register_21_q, register_22_q, register_23_q, register_24_q, register_25_q,
       register_26_q, register_27_q, register_28_q, register_29_q, register_30_q, register_31_q,
       register_32_q;

  Decoder #(.select(5)) decoder_1 (
    .out0(decoder_1_out0), .out1(decoder_1_out1), .out2(decoder_1_out2), .out3(decoder_1_out3),
    .out4(decoder_1_out4), .out5(decoder_1_out5), .out6(decoder_1_out6), .out7(decoder_1_out7),
    .out8(decoder_1_out8), .out9(decoder_1_out9), .out10(decoder_1_out10), .out11(decoder_1_out11),
    .out12(decoder_1_out12), .out13(decoder_1_out13), .out14(decoder_1_out14), .out15(decoder_1_out15),
    .out16(decoder_1_out16), .out17(decoder_1_out17), .out18(decoder_1_out18), .out19(decoder_1_out19),
    .out20(decoder_1_out20), .out21(decoder_1_out21), .out22(decoder_1_out22), .out23(decoder_1_out23),
    .out24(decoder_1_out24), .out25(decoder_1_out25), .out26(decoder_1_out26), .out27(decoder_1_out27),
    .out28(decoder_1_out28), .out29(decoder_1_out29), .out30(decoder_1_out30), .out31(decoder_1_out31),
    .sel(in_2));  // open: en
  and and_1 (and_1_out, decoder_1_out0, in_4, in_3);
  and and_2 (and_2_out, decoder_1_out1, in_4, in_3);
  and and_3 (and_3_out, decoder_1_out2, in_4, in_3);
  and and_4 (and_4_out, decoder_1_out3, in_4, in_3);
  and and_5 (and_5_out, decoder_1_out4, in_4, in_3);
  and and_6 (and_6_out, decoder_1_out5, in_4, in_3);
  and and_7 (and_7_out, decoder_1_out6, in_4, in_3);
  and and_8 (and_8_out, decoder_1_out7, in_4, in_3);
  and and_9 (and_9_out, decoder_1_out8, in_4, in_3);
  and and_10 (and_10_out, decoder_1_out9, in_4, in_3);
  and and_11 (and_11_out, decoder_1_out10, in_4, in_3);
  and and_12 (and_12_out, decoder_1_out11, in_4, in_3);
  and and_13 (and_13_out, decoder_1_out12, in_4, in_3);
  and and_14 (and_14_out, decoder_1_out13, in_4, in_3);
  and and_15 (and_15_out, decoder_1_out14, in_4, in_3);
  and and_16 (and_16_out, decoder_1_out15, in_4, in_3);
  and and_17 (and_17_out, in_3, in_4, decoder_1_out16);
  and and_18 (and_18_out, in_3, in_4, decoder_1_out17);
  and and_19 (and_19_out, in_3, in_4, decoder_1_out18);
  and and_20 (and_20_out, in_3, in_4, decoder_1_out19);
  and and_21 (and_21_out, in_3, in_4, decoder_1_out20);
  and and_22 (and_22_out, in_3, in_4, decoder_1_out21);
  and and_23 (and_23_out, in_3, in_4, decoder_1_out22);
  and and_24 (and_24_out, in_3, in_4, decoder_1_out23);
  and and_25 (and_25_out, in_3, in_4, decoder_1_out24);
  and and_26 (and_26_out, in_3, in_4, decoder_1_out25);
  and and_27 (and_27_out, in_3, in_4, decoder_1_out26);
  and and_28 (and_28_out, in_3, in_4, decoder_1_out27);
  and and_29 (and_29_out, in_3, in_4, decoder_1_out28);
  and and_30 (and_30_out, in_3, in_4, decoder_1_out29);
  and and_31 (and_31_out, in_3, in_4, decoder_1_out30);
  and and_32 (and_32_out, in_3, in_4, decoder_1_out31);
  Register #(.width(32), .trigger("high")) register_1 (
    .D(in_1), .en(and_1_out), .Q(register_1_q), .clk(in_3));  // open: clr
  Register #(.width(32), .trigger("high")) register_2 (
    .D(in_1), .en(and_2_out), .Q(register_2_q), .clk(in_3));  // open: clr
  Register #(.width(32), .trigger("high")) register_3 (
    .D(in_1), .en(and_3_out), .Q(register_3_q), .clk(in_3));  // open: clr
  Register #(.width(32), .trigger("high")) register_4 (
    .D(in_1), .en(and_4_out), .Q(register_4_q), .clk(in_3));  // open: clr
  Register #(.width(32), .trigger("high")) register_5 (
    .D(in_1), .en(and_5_out), .Q(register_5_q), .clk(in_3));  // open: clr
  Register #(.width(32), .trigger("high")) register_6 (
    .D(in_1), .en(and_6_out), .Q(register_6_q), .clk(in_3));  // open: clr
  Register #(.width(32), .trigger("high")) register_7 (
    .D(in_1), .en(and_7_out), .Q(register_7_q), .clk(in_3));  // open: clr
  Register #(.width(32), .trigger("high")) register_8 (
    .D(in_1), .en(and_8_out), .Q(register_8_q), .clk(in_3));  // open: clr
  Register #(.width(32), .trigger("high")) register_9 (
    .D(in_1), .en(and_9_out), .Q(register_9_q), .clk(in_3));  // open: clr
  Register #(.width(32), .trigger("high")) register_10 (
    .D(in_1), .en(and_10_out), .Q(register_10_q), .clk(in_3));  // open: clr
  Register #(.width(32), .trigger("high")) register_11 (
    .D(in_1), .en(and_11_out), .Q(register_11_q), .clk(in_3));  // open: clr
  Register #(.width(32), .trigger("high")) register_12 (
    .D(in_1), .en(and_12_out), .Q(register_12_q), .clk(in_3));  // open: clr
  Register #(.width(32), .trigger("high")) register_13 (
    .D(in_1), .en(and_13_out), .Q(register_13_q), .clk(in_3));  // open: clr
  Register #(.width(32), .trigger("high")) register_14 (
    .D(in_1), .en(and_14_out), .Q(register_14_q), .clk(in_3));  // open: clr
  Register #(.width(32), .trigger("high")) register_15 (
    .D(in_1), .en(and_15_out), .Q(register_15_q), .clk(in_3));  // open: clr
  Register #(.width(32), .trigger("high")) register_16 (
    .D(in_1), .en(and_16_out), .Q(register_16_q), .clk(in_3));  // open: clr
  Register #(.width(32), .trigger("high")) register_17 (
    .D(in_1), .en(and_17_out), .Q(register_17_q), .clk(in_3));  // open: clr
  Register #(.width(32), .trigger("high")) register_18 (
    .D(in_1), .en(and_18_out), .Q(register_18_q), .clk(in_3));  // open: clr
  Register #(.width(32), .trigger("high")) register_19 (
    .D(in_1), .en(and_19_out), .Q(register_19_q), .clk(in_3));  // open: clr
  Register #(.width(32), .trigger("high")) register_20 (
    .D(in_1), .en(and_20_out), .Q(register_20_q), .clk(in_3));  // open: clr
  Register #(.width(32), .trigger("high")) register_21 (
    .D(in_1), .en(and_21_out), .Q(register_21_q), .clk(in_3));  // open: clr
  Register #(.width(32), .trigger("high")) register_22 (
    .D(in_1), .en(and_22_out), .Q(register_22_q), .clk(in_3));  // open: clr
  Register #(.width(32), .trigger("high")) register_23 (
    .D(in_1), .en(and_23_out), .Q(register_23_q), .clk(in_3));  // open: clr
  Register #(.width(32), .trigger("high")) register_24 (
    .D(in_1), .en(and_24_out), .Q(register_24_q), .clk(in_3));  // open: clr
  Register #(.width(32), .trigger("high")) register_25 (
    .D(in_1), .en(and_25_out), .Q(register_25_q), .clk(in_3));  // open: clr
  Register #(.width(32), .trigger("high")) register_26 (
    .D(in_1), .en(and_26_out), .Q(register_26_q), .clk(in_3));  // open: clr
  Register #(.width(32), .trigger("high")) register_27 (
    .D(in_1), .en(and_27_out), .Q(register_27_q), .clk(in_3));  // open: clr
  Register #(.width(32), .trigger("high")) register_28 (
    .D(in_1), .en(and_28_out), .Q(register_28_q), .clk(in_3));  // open: clr
  Register #(.width(32), .trigger("high")) register_29 (
    .D(in_1), .en(and_29_out), .Q(register_29_q), .clk(in_3));  // open: clr
  Register #(.width(32), .trigger("high")) register_30 (
    .D(in_1), .en(and_30_out), .Q(register_30_q), .clk(in_3));  // open: clr
  Register #(.width(32), .trigger("high")) register_31 (
    .D(in_1), .en(and_31_out), .Q(register_31_q), .clk(in_3));  // open: clr
  Register #(.width(32), .trigger("high")) register_32 (
    .D(in_1), .en(and_32_out), .Q(register_32_q), .clk(in_3));  // open: clr
  Multiplexer #(.select(5), .width(32)) multiplexer_1 (
    .in0(register_1_q), .in1(register_2_q), .in2(register_3_q), .in3(register_4_q), .in4(register_5_q),
    .in5(register_6_q), .in6(register_7_q), .in7(register_8_q), .in8(register_9_q), .in9(register_10_q),
    .in10(register_11_q), .in11(register_12_q), .in12(register_13_q), .in13(register_14_q),
    .in14(register_15_q), .in15(register_16_q), .in16(register_17_q), .in17(register_18_q),
    .in18(register_19_q), .in19(register_20_q), .in20(register_21_q), .in21(register_22_q),
    .in22(register_23_q), .in23(register_24_q), .in24(register_25_q), .in25(register_26_q),
    .in26(register_27_q), .in27(register_28_q), .in28(register_29_q), .in29(register_30_q),
    .in30(register_31_q), .in31(register_32_q), .out(out_7), .sel(in_5));  // open: en
  Multiplexer #(.select(5), .width(32)) multiplexer_2 (
    .in0(register_1_q), .in1(register_2_q), .in2(register_3_q), .in3(register_4_q), .in4(register_5_q),
    .in5(register_6_q), .in6(register_7_q), .in7(register_8_q), .in8(register_9_q), .in9(register_10_q),
    .in10(register_11_q), .in11(register_12_q), .in12(register_13_q), .in13(register_14_q),
    .in14(register_15_q), .in15(register_16_q), .in16(register_17_q), .in17(register_18_q),
    .in18(register_19_q), .in19(register_20_q), .in20(register_21_q), .in21(register_22_q),
    .in22(register_23_q), .in23(register_24_q), .in24(register_25_q), .in25(register_26_q),
    .in26(register_27_q), .in27(register_28_q), .in28(register_29_q), .in29(register_30_q),
    .in30(register_31_q), .in31(register_32_q), .out(out_8), .sel(in_6));  // open: en

  // Other names for the same wires on the sheet: CLK = in_3; WE = in_4; 地址1读出数据[31:0] = out_7; 地址2读出数据[31:0] = out_8;
  //   寄存器地址输入[4:0] = in_2; 读出地址1[4:0] = in_5; 读出地址2[4:0] = in_6; 输入[31:0] = in_1
endmodule

module \数据互传  (
  input  [4:0] in_1,
  input  in_2,
  input  [1:0] in_3,
  input  [1:0] in_4,
  input  in_5,
  input  [31:0] in_6,
  input  [4:0] in_7,
  input  in_8,
  input  [4:0] in_9,
  input  in_10,
  input  [2:0] in_11,
  output [31:0] out_12
);

  wire [31:0] alu_1_s, multiplexer_1_out, multiplexer_2_out, regfile_1_out_7, regfile_1_out_8, undriven,
       \存储器_1_输出 ;

  RegFile regfile_1 (
    .in_1(multiplexer_1_out), .out_7(regfile_1_out_7), .out_8(regfile_1_out_8), .in_2(in_9), .in_4(in_2),
    .in_3(in_8), .in_5(in_1), .in_6(in_7));
  Multiplexer #(.select(2), .width(32), .enable("false")) multiplexer_1 (
    .in0(in_6), .in1(undriven), .in2(\存储器_1_输出 ), .in3({32{1'b0}}), .out(multiplexer_1_out), .sel(in_3));
  Multiplexer #(.width(32), .enable("false")) multiplexer_2 (
    .in0(regfile_1_out_8), .in1(in_6), .out(multiplexer_2_out), .sel(in_10));
  ALU alu_1 (.X(regfile_1_out_7), .Y(multiplexer_2_out), .ALuOp(in_11), .S(alu_1_s), .\使能 (1'b1));  // open: OF, UOF, ZF
  \存储器  \u_存储器_1  (.\地址 (alu_1_s[13:0]), .\数据 (regfile_1_out_8), .WE(in_5), .\输出 (\存储器_1_输出 ), .CLK(in_8));
  Multiplexer #(.select(2), .width(32), .enable("false")) multiplexer_3 (
    .in0(undriven), .in1(regfile_1_out_8), .in2(\存储器_1_输出 ), .in3(multiplexer_1_out), .out(out_12), .sel(in_4));

  // Other names for the same wires on the sheet: AluOp[2:0] = in_11; ALuYSel = in_10; CLK = in_8; DisSel[1:0] = in_4;
  //   DMWr = in_5; RFWr = in_2; RWSel[1:0] = in_3; 寄存器地址输入[4:0] = in_9; 读出地址1[4:0] = in_1; 读出地址2[4:0] = in_7;
  //   输入[31:0] = in_6; 输出[31:0] = out_12

  // Notes on the sheet:
  //   ALU_OP                  运算功能
  //   000                          R=X+Y
  //   001                          R=X-Y
  //   010                         R=X&Y
  //   011                          R=X|Y
  //   100                         R=X异或Y
  //   101                         R=B
  //   110                         R=~B
  //   111                      R=(X<Y)?1:0
endmodule
