// Logisim project 实验二3.0.circ as structural Verilog: 4 circuits, main circuit 存储器扩展
module \存储器扩展  (
  input  CLK,
  input  WE,
  input  [13:0] Addr,
  input  [31:0] Din,
  output [31:0] Dout
);

  wire decoder_1_out0, decoder_1_out1, decoder_1_out2, decoder_1_out3, not_1_out;
  wire [31:0] undriven;

  Decoder #(.select(2), .tristate("false"), .disabled("Z"), .enable("false")) decoder_1 (
    .out0(decoder_1_out0), .out1(decoder_1_out1), .out2(decoder_1_out2), .out3(decoder_1_out3),
    .sel(Addr[13:12]));
  not not_1 (not_1_out, WE);
  RAM #(.addrWidth(12), .dataWidth(8), .bus("separate"), .Select("high")) ram_1 (
    .addr(Addr[11:0]), .din(Din[7:0]), .data(Dout[7:0]), .str(WE), .sel(decoder_1_out0), .clk(CLK),
    .ld(not_1_out));  // open: clr
  RAM #(.addrWidth(12), .dataWidth(8), .bus("separate"), .Select("high")) ram_2 (
    .addr(Addr[11:0]), .din(Din[15:8]), .data(Dout[15:8]), .str(WE), .sel(decoder_1_out0), .clk(CLK),
    .ld(not_1_out));  // open: clr
  RAM #(.addrWidth(12), .dataWidth(8), .bus("separate"), .Select("high")) ram_3 (
    .addr(Addr[11:0]), .din(Din[23:16]), .data(Dout[23:16]), .str(WE), .sel(decoder_1_out0), .clk(CLK),
    .ld(not_1_out));  // open: clr
  RAM #(.addrWidth(12), .dataWidth(8), .bus("separate"), .Select("high")) ram_4 (
    .addr(Addr[11:0]), .din(Din[31:24]), .data(Dout[31:24]), .str(WE), .sel(decoder_1_out0), .clk(CLK),
    .ld(not_1_out));  // open: clr
  Hex_Digit_Display hex_digit_display_1 (.value(Dout[15:12]));  // open: dp
  Hex_Digit_Display hex_digit_display_2 (.value(Dout[31:28]));  // open: dp
  Hex_Digit_Display hex_digit_display_3 (.value(Dout[7:4]));  // open: dp
  Hex_Digit_Display hex_digit_display_4 (.value(Dout[11:8]));  // open: dp
  Hex_Digit_Display hex_digit_display_5 (.value(Dout[27:24]));  // open: dp
  Hex_Digit_Display hex_digit_display_6 (.value(Dout[23:20]));  // open: dp
  Hex_Digit_Display hex_digit_display_7 (.value(Dout[3:0]));  // open: dp
  Hex_Digit_Display hex_digit_display_8 (.value(Dout[19:16]));  // open: dp
  RAM #(.addrWidth(12), .dataWidth(8), .bus("separate"), .Select("high")) ram_5 (
    .addr(Addr[11:0]), .din(Din[7:0]), .data(Dout[7:0]), .str(WE), .sel(decoder_1_out1), .clk(CLK),
    .ld(not_1_out));  // open: clr
  RAM #(.addrWidth(12), .dataWidth(8), .bus("separate"), .Select("high")) ram_6 (
    .addr(Addr[11:0]), .din(Din[15:8]), .data(Dout[15:8]), .str(WE), .sel(decoder_1_out1), .clk(CLK),
    .ld(not_1_out));  // open: clr
  RAM #(.addrWidth(12), .dataWidth(8), .bus("separate"), .Select("high")) ram_7 (
    .addr(Addr[11:0]), .din(Din[23:16]), .data(Dout[23:16]), .str(WE), .sel(decoder_1_out1), .clk(CLK),
    .ld(not_1_out));  // open: clr
  RAM #(.addrWidth(12), .dataWidth(8), .bus("separate"), .Select("high")) ram_8 (
    .addr(Addr[11:0]), .din(Din[31:24]), .data(Dout[31:24]), .str(WE), .sel(decoder_1_out1), .clk(CLK),
    .ld(not_1_out));  // open: clr
  Hex_Digit_Display hex_digit_display_9 (.value(Dout[15:12]));  // open: dp
  Hex_Digit_Display hex_digit_display_10 (.value(Dout[11:8]));  // open: dp
  Hex_Digit_Display hex_digit_display_11 (.value(Dout[27:24]));  // open: dp
  Hex_Digit_Display hex_digit_display_12 (.value(Dout[31:28]));  // open: dp
  Hex_Digit_Display hex_digit_display_13 (.value(Dout[7:4]));  // open: dp
  Hex_Digit_Display hex_digit_display_14 (.value(Dout[3:0]));  // open: dp
  Hex_Digit_Display hex_digit_display_15 (.value(Dout[19:16]));  // open: dp
  Hex_Digit_Display hex_digit_display_16 (.value(Dout[23:20]));  // open: dp
  RAM #(.addrWidth(12), .dataWidth(8), .bus("separate"), .Select("high")) ram_9 (
    .addr(Addr[11:0]), .din(Din[7:0]), .data(Dout[7:0]), .str(WE), .sel(decoder_1_out2), .clk(CLK),
    .ld(not_1_out));  // open: clr
  RAM #(.addrWidth(12), .dataWidth(8), .bus("separate"), .Select("high")) ram_10 (
    .addr(Addr[11:0]), .din(Din[15:8]), .data(Dout[15:8]), .str(WE), .sel(decoder_1_out2), .clk(CLK),
    .ld(not_1_out));  // open: clr
  RAM #(.addrWidth(12), .dataWidth(8), .bus("separate"), .Select("high")) ram_11 (
    .addr(Addr[11:0]), .din(Din[23:16]), .data(Dout[23:16]), .str(WE), .sel(decoder_1_out2), .clk(CLK),
    .ld(not_1_out));  // open: clr
  RAM #(.addrWidth(12), .dataWidth(8), .bus("separate"), .Select("high")) ram_12 (
    .addr(Addr[11:0]), .din(Din[31:24]), .data(Dout[31:24]), .str(WE), .sel(decoder_1_out2), .clk(CLK),
    .ld(not_1_out));  // open: clr
  Hex_Digit_Display hex_digit_display_17 (.value(Dout[15:12]));  // open: dp
  Hex_Digit_Display hex_digit_display_18 (.value(Dout[11:8]));  // open: dp
  Hex_Digit_Display hex_digit_display_19 (.value(Dout[31:28]));  // open: dp
  Hex_Digit_Display hex_digit_display_20 (.value(Dout[27:24]));  // open: dp
  RAM #(.addrWidth(12), .dataWidth(8), .bus("separate"), .Select("high")) ram_13 (
    .addr(Addr[11:0]), .din(Din[7:0]), .data(Dout[7:0]), .str(WE), .sel(decoder_1_out3), .clk(CLK),
    .ld(not_1_out));  // open: clr
  RAM #(.addrWidth(12), .dataWidth(8), .bus("separate"), .Select("high")) ram_14 (
    .addr(Addr[11:0]), .din(Din[15:8]), .data(Dout[15:8]), .sel(decoder_1_out3), .clk(CLK), .ld(not_1_out));  // open: str, clr
  RAM #(.addrWidth(12), .dataWidth(8), .bus("separate"), .Select("high")) ram_15 (
    .addr(Addr[11:0]), .din(Din[23:16]), .data(Dout[23:16]), .sel(decoder_1_out3), .clk(CLK), .ld(not_1_out));  // open: str, clr
  RAM #(.addrWidth(12), .dataWidth(8), .bus("separate"), .Select("high")) ram_16 (
    .addr(Addr[11:0]), .din(Din[31:24]), .data(Dout[31:24]), .str(WE), .sel(decoder_1_out3), .clk(CLK),
    .ld(not_1_out));  // open: clr
  Hex_Digit_Display hex_digit_display_21 (.value(Dout[7:4]));  // open: dp
  Hex_Digit_Display hex_digit_display_22 (.value(Dout[3:0]));  // open: dp
  Hex_Digit_Display hex_digit_display_23 (.value(Dout[23:20]));  // open: dp
  Hex_Digit_Display hex_digit_display_24 (.value(Dout[19:16]));  // open: dp
  Hex_Digit_Display hex_digit_display_25 (.value(Dout[15:12]));  // open: dp
  Hex_Digit_Display hex_digit_display_26 (.value(Dout[31:28]));  // open: dp
  Hex_Digit_Display hex_digit_display_27 (.value(Dout[11:8]));  // open: dp
  Hex_Digit_Display hex_digit_display_28 (.value(Dout[7:4]));  // open: dp
  Hex_Digit_Display hex_digit_display_29 (.value(Dout[23:20]));  // open: dp
  Hex_Digit_Display hex_digit_display_30 (.value(Dout[27:24]));  // open: dp
  Hex_Digit_Display hex_digit_display_31 (.value(Dout[3:0]));  // open: dp
  Hex_Digit_Display hex_digit_display_32 (.value(Dout[19:16]));  // open: dp
  Hex_Digit_Display hex_digit_display_33 (.value(undriven[15:12]));  // open: dp
  Hex_Digit_Display hex_digit_display_34 (.value(undriven[11:8]));  // open: dp
  Hex_Digit_Display hex_digit_display_35 (.value(undriven[31:28]));  // open: dp
  Hex_Digit_Display hex_digit_display_36 (.value(undriven[27:24]));  // open: dp
  Hex_Digit_Display hex_digit_display_37 (.value(undriven[7:4]));  // open: dp
  Hex_Digit_Display hex_digit_display_38 (.value(undriven[3:0]));  // open: dp
  Hex_Digit_Display hex_digit_display_39 (.value(undriven[19:16]));  // open: dp
  Hex_Digit_Display hex_digit_display_40 (.value(undriven[23:20]));  // open: dp

  // Notes on the sheet:
  //   输入引脚区
  //   输入
  //   译码器
  //   输出引脚区
  //   RAM 4K×8
endmodule

module \RegFile模块  (
  input  CLK,
  input  WE,
  input  [4:0] RA1,
  input  [4:0] RA2,
  input  [31:0] Din,
  input  [4:0] WA,
  output [31:0] RD1,
  output [31:0] RD2
);

  wire demultiplexer_1_out0, demultiplexer_1_out1, demultiplexer_1_out2, demultiplexer_1_out3,
       demultiplexer_1_out4, demultiplexer_1_out5, demultiplexer_1_out6, demultiplexer_1_out7,
       demultiplexer_1_out8, demultiplexer_1_out9, demultiplexer_1_out10, demultiplexer_1_out11,
       demultiplexer_1_out12, demultiplexer_1_out13, demultiplexer_1_out14, demultiplexer_1_out15,
       demultiplexer_1_out16, demultiplexer_1_out17, demultiplexer_1_out18, demultiplexer_1_out19,
       demultiplexer_1_out20, demultiplexer_1_out21, demultiplexer_1_out22, demultiplexer_1_out23,
       demultiplexer_1_out24, demultiplexer_1_out25, demultiplexer_1_out26, demultiplexer_1_out27,
       demultiplexer_1_out28, demultiplexer_1_out29, demultiplexer_1_out30, demultiplexer_1_out31;
  wire [31:0] register_1_q, register_2_q, register_3_q, register_4_q, register_5_q, register_6_q,
       register_7_q, register_8_q, register_9_q, register_10_q, register_11_q, register_12_q, register_13_q,
       register_14_q, register_15_q, register_16_q, register_17_q, register_18_q, register_19_q,
       register_20_q, register_21_q, register_22_q, register_23_q, register_24_q, register_25_q,
       register_26_q, register_27_q, register_28_q, register_29_q, register_30_q, register_31_q,
       register_32_q;

  Demultiplexer #(.select(5), .width(1), .tristate("false"), .disabled("Z"), .enable("false")) demultiplexer_1 (
    .out0(demultiplexer_1_out0), .out1(demultiplexer_1_out1), .out2(demultiplexer_1_out2),
    .out3(demultiplexer_1_out3), .out4(demultiplexer_1_out4), .out5(demultiplexer_1_out5),
    .out6(demultiplexer_1_out6), .out7(demultiplexer_1_out7), .out8(demultiplexer_1_out8),
    .out9(demultiplexer_1_out9), .out10(demultiplexer_1_out10), .out11(demultiplexer_1_out11),
    .out12(demultiplexer_1_out12), .out13(demultiplexer_1_out13), .out14(demultiplexer_1_out14),
    .out15(demultiplexer_1_out15), .out16(demultiplexer_1_out16), .out17(demultiplexer_1_out17),
    .out18(demultiplexer_1_out18), .out19(demultiplexer_1_out19), .out20(demultiplexer_1_out20),
    .out21(demultiplexer_1_out21), .out22(demultiplexer_1_out22), .out23(demultiplexer_1_out23),
    .out24(demultiplexer_1_out24), .out25(demultiplexer_1_out25), .out26(demultiplexer_1_out26),
    .out27(demultiplexer_1_out27), .out28(demultiplexer_1_out28), .out29(demultiplexer_1_out29),
    .out30(demultiplexer_1_out30), .out31(demultiplexer_1_out31), .in(WE), .sel(WA));
  Register #(.width(32), .trigger("rising"), .Select("low")) register_1 (
    .D({32{1'b0}}), .en(demultiplexer_1_out0), .Q(register_1_q), .clk(CLK), .clr(1'b1));
  Register #(.width(32), .trigger("rising"), .Select("low")) register_2 (
    .D(Din), .en(demultiplexer_1_out1), .Q(register_2_q), .clk(CLK));  // open: clr
  Register #(.width(32), .trigger("rising"), .Select("low")) register_3 (
    .D(Din), .en(demultiplexer_1_out2), .Q(register_3_q), .clk(CLK));  // open: clr
  Register #(.width(32), .trigger("rising"), .Select("low")) register_4 (
    .D(Din), .en(demultiplexer_1_out3), .Q(register_4_q), .clk(CLK));  // open: clr
  Register #(.width(32), .trigger("rising"), .Select("low")) register_5 (
    .D(Din), .en(demultiplexer_1_out4), .Q(register_5_q), .clk(CLK));  // open: clr
  Register #(.width(32), .trigger("rising"), .Select("low")) register_6 (
    .D(Din), .en(demultiplexer_1_out5), .Q(register_6_q), .clk(CLK));  // open: clr
  Register #(.width(32), .trigger("rising"), .Select("low")) register_7 (
    .D(Din), .en(demultiplexer_1_out6), .Q(register_7_q), .clk(CLK));  // open: clr
  Register #(.width(32), .trigger("rising"), .Select("low")) register_8 (
    .D(Din), .en(demultiplexer_1_out7), .Q(register_8_q), .clk(CLK));  // open: clr
  Register #(.width(32), .trigger("rising"), .Select("low")) register_9 (
    .D(Din), .en(demultiplexer_1_out8), .Q(register_9_q), .clk(CLK));  // open: clr
  Register #(.width(32), .trigger("rising"), .Select("low")) register_10 (
    .D(Din), .en(demultiplexer_1_out9), .Q(register_10_q), .clk(CLK));  // open: clr
  Register #(.width(32), .trigger("rising"), .Select("low")) register_11 (
    .D(Din), .en(demultiplexer_1_out10), .Q(register_11_q), .clk(CLK));  // open: clr
  Register #(.width(32), .trigger("rising"), .Select("low")) register_12 (
    .D(Din), .en(demultiplexer_1_out11), .Q(register_12_q), .clk(CLK));  // open: clr
  Register #(.width(32), .trigger("rising"), .Select("low")) register_13 (
    .D(Din), .en(demultiplexer_1_out12), .Q(register_13_q), .clk(CLK));  // open: clr
  Register #(.width(32), .trigger("rising"), .Select("low")) register_14 (
    .D(Din), .en(demultiplexer_1_out13), .Q(register_14_q), .clk(CLK));  // open: clr
  Register #(.width(32), .trigger("rising"), .Select("low")) register_15 (
    .D(Din), .en(demultiplexer_1_out14), .Q(register_15_q), .clk(CLK));  // open: clr
  Register #(.width(32), .trigger("rising"), .Select("low")) register_16 (
    .D(Din), .en(demultiplexer_1_out15), .Q(register_16_q), .clk(CLK));  // open: clr
  Register #(.width(32), .trigger("rising"), .Select("low")) register_17 (
    .D(Din), .en(demultiplexer_1_out16), .Q(register_17_q), .clk(CLK));  // open: clr
  Register #(.width(32), .trigger("rising"), .Select("low")) register_18 (
    .D(Din), .en(demultiplexer_1_out17), .Q(register_18_q), .clk(CLK));  // open: clr
  Register #(.width(32), .trigger("rising"), .Select("low")) register_19 (
    .D(Din), .en(demultiplexer_1_out18), .Q(register_19_q), .clk(CLK));  // open: clr
  Register #(.width(32), .trigger("rising"), .Select("low")) register_20 (
    .D(Din), .en(demultiplexer_1_out19), .Q(register_20_q), .clk(CLK));  // open: clr
  Register #(.width(32), .trigger("rising"), .Select("low")) register_21 (
    .D(Din), .en(demultiplexer_1_out20), .Q(register_21_q), .clk(CLK));  // open: clr
  Register #(.width(32), .trigger("rising"), .Select("low")) register_22 (
    .D(Din), .en(demultiplexer_1_out21), .Q(register_22_q), .clk(CLK));  // open: clr
  Register #(.width(32), .trigger("rising"), .Select("low")) register_23 (
    .D(Din), .en(demultiplexer_1_out22), .Q(register_23_q), .clk(CLK));  // open: clr
  Register #(.width(32), .trigger("rising"), .Select("low")) register_24 (
    .D(Din), .en(demultiplexer_1_out23), .Q(register_24_q), .clk(CLK));  // open: clr
  Register #(.width(32), .trigger("rising"), .Select("low")) register_25 (
    .D(Din), .en(demultiplexer_1_out24), .Q(register_25_q), .clk(CLK));  // open: clr
  Register #(.width(32), .trigger("rising"), .Select("low")) register_26 (
    .D(Din), .en(demultiplexer_1_out25), .Q(register_26_q), .clk(CLK));  // open: clr
  Register #(.width(32), .trigger("rising"), .Select("low")) register_27 (
    .D(Din), .en(demultiplexer_1_out26), .Q(register_27_q), .clk(CLK));  // open: clr
  Register #(.width(32), .trigger("rising"), .Select("low")) register_28 (
    .D(Din), .en(demultiplexer_1_out27), .Q(register_28_q), .clk(CLK));  // open: clr
  Register #(.width(32), .trigger("rising"), .Select("low")) register_29 (
    .D(Din), .en(demultiplexer_1_out28), .Q(register_29_q), .clk(CLK));  // open: clr
  Register #(.width(32), .trigger("rising"), .Select("low")) register_30 (
    .D(Din), .en(demultiplexer_1_out29), .Q(register_30_q), .clk(CLK));  // open: clr
  Register #(.width(32), .trigger("rising"), .Select("low")) register_31 (
    .D(Din), .en(demultiplexer_1_out30), .Q(register_31_q), .clk(CLK));  // open: clr
  Register #(.width(32), .trigger("rising"), .Select("low")) register_32 (
    .D(Din), .en(demultiplexer_1_out31), .Q(register_32_q));  // open: clk, clr
  Multiplexer #(.select(5), .width(32), .disabled("Z"), .enable("false")) multiplexer_1 (
    .in0(register_1_q), .in1(register_2_q), .in2(register_3_q), .in3(register_4_q), .in4(register_5_q),
    .in5(register_6_q), .in6(register_7_q), .in7(register_8_q), .in8(register_9_q), .in9(register_10_q),
    .in10(register_11_q), .in11(register_12_q), .in12(register_13_q), .in13(register_14_q),
    .in14(register_15_q), .in15(register_16_q), .in16(register_17_q), .in17(register_18_q),
    .in18(register_19_q), .in19(register_20_q), .in20(register_21_q), .in21(register_22_q),
    .in22(register_23_q), .in23(register_24_q), .in24(register_25_q), .in25(register_26_q),
    .in26(register_27_q), .in27(register_28_q), .in28(register_29_q), .in29(register_30_q),
    .in30(register_31_q), .in31(register_32_q), .out(RD1), .sel(RA1));
  Multiplexer #(.select(5), .width(32), .disabled("Z"), .enable("false")) multiplexer_2 (
    .in0(register_1_q), .in1(register_2_q), .in2(register_3_q), .in3(register_4_q), .in4(register_5_q),
    .in5(register_6_q), .in6(register_7_q), .in7(register_8_q), .in8(register_9_q), .in9(register_10_q),
    .in10(register_11_q), .in11(register_12_q), .in12(register_13_q), .in13(register_14_q),
    .in14(register_15_q), .in15(register_16_q), .in16(register_17_q), .in17(register_18_q),
    .in18(register_19_q), .in19(register_20_q), .in20(register_21_q), .in21(register_22_q),
    .in22(register_23_q), .in23(register_24_q), .in24(register_25_q), .in25(register_26_q),
    .in26(register_27_q), .in27(register_28_q), .in28(register_29_q), .in29(register_30_q),
    .in30(register_31_q), .in31(register_32_q), .out(RD2), .sel(RA2));

  // Notes on the sheet:
  //   输入引脚区
  //   输出引脚区
endmodule

module \数据互传  (
  input  CLK,
  input  in_2,
  input  [2:0] AluOp,
  input  [1:0] RWsel,
  input  [4:0] in_5,
  input  [4:0] RA2,
  input  [31:0] Din,
  input  [1:0] Dispsel,
  input  [4:0] WA,
  input  in_10,
  input  in_11,
  output [31:0] Disp
);

  wire [31:0] multiplexer_1_out, multiplexer_2_out, \n32位alu_1_p4 , \regfile模块_1_rd1 , \regfile模块_1_rd2 ,
       \存储器扩展_1_dout ;

  \RegFile模块  \regfile模块_1  (
    .RA1(in_5), .RA2(RA2), .WA(WA), .Din(multiplexer_1_out), .CLK(CLK), .WE(in_2), .RD1(\regfile模块_1_rd1 ),
    .RD2(\regfile模块_1_rd2 ));
  Multiplexer #(.select(2), .width(32), .disabled("Z"), .enable("false")) multiplexer_1 (
    .in0(Din), .in1(\n32位alu_1_p4 ), .in2(\存储器扩展_1_dout ), .in3({32{1'b0}}), .out(multiplexer_1_out),
    .sel(RWsel));
  Multiplexer #(.select(1), .width(32), .disabled("Z"), .enable("false")) multiplexer_2 (
    .in0(\regfile模块_1_rd2 ), .in1(Din), .out(multiplexer_2_out), .sel(in_10));
  // _32位ALU 32位alu_1: pin names not known; wires that end beside it: \regfile模块_1_rd1 , multiplexer_2_out, AluOp, \n32位alu_1_p4 
  \存储器扩展  \u_存储器扩展_1  (
    .Addr(\n32位alu_1_p4 [13:0]), .Din(\regfile模块_1_rd2 ), .CLK(CLK), .WE(in_11), .Dout(\存储器扩展_1_dout ));
  Multiplexer #(.select(2), .width(32), .disabled("Z"), .enable("false")) multiplexer_3 (
    .in0(\n32位alu_1_p4 ), .in1(\regfile模块_1_rd2 ), .in2(\存储器扩展_1_dout ), .in3(multiplexer_1_out), .out(Disp),
    .sel(Dispsel));
  Hex_Digit_Display hex_digit_display_1 (.value(Disp[15:12]));  // open: dp
  Hex_Digit_Display hex_digit_display_2 (.value(Disp[31:28]));  // open: dp
  Hex_Digit_Display hex_digit_display_3 (.value(Disp[7:4]));  // open: dp
  Hex_Digit_Display hex_digit_display_4 (.value(Disp[11:8]));  // open: dp
  Hex_Digit_Display hex_digit_display_5 (.value(Disp[27:24]));  // open: dp
  Hex_Digit_Display hex_digit_display_6 (.value(Disp[23:20]));  // open: dp
  Hex_Digit_Display hex_digit_display_7 (.value(Disp[3:0]));  // open: dp
  Hex_Digit_Display hex_digit_display_8 (.value(Disp[19:16]));  // open: dp

  // Other names for the same wires on the sheet: AluYSel = in_10; Display[31:0] = Disp; DMWr = in_11; RA1[4:0] = in_5;
  //   RFWr = in_2

  // Notes on the sheet:
  //   输入引脚区
  //   输出引脚区
  //   ALU计算
endmodule

module test (
  input  CLK,
  input  WE,
  input  [13:0] Addr,
  input  [31:0] Din,
  output [31:0] Dout
);

  wire and_1_out, clock_1_out, not_1_out;
  wire [13:0] adder_1_out, counter_1_q, counter_2_q, or_1_out;
  wire [31:0] adder_2_out, bit_extender_1_out;

  Counter #(.width(14), .max('hf), .ongoal("stay"), .trigger("rising"), .behavior("old")) counter_1 (
    .Q(counter_1_q), .clk(and_1_out), .clr(not_1_out));  // open: load, D, count, carry, preset
  Counter #(.width(14), .max('hf), .ongoal("stay"), .trigger("rising"), .behavior("old")) counter_2 (
    .Q(counter_2_q), .clk(and_1_out), .clr(WE));  // open: load, D, count, carry, preset
  not not_1 (not_1_out, WE);
  assign or_1_out = counter_1_q | counter_2_q;  // OR_Gate or_1, 14 bits wide
  assign bit_extender_1_out = {{18{1'b0}}, or_1_out};  // Bit_Extender bit_extender_1
  Adder #(.width(14)) adder_1 (.a(or_1_out), .b(Addr), .out(adder_1_out));  // open: cin, cout
  Adder #(.width(32)) adder_2 (.a(bit_extender_1_out), .b(Din), .out(adder_2_out));  // open: cin, cout
  \存储器扩展  \u_存储器扩展_1  (.Addr(adder_1_out), .Din(adder_2_out), .CLK(and_1_out), .WE(WE), .Dout(Dout));
  and and_1 (and_1_out, clock_1_out, CLK);
  Clock #(.highDuration(1), .lowDuration(1)) clock_1 (.out(clock_1_out));

  // Notes on the sheet:
  //   输入引脚区
  //   输出引脚区
  //   从16开始向后读取16次
endmodule
