// Logisim project 1-ALU2021-KL0902.circ as structural Verilog: 5 circuits, main circuit 1-1  8位加法器
module \_1_1__8位加法器  (
  input  [7:0] X,
  input  [7:0] Y,
  input  Cin,
  output [7:0] S,
  output Cout,
  output OF
);

  \_1位全加器  \u_1位全加器_1  ();  // open: Cout, Si, Cin, Xi, Yi
  // Probe on X
  // Probe on Y
  // Probe on S
  // Probe on X
  // Probe on Y
  // Probe on S

  // Notes on the sheet:
  //   输入引脚区
  //   注：不能增加任何输入输出端口信号
  //   （1）使用1位全加器FA实现8位加法器，给出溢出标志OF
  //   输出引脚区
  //   =
  //   有符号数
  //   （2）封装电路供后续实验使用
  //   =
  //   结果测试区
  //   无符号数
endmodule

module \_1_2_32位可控加减器  (
  input  Sub,
  input  [31:0] X,
  input  [31:0] Y,
  output CF,
  output OF,
  output ZF,
  output SF,
  output [31:0] S
);

  wire [2:0] multiplexer_1_out, multiplexer_1_out_2, multiplexer_1_out_3;

  \_1_1__8位加法器  \u_1_1_8位加法器_1  ();  // open: X, Y, Cin, S, Cout, OF
  // Probe on X
  // Probe on Y
  // Probe on S
  // Probe on X
  // Probe on Y
  // Probe on S
  DotMatrix #(.inputtype("column"), .matrixcols(3), .matrixrows(3), .persist(0), .dotshape("square")) dotmatrix_1 (
    .col0(multiplexer_1_out_3), .col1(multiplexer_1_out_2), .col2(multiplexer_1_out));
  Multiplexer #(.select(1), .width(9), .disabled("Z"), .enable("false")) multiplexer_1 (
    .in0(9'hba), .in1(9'h92), .out({multiplexer_1_out_3, multiplexer_1_out_2, multiplexer_1_out}), .sel(Sub));

  // Notes on the sheet:
  //   输入引脚区
  //   注：不能增加任何输入输出端口信号
  //   用封装后的8位加法器构成32位加减可控运算器，并产生正确的标志位
  //   输出引脚区
  //   =
  //   有符号数
  //   =
  //   结果测试区
  //   无符号数
endmodule

module \_1_3_32位ALU  (
  input  [2:0] AluOp,
  input  [31:0] X,
  input  [31:0] Y,
  output OF,
  output UOF,
  output ZF,
  output [31:0] S
);

  // Probe on X
  // Probe on Y
  // Probe on S
  // Probe on X
  // Probe on Y
  // Probe on S

  // Notes on the sheet:
  //   输入引脚区
  //   000 ：S=X+Y
  //   注：不能增加任何输入输出端口信号
  //   001：S=X-Y
  //   010 ：S=X&Y
  //   实现一个32位的ALU，可以由AluOP控制实现8种运算操作，并产生正确的标志位。AluOp与运算关系如下：
  //   011：S=X|Y
  //   输出引脚区
  //   100 ：S=X^Y
  //   =
  //   有符号数
  //   101 ：S=Y
  //   110 ：S=~Y
  //   =
  //   结果测试区
  //   无符号数
  //   111 ：S=X<Y?1:0
endmodule

module \_1_4_补码一位乘法器  (
  input  [7:0] X,
  input  [7:0] Y,
  output [15:0] S
);

  wire Reset, Yn_1_q;
  wire [0:0] \n1_1_8位加法器_1_s ;
  wire [6:0] \n1_1_8位加法器_1_s_2 ;

  Clock #(.highDuration(1), .lowDuration(1)) clock_1 ();  // open: out
  Button \u_复位  (.out(Reset));
  // Probe on S[15:8]
  Register #(.width(8), .trigger("rising"), .Select("low")) \u_Σ_2  (.Q(S[15:8]), .clr(Reset));  // open: D, en, clk
  Register #(.width(8), .trigger("rising"), .Select("low")) u_Y (.Q(S[7:0]), .clr(Reset));  // open: D, en, clk
  \_1_1__8位加法器  \u_1_1_8位加法器_1  (.S({\n1_1_8位加法器_1_s_2 , \n1_1_8位加法器_1_s [0]}));  // open: X, Y, Cin, Cout, OF
  // Probe on S[7:0]
  Register #(.width(1), .trigger("rising"), .Select("low")) Yn_1 (.Q(Yn_1_q), .clr(Reset));  // open: D, en, clk
  // Probe on Yn_1_q
  // Probe on X
  // Probe on Y
  // Probe on S

  // Other names for the same wires on the sheet: 乘积[15:0] = S

  // Notes on the sheet:
  //   注：不能增加任何输入输出端口信号
  //   输入引脚区
  //   功能说明：补码一位乘法器，S=X×Y，要求采用Booth乘法实现，最终结果输出到乘积引脚上。
  //   算术右移1位
  //   输出引脚区
  //   =
  //   有符号数
  //   核心算法：｛∑，Y｝=｛∑，( Yn+1-Yn ) [X]    ,    Y }  / 2
  //   结果测试区
  //   补
endmodule

module \_1位全加器  (
  input  Cin,
  input  Xi,
  input  Yi,
  output Cout,
  output Si
);

  wire and_1_out, and_2_out, xor_2_out;

  and and_1 (and_1_out, Xi, Yi);
  or or_1 (Cout, and_1_out, and_2_out);
  and and_2 (and_2_out, Cin, xor_2_out);
  xor xor_1 (Si, Cin, xor_2_out);
  xor xor_2 (xor_2_out, Xi, Yi);
endmodule
