// Logisim project 17黄少政.circ as structural Verilog: 5 circuits, main circuit 1-4 补码一位乘法器
module \_1位全加器  (
  input  Cin,
  input  Xi,
  input  Yi,
  output Cout,
  output Si
);

  wire and_1_out, and_2_out, xor_2_out;

  and and_1 (and_1_out, Xi, Yi);
  or or_1 (Cout, and_1_out, and_2_out);
  and and_2 (and_2_out, Cin, xor_2_out);
  xor xor_1 (Si, Cin, xor_2_out);
  xor xor_2 (xor_2_out, Xi, Yi);
endmodule

module \_1_1__8位加法器  (
  input  [7:0] X,
  input  [7:0] Y,
  input  Cin,
  output [7:0] S,
  output Cout,
  output OF
);

  wire \n1位全加器_2_cout , \n1位全加器_3_cout , \n1位全加器_4_cout , \n1位全加器_5_cout , \n1位全加器_6_cout , \n1位全加器_7_cout ,
       \n1位全加器_8_cout ;

  xor xor_1 (OF, Cout, \n1位全加器_2_cout );
  \_1位全加器  \u_1位全加器_1  (.Cout(Cout), .Si(S[7]), .Cin(\n1位全加器_2_cout ), .Xi(X[7]), .Yi(Y[7]));
  \_1位全加器  \u_1位全加器_2  (.Cout(\n1位全加器_2_cout ), .Si(S[6]), .Cin(\n1位全加器_4_cout ), .Xi(X[6]), .Yi(Y[6]));
  \_1位全加器  \u_1位全加器_3  (.Cout(\n1位全加器_3_cout ), .Si(S[4]), .Cin(\n1位全加器_5_cout ), .Xi(X[4]), .Yi(Y[4]));
  \_1位全加器  \u_1位全加器_4  (.Cout(\n1位全加器_4_cout ), .Si(S[5]), .Cin(\n1位全加器_3_cout ), .Xi(X[5]), .Yi(Y[5]));
  \_1位全加器  \u_1位全加器_5  (.Cout(\n1位全加器_5_cout ), .Si(S[3]), .Cin(\n1位全加器_6_cout ), .Xi(X[3]), .Yi(Y[3]));
  \_1位全加器  \u_1位全加器_6  (.Cout(\n1位全加器_6_cout ), .Si(S[2]), .Cin(\n1位全加器_8_cout ), .Xi(X[2]), .Yi(Y[2]));
  \_1位全加器  \u_1位全加器_7  (.Cout(\n1位全加器_7_cout ), .Si(S[0]), .Cin(Cin), .Xi(X[0]), .Yi(Y[0]));
  \_1位全加器  \u_1位全加器_8  (.Cout(\n1位全加器_8_cout ), .Si(S[1]), .Cin(\n1位全加器_7_cout ), .Xi(X[1]), .Yi(Y[1]));
  // Probe on X
  // Probe on Y
  // Probe on S
  // Probe on X
  // Probe on Y
  // Probe on S

  // Notes on the sheet:
  //   输入引脚区
  //   注：不能增加任何输入输出端口信号
  //   （1）使用1位全加器FA实现8位加法器，给出溢出标志OF
  //   输出引脚区
  //   =
  //   有符号数
  //   （2）封装电路供后续实验使用
  //   =
  //   结果测试区
  //   无符号数
endmodule

module \_1_2_32位可控加减器  (
  input  Sub,
  input  [31:0] X,
  input  [31:0] Y,
  output CF,
  output OF,
  output ZF,
  output SF,
  output [31:0] S
);

  wire \n1_1_8位加法器_1_cout , \n1_1_8位加法器_2_cout , \n1_1_8位加法器_3_cout , or_2_out;
  wire [2:0] multiplexer_1_out, multiplexer_1_out_2, multiplexer_1_out_3;
  wire [7:0] or_1_out, xor_1_out, xor_2_out, xor_3_out, xor_4_out;

  \_1_1__8位加法器  \u_1_1_8位加法器_1  (
    .X(X[7:0]), .Y(xor_1_out), .Cin(Sub), .S(S[7:0]), .Cout(\n1_1_8位加法器_1_cout ));  // open: OF
  assign xor_1_out = Y[7:0] ^ {8{Sub}};  // XOR_Gate xor_1, 8 bits wide
  assign xor_2_out = Y[15:8] ^ {8{Sub}};  // XOR_Gate xor_2, 8 bits wide
  \_1_1__8位加法器  \u_1_1_8位加法器_2  (
    .X(X[15:8]), .Y(xor_2_out), .Cin(\n1_1_8位加法器_1_cout ), .S(S[15:8]), .Cout(\n1_1_8位加法器_2_cout ));  // open: OF
  \_1_1__8位加法器  \u_1_1_8位加法器_3  (
    .X(X[23:16]), .Y(xor_3_out), .Cin(\n1_1_8位加法器_2_cout ), .S(S[23:16]), .Cout(\n1_1_8位加法器_3_cout ));  // open: OF
  assign xor_3_out = Y[23:16] ^ {8{Sub}};  // XOR_Gate xor_3, 8 bits wide
  // Probe on X
  // Probe on Y
  // Probe on S
  assign xor_4_out = Y[31:24] ^ {8{Sub}};  // XOR_Gate xor_4, 8 bits wide
  \_1_1__8位加法器  \u_1_1_8位加法器_4  (
    .X(X[31:24]), .Y(xor_4_out), .Cin(\n1_1_8位加法器_3_cout ), .S(S[31:24]), .Cout(CF), .OF(OF));
  DotMatrix #(.inputtype("column"), .matrixcols(3), .matrixrows(3), .persist(0), .dotshape("square")) dotmatrix_1 (
    .col0(multiplexer_1_out_3), .col1(multiplexer_1_out_2), .col2(multiplexer_1_out));
  Multiplexer #(.select(1), .width(9), .disabled("Z"), .enable("false")) multiplexer_1 (
    .in0(9'hba), .in1(9'h92), .out({multiplexer_1_out_3, multiplexer_1_out_2, multiplexer_1_out}), .sel(Sub));
  // Probe on X
  // Probe on Y
  // Probe on S
  assign or_1_out = S[31:24] | S[23:16] | S[15:8] | S[7:0];  // OR_Gate or_1, 8 bits wide
  not not_1 (ZF, or_2_out);
  or or_2 (or_2_out, or_1_out[0], or_1_out[1], or_1_out[2], or_1_out[3], or_1_out[4], or_1_out[5], or_1_out[6], or_1_out[7]);

  assign SF = S[31];

  // Notes on the sheet:
  //   输入引脚区
  //   注：不能增加任何输入输出端口信号
  //   subtract
  //   用封装后的8位加法器构成32位加减可控运算器，并产生正确的标志位
  //   输出引脚区
  //   =
  //   有符号数
  //   carry
  //   overflow
  //   =
  //   结果测试区
  //   无符号数
  //   加减符号显示器
  //   sign
  //   zero
endmodule

module \_1_3_32位ALU  (
  input  [2:0] AluOp,
  input  [31:0] X,
  input  [31:0] Y,
  output OF,
  output UOF,
  output ZF,
  output [31:0] S
);

  wire \n1_2_32位可控加减器_1_of , \n1_2_32位可控加减器_2_of ;
  wire [31:0] and_1_out, bit_extender_1_out, \n1_2_32位可控加减器_1_s , \n1_2_32位可控加减器_2_s , not_1_out, or_1_out,
       xor_1_out;

  \_1_2_32位可控加减器  \u_1_2_32位可控加减器_1  (
    .X(X), .Y(Y), .Sub(1'b0), .S(\n1_2_32位可控加减器_1_s ), .OF(\n1_2_32位可控加减器_1_of ));  // open: CF, ZF, SF
  \_1_2_32位可控加减器  \u_1_2_32位可控加减器_2  (
    .X(X), .Y(Y), .Sub(1'b1), .S(\n1_2_32位可控加减器_2_s ), .OF(\n1_2_32位可控加减器_2_of ));  // open: CF, ZF, SF
  assign and_1_out = X & Y;  // AND_Gate and_1, 32 bits wide
  assign or_1_out = X | Y;  // OR_Gate or_1, 32 bits wide
  assign xor_1_out = X ^ Y;  // XOR_Gate xor_1, 32 bits wide
  assign not_1_out = ~Y;  // NOT_Gate not_1, 32 bits wide
  Comparator #(.width(32), .mode("twosComplement")) comparator_1 (.a(Y), .b(X), .eq(ZF));  // open: gt, lt
  or or_2 (OF, \n1_2_32位可控加减器_2_of , \n1_2_32位可控加减器_1_of );
  assign bit_extender_1_out = {{31{1'b0}}, ZF};  // Bit_Extender bit_extender_1
  Multiplexer #(.select(3), .width(32), .disabled("Z"), .enable("false")) multiplexer_1 (
    .in0(\n1_2_32位可控加减器_1_s ), .in1(\n1_2_32位可控加减器_2_s ), .in2(and_1_out), .in3(or_1_out), .in4(xor_1_out),
    .in5(Y), .in6(not_1_out), .in7(bit_extender_1_out), .out(S), .sel(AluOp));
  // Probe on X
  // Probe on Y
  // Probe on S
  // Probe on X
  // Probe on Y
  // Probe on S

  // Notes on the sheet:
  //   输入引脚区
  //   000 ：S=X+Y
  //   注：不能增加任何输入输出端口信号
  //   001：S=X-Y
  //   010 ：S=X&Y
  //   实现一个32位的ALU，可以由AluOP控制实现8种运算操作，并产生正确的标志位。AluOp与运算关系如下：
  //   011：S=X|Y
  //   输出引脚区
  //   100 ：S=X^Y
  //   =
  //   有符号数
  //   101 ：S=Y
  //   110 ：S=~Y
  //   =
  //   结果测试区
  //   无符号数
  //   111 ：S=X<Y?1:0
endmodule

module \_1_4_补码一位乘法器  (
  input  [7:0] X,
  input  [7:0] Y,
  output [15:0] S
);

  wire clock_1_out, comparator_1_gt, comparator_2_gt, Reset;
  wire [0:0] \n1_1_8位加法器_1_s_2 ;
  wire [1:1] Yn_1_q;
  wire [7:0] multiplexer_1_out, multiplexer_2_out, \n1_1_8位加法器_1_s , negator_1_out, register_1_q;

  Clock #(.highDuration(1), .lowDuration(1)) clock_1 (.out(clock_1_out));
  Button \u_复位  (.out(Reset));
  // Probe on S[15:8]
  Register #(.width(8), .trigger("rising"), .Select("low")) \u_Σ_2  (
    .D({{2{\n1_1_8位加法器_1_s [7]}}, \n1_1_8位加法器_1_s [5:0]}), .en(clock_1_out), .Q(S[15:8]), .clr(Reset),
    .cs(comparator_1_gt));  // open: clk, preset
  Multiplexer #(.select(1), .width(8), .disabled("Z"), .enable("false")) multiplexer_1 (
    .in0(Y), .in1({\n1_1_8位加法器_1_s_2 [0], S[7:1]}), .out(multiplexer_1_out), .sel(comparator_2_gt));
  \_1_1__8位加法器  \u_1_1_8位加法器_1  (
    .X(S[15:8]), .Y(multiplexer_2_out),
    .S({\n1_1_8位加法器_1_s [7], \n1_1_8位加法器_1_s [5:0], \n1_1_8位加法器_1_s_2 [0]}));  // open: Cin, Cout, OF
  Multiplexer #(.select(2), .width(8), .disabled("Z"), .enable("false")) multiplexer_2 (
    .in0({8{1'b0}}), .in1(X), .in2(negator_1_out), .in3({8{1'b0}}), .out(multiplexer_2_out),
    .sel({Yn_1_q[1], S[0]}));
  Negator #(.width(8)) negator_1 (.in(X), .out(negator_1_out));
  Register #(.width(8), .trigger("rising"), .Select("low")) u_Y (
    .D(multiplexer_1_out), .en(clock_1_out), .Q(S[7:0]), .clr(Reset), .cs(comparator_1_gt));  // open: clk, preset
  // Probe on S[7:0]
  Register #(.width(1), .trigger("rising"), .Select("low")) Yn_1 (
    .D(S[0]), .en(clock_1_out), .Q(Yn_1_q[1]), .clr(Reset), .cs(comparator_1_gt));  // open: clk, preset
  // Probe on Yn_1_q[1]
  Register #(.width(8), .trigger("rising"), .Select("low")) register_1 (
    .en(Reset), .Q(register_1_q), .clr(clock_1_out));  // open: D, clk
  // Probe on X
  // Probe on Y
  // Probe on S
  Comparator #(.width(8), .mode("twosComplement")) comparator_1 (
    .a(8'h9), .b(register_1_q), .gt(comparator_1_gt));  // open: eq, lt
  Comparator #(.width(8), .mode("twosComplement")) comparator_2 (
    .a(register_1_q), .b({8{1'b0}}), .gt(comparator_2_gt));  // open: eq, lt

  // Other names for the same wires on the sheet: 乘积[15:0] = S

  // Notes on the sheet:
  //   注：不能增加任何输入输出端口信号
  //   输入引脚区
  //   算术右移1位
  //   功能说明：补码一位乘法器，S=X×Y，要求采用Booth乘法实现，最终结果输出到乘积引脚上。
  //   输出引脚区
  //   =
  //   有符号数
  //   核心算法：｛∑，Y｝=｛∑，( Yn+1-Yn ) [X]    ,    Y }  / 2
  //   结果测试区
  //   补
endmodule
