// Logisim project 2.0.circ as structural Verilog
module \一位全加器  (
  input  An,
  input  Bn,
  input  Cn_1,
  output Cn,
  output Fn
);

  wire nand_1_out, nand_2_out, xor_1_out;

  nand nand_1 (nand_1_out, An, Bn);
  nand nand_2 (nand_2_out, Cn_1, xor_1_out);
  xor xor_1 (xor_1_out, An, Bn);
  nand nand_3 (Cn, nand_1_out, nand_2_out);
  xor xor_2 (Fn, Cn_1, xor_1_out);
endmodule

module \_8位可控加法器  (
  input  Cin,
  input  K1,
  input  K0,
  input  [7:0] \Y加数_减数 ,
  input  [7:0] \X被加数_被减数 ,
  output \ZF_结果为0_ZF_1 ,
  output \OF_有溢出_OF_1 ,
  output \SF_结果为负_SF_1 ,
  output [7:0] \计算结果 ,
  output \CF_进位_借位_有进位_借位_CF_1 ,
  output Cout
);

  wire and_1_out, and_2_out, not_1_out, or_1_out, xor_3_out, xor_4_out, xor_5_out, xor_6_out, xor_7_out,
       xor_8_out, xor_9_out, xor_10_out, xor_11_out, \一位全加器_2_cn , \一位全加器_3_cn , \一位全加器_4_cn , \一位全加器_5_cn ,
       \一位全加器_6_cn , \一位全加器_7_cn , \一位全加器_8_cn ;

  xor xor_1 (\CF_进位_借位_有进位_借位_CF_1 , Cout, K1);
  \一位全加器  \u_一位全加器_1  (.An(\X被加数_被减数 [7]), .Bn(xor_3_out), .Cn_1(\一位全加器_2_cn ), .Cn(Cout), .Fn(\SF_结果为负_SF_1 ));
  xor xor_2 (\OF_有溢出_OF_1 , Cout, \一位全加器_2_cn );
  xor xor_3 (xor_3_out, \Y加数_减数 [7], K1);
  \一位全加器  \u_一位全加器_2  (.An(\X被加数_被减数 [6]), .Bn(xor_4_out), .Cn_1(\一位全加器_3_cn ), .Cn(\一位全加器_2_cn ), .Fn(\计算结果 [6]));
  xor xor_4 (xor_4_out, \Y加数_减数 [6], K1);
  \一位全加器  \u_一位全加器_3  (.An(\X被加数_被减数 [5]), .Bn(xor_5_out), .Cn_1(\一位全加器_4_cn ), .Cn(\一位全加器_3_cn ), .Fn(\计算结果 [5]));
  xor xor_5 (xor_5_out, \Y加数_减数 [5], K1);
  \一位全加器  \u_一位全加器_4  (.An(\X被加数_被减数 [4]), .Bn(xor_6_out), .Cn_1(\一位全加器_5_cn ), .Cn(\一位全加器_4_cn ), .Fn(\计算结果 [4]));
  xor xor_6 (xor_6_out, \Y加数_减数 [4], K1);
  \一位全加器  \u_一位全加器_5  (.An(\X被加数_被减数 [3]), .Bn(xor_7_out), .Cn_1(\一位全加器_6_cn ), .Cn(\一位全加器_5_cn ), .Fn(\计算结果 [3]));
  xor xor_7 (xor_7_out, \Y加数_减数 [3], K1);
  \一位全加器  \u_一位全加器_6  (.An(\X被加数_被减数 [2]), .Bn(xor_8_out), .Cn_1(\一位全加器_7_cn ), .Cn(\一位全加器_6_cn ), .Fn(\计算结果 [2]));
  nor nor_1 (\ZF_结果为0_ZF_1 , \SF_结果为负_SF_1 , \计算结果 [6], \计算结果 [5], \计算结果 [4], \计算结果 [3], \计算结果 [2], \计算结果 [1], \计算结果 [0]);
  xor xor_8 (xor_8_out, \Y加数_减数 [2], K1);
  \一位全加器  \u_一位全加器_7  (.An(\X被加数_被减数 [1]), .Bn(xor_9_out), .Cn_1(\一位全加器_8_cn ), .Cn(\一位全加器_7_cn ), .Fn(\计算结果 [1]));
  xor xor_9 (xor_9_out, \Y加数_减数 [1], K1);
  \一位全加器  \u_一位全加器_8  (.An(\X被加数_被减数 [0]), .Bn(xor_10_out), .Cn_1(or_1_out), .Cn(\一位全加器_8_cn ), .Fn(\计算结果 [0]));
  xor xor_10 (xor_10_out, \Y加数_减数 [0], K1);
  and and_1 (and_1_out, K1, not_1_out);
  not not_1 (not_1_out, Cin);
  or or_1 (or_1_out, and_1_out, and_2_out);
  and and_2 (and_2_out, Cin, xor_11_out);
  xor xor_11 (xor_11_out, K1, K0);

  assign \计算结果 [7] = \SF_结果为负_SF_1 ;

  // Notes on the sheet:
  //   K1 K0=0 0:X+Y
  //   K1 K0=0 1:X+Y+Cin
  //   K1 K0=1 0:X-Y
  //   K1 K0=1 1:X-Y-Cin
endmodule

module \_32位可控加减器2_0  (
  input  in_1,
  input  [31:0] in_2,
  input  [31:0] in_3,
  output \ZF_结果为0_ZF_1 ,
  output [31:0] out_5,
  output \SF_结果为负_SF_1 ,
  output \OF_有溢出_OF_1 ,
  output \CF_进位_借位_有进位_借位_CF_1 
);

  wire \n8位可控加法器_1_cout , \n8位可控加法器_1_zf_结果为0_zf_1 , \n8位可控加法器_2_cf_进位_借位_有进位_借位_cf_1 ,
       \n8位可控加法器_2_zf_结果为0_zf_1 , \n8位可控加法器_3_cf_进位_借位_有进位_借位_cf_1 , \n8位可控加法器_3_zf_结果为0_zf_1 ,
       \n8位可控加法器_4_cf_进位_借位_有进位_借位_cf_1 , \n8位可控加法器_4_zf_结果为0_zf_1 ;

  xor xor_1 (\CF_进位_借位_有进位_借位_CF_1 , in_1, \n8位可控加法器_1_cout );
  \_8位可控加法器  \u_8位可控加法器_1  (
    .\OF_有溢出_OF_1 (\OF_有溢出_OF_1 ), .\计算结果 (out_5[31:24]), .\Y加数_减数 (in_3[31:24]), .\X被加数_被减数 (in_2[31:24]),
    .K0(1'b1), .K1(in_1), .Cin(\n8位可控加法器_2_cf_进位_借位_有进位_借位_cf_1 ),
    .\ZF_结果为0_ZF_1 (\n8位可控加法器_1_zf_结果为0_zf_1 ), .Cout(\n8位可控加法器_1_cout ));  // open: CF_进位_借位_有进位_借位_CF_1, SF_结果为负_SF_1
  and and_1 (\ZF_结果为0_ZF_1 , \n8位可控加法器_1_zf_结果为0_zf_1 , \n8位可控加法器_2_zf_结果为0_zf_1 , \n8位可控加法器_3_zf_结果为0_zf_1 , \n8位可控加法器_4_zf_结果为0_zf_1 );
  \_8位可控加法器  \u_8位可控加法器_2  (
    .\CF_进位_借位_有进位_借位_CF_1 (\n8位可控加法器_2_cf_进位_借位_有进位_借位_cf_1 ), .\计算结果 (out_5[23:16]),
    .\Y加数_减数 (in_3[23:16]), .\X被加数_被减数 (in_2[23:16]), .K0(1'b1), .K1(in_1),
    .Cin(\n8位可控加法器_3_cf_进位_借位_有进位_借位_cf_1 ), .\ZF_结果为0_ZF_1 (\n8位可控加法器_2_zf_结果为0_zf_1 ));  // open: OF_有溢出_OF_1, SF_结果为负_SF_1, Cout
  \_8位可控加法器  \u_8位可控加法器_3  (
    .\CF_进位_借位_有进位_借位_CF_1 (\n8位可控加法器_3_cf_进位_借位_有进位_借位_cf_1 ), .\计算结果 (out_5[15:8]), .\Y加数_减数 (in_3[15:8]),
    .\X被加数_被减数 (in_2[15:8]), .K0(1'b1), .K1(in_1), .Cin(\n8位可控加法器_4_cf_进位_借位_有进位_借位_cf_1 ),
    .\ZF_结果为0_ZF_1 (\n8位可控加法器_3_zf_结果为0_zf_1 ));  // open: OF_有溢出_OF_1, SF_结果为负_SF_1, Cout
  \_8位可控加法器  \u_8位可控加法器_4  (
    .\CF_进位_借位_有进位_借位_CF_1 (\n8位可控加法器_4_cf_进位_借位_有进位_借位_cf_1 ), .\计算结果 (out_5[7:0]), .\Y加数_减数 (in_3[7:0]),
    .\X被加数_被减数 (in_2[7:0]), .K0(1'b1), .K1(in_1), .Cin(1'b0), .\ZF_结果为0_ZF_1 (\n8位可控加法器_4_zf_结果为0_zf_1 ));  // open: OF_有溢出_OF_1, SF_结果为负_SF_1, Cout

  assign \SF_结果为负_SF_1  = out_5[31];
endmodule

module \补码一位乘法器  (
  input  [7:0] X,
  input  [7:0] Y,
  output [15:0] \乘积 
);

  wire and_1_out, button_1_out, clock_1_out, comparator_1_eq, comparator_2_gt, not_2_out, not_3_out;
  wire [0:0] \n8位可控加法器_1_计算结果_2 , \Yn_1位存放_q ;
  wire [7:0] _1_q, multiplexer_1_out, multiplexer_2_out, \n8位可控加法器_1_计算结果 , not_1_out;

  Clock clock_1 (.out(clock_1_out));
  Register \u_求和  (
    .D({{2{\n8位可控加法器_1_计算结果 [7]}}, \n8位可控加法器_1_计算结果 [5:0]}), .en(not_3_out), .Q(\乘积 [15:8]),
    .clk(clock_1_out), .clr(button_1_out));
  Register \Y存放  (.D(multiplexer_2_out), .en(not_3_out), .Q(\乘积 [7:0]), .clk(clock_1_out), .clr(button_1_out));
  \_8位可控加法器  \u_8位可控加法器_1  (
    .\计算结果 ({\n8位可控加法器_1_计算结果 [7], \n8位可控加法器_1_计算结果 [5:0], \n8位可控加法器_1_计算结果_2 [0]}),
    .\Y加数_减数 (multiplexer_1_out), .\X被加数_被减数 (\乘积 [15:8]), .K0(1'b1), .K1(1'b0), .Cin(and_1_out));  // open: CF_进位_借位_有进位_借位_CF_1, OF_有溢出_OF_1, SF_结果为负_SF_1, ZF_结果为0_ZF_1, Cout
  Multiplexer #(.select(2), .width(8), .enable("false")) multiplexer_1 (
    .in0({8{1'b0}}), .in1(X), .in2(not_1_out), .in3({8{1'b0}}), .out(multiplexer_1_out),
    .sel({\乘积 [0], \Yn_1位存放_q [0]}));
  assign not_1_out = ~X;  // NOT_Gate not_1, 8 bits wide
  Register #(.width(1)) \Yn_1位存放  (
    .D(\乘积 [0]), .en(not_3_out), .Q(\Yn_1位存放_q [0]), .clk(clock_1_out), .clr(button_1_out));
  Multiplexer #(.width(8), .enable("false")) multiplexer_2 (
    .in0({\n8位可控加法器_1_计算结果_2 [0], \乘积 [7:1]}), .in1(Y), .out(multiplexer_2_out), .sel(comparator_1_eq));
  and and_1 (and_1_out, \乘积 [0], not_2_out);
  not not_2 (not_2_out, \Yn_1位存放_q [0]);
  Counter _1 (.count(not_3_out), .Q(_1_q), .clk(clock_1_out), .clr(button_1_out));  // open: load, D, carry
  Button button_1 (.out(button_1_out));
  not not_3 (not_3_out, comparator_2_gt);
  Comparator comparator_1 (.a(_1_q), .b({8{1'b0}}), .eq(comparator_1_eq));  // open: gt, lt
  Comparator comparator_2 (.a(_1_q), .b(8'h8), .gt(comparator_2_gt));  // open: eq, lt

  // Notes on the sheet:
  //   相等+0
  //   X补     -X补
  //   相等+0
  //   判断Yn+1Yn
  //   判断Yn+1Yn
  //   右移次数
endmodule
